// Logisim project кактус.circ as structural Verilog: 11 circuits, main circuit main
module main (
  input  in_1,
  input  in_2,
  input  in_3
);

  wire and_1_out, clock_1_out, \скорость_1_out_3 , \управление_картинкой_1_какстус ;
  wire [31:0] \кактус2_1_out_2 , \кактус2_1_out_3 , \кактус2_1_out_4 , \кактус2_1_out_5 , \кактус2_1_out_6 ,
       \кактус2_1_out_7 , \кактус2_1_out_8 , \сдвиг_э_та_1_out_9 , \сдвиг_э_та_1_out_10 ,
       \сдвиг_э_та_1_out_11 , \сдвиг_э_та_1_out_12 , \сдвиг_э_та_1_out_13 , \сдвиг_э_та_1_out_14 ,
       \сдвиг_э_та_1_out_15 , \сдвиг_э_та_2_out_9 , \сдвиг_э_та_2_out_10 , \сдвиг_э_та_2_out_11 ,
       \сдвиг_э_та_2_out_12 , \сдвиг_э_та_2_out_13 , \сдвиг_э_та_2_out_14 ;

  Clock clock_1 (.out(clock_1_out));
  \скорость  \u_скорость_1  (.in_1(clock_1_out), .in_2(in_2), .out_3(\скорость_1_out_3 ));
  \управление_картинкой  \u_управление_картинкой_1  (
    .\какстус (\управление_картинкой_1_какстус ), .clock(\скорость_1_out_3 ));  // open: птерадаптель
  and and_1 (and_1_out, \скорость_1_out_3 , \управление_картинкой_1_какстус );
  \сдвиг_э_та  \u_сдвиг_э_та_1  (
    .in_5(\скорость_1_out_3 ), .in_1(\кактус2_1_out_2 ), .in_2(\кактус2_1_out_3 ), .in_3(\кактус2_1_out_4 ),
    .in_4(\кактус2_1_out_5 ), .in_6(\кактус2_1_out_6 ), .in_7(\кактус2_1_out_7 ), .in_8(\кактус2_1_out_8 ),
    .out_9(\сдвиг_э_та_1_out_9 ), .out_10(\сдвиг_э_та_1_out_10 ), .out_11(\сдвиг_э_та_1_out_11 ),
    .out_12(\сдвиг_э_та_1_out_12 ), .out_13(\сдвиг_э_та_1_out_13 ), .out_14(\сдвиг_э_та_1_out_14 ),
    .out_15(\сдвиг_э_та_1_out_15 ));
  \кактус2  \u_кактус2_1  (
    .in_1(and_1_out), .out_2(\кактус2_1_out_2 ), .out_3(\кактус2_1_out_3 ), .out_4(\кактус2_1_out_4 ),
    .out_5(\кактус2_1_out_5 ), .out_6(\кактус2_1_out_6 ), .out_7(\кактус2_1_out_7 ), .out_8(\кактус2_1_out_8 ));
  \сдвиг_э_та  \u_сдвиг_э_та_2  (
    .in_5(\скорость_1_out_3 ), .in_1(\сдвиг_э_та_1_out_9 ), .in_2(\сдвиг_э_та_1_out_10 ),
    .in_3(\сдвиг_э_та_1_out_11 ), .in_4(\сдвиг_э_та_1_out_12 ), .in_6(\сдвиг_э_та_1_out_13 ),
    .in_7(\сдвиг_э_та_1_out_14 ), .in_8(\сдвиг_э_та_1_out_15 ), .out_9(\сдвиг_э_та_2_out_9 ),
    .out_10(\сдвиг_э_та_2_out_10 ), .out_11(\сдвиг_э_та_2_out_11 ), .out_12(\сдвиг_э_та_2_out_12 ),
    .out_13(\сдвиг_э_та_2_out_13 ), .out_14(\сдвиг_э_та_2_out_14 ), .out_15(\сдвиг_э_та_2_out_14 ));
  DotMatrix #(.inputtype("row"), .matrixcols(32), .matrixrows(32)) dotmatrix_1 (
    .row0({32{1'b0}}), .row1({32{1'b0}}), .row2({32{1'b0}}), .row3({32{1'b0}}), .row4({32{1'b0}}),
    .row5({32{1'b0}}), .row6({32{1'b0}}), .row7({32{1'b0}}), .row8({32{1'b0}}), .row9({32{1'b0}}),
    .row10({32{1'b0}}), .row11({32{1'b0}}), .row12({32{1'b0}}), .row13({32{1'b0}}), .row14({32{1'b0}}),
    .row15({32{1'b0}}), .row16({32{1'b0}}), .row17({32{1'b0}}), .row18({32{1'b0}}), .row19({32{1'b0}}),
    .row20({32{1'b0}}), .row21({32{1'b0}}), .row22({32{1'b0}}), .row23({32{1'b0}}), .row24({32{1'b0}}),
    .row25(\сдвиг_э_та_2_out_9 ), .row26(\сдвиг_э_та_2_out_10 ), .row27(\сдвиг_э_та_2_out_11 ),
    .row28(\сдвиг_э_та_2_out_12 ), .row29(\сдвиг_э_та_2_out_13 ), .row30(\сдвиг_э_та_2_out_14 ),
    .row31(\сдвиг_э_та_2_out_14 ));
  DotMatrix #(.inputtype("row"), .matrixcols(32), .matrixrows(32)) dotmatrix_2 (
    .row0({32{1'b0}}), .row1({32{1'b0}}), .row2({32{1'b0}}), .row3({32{1'b0}}), .row4({32{1'b0}}),
    .row5({32{1'b0}}), .row6({32{1'b0}}), .row7({32{1'b0}}), .row8({32{1'b0}}), .row9({32{1'b0}}),
    .row10({32{1'b0}}), .row11({32{1'b0}}), .row12({32{1'b0}}), .row13({32{1'b0}}), .row14({32{1'b0}}),
    .row15({32{1'b0}}), .row16({32{1'b0}}), .row17({32{1'b0}}), .row18({32{1'b0}}), .row19({32{1'b0}}),
    .row20({32{1'b0}}), .row21({32{1'b0}}), .row22({32{1'b0}}), .row23({32{1'b0}}), .row24({32{1'b0}}),
    .row25(\сдвиг_э_та_1_out_9 ), .row26(\сдвиг_э_та_1_out_10 ), .row27(\сдвиг_э_та_1_out_11 ),
    .row28(\сдвиг_э_та_1_out_12 ), .row29(\сдвиг_э_та_1_out_13 ), .row30(\сдвиг_э_та_1_out_14 ),
    .row31(\сдвиг_э_та_1_out_15 ));
endmodule

module cactus (
  input  in_1,
  output [31:0] out_2,
  output [31:0] out_3,
  output [31:0] out_4,
  output [31:0] out_5,
  output [31:0] out_6,
  output [31:0] out_7,
  output [31:0] out_8
);

  wire [4:0] counter_1_q, negator_1_out, \инкримент_1_r ;
  wire [31:0] shifter_1_out, shifter_2_out, shifter_3_out, shifter_4_out, shifter_5_out, shifter_6_out,
       shifter_7_out, shifter_8_out;

  \инкримент  \u_инкримент_1  (.X(counter_1_q), .R(\инкримент_1_r ));  // open: Cout
  Counter #(.width(5), .max('h1f)) counter_1 (
    .D(\инкримент_1_r ), .count(1'b1), .Q(counter_1_q), .clk(in_1));  // open: load, carry, clr
  Negator #(.width(5)) negator_1 (.in(\инкримент_1_r ), .out(negator_1_out));
  Shifter #(.width(32)) shifter_1 (.in(out_2), .\dist (5'b00001), .out(shifter_1_out));
  Shifter #(.width(32), .shift("lr")) shifter_2 (.in(out_2), .\dist (5'b00001), .out(shifter_2_out));
  Shifter #(.width(32)) shifter_3 (.in(out_2), .\dist (5'b00001), .out(shifter_3_out));
  Shifter #(.width(32), .shift("lr")) shifter_4 (.in(out_2), .\dist (5'b00001), .out(shifter_4_out));
  Decoder #(.select(5)) decoder_1 (
    .out0(out_2[31]), .out1(out_2[30]), .out2(out_2[29]), .out3(out_2[28]), .out4(out_2[27]),
    .out5(out_2[26]), .out6(out_2[25]), .out7(out_2[24]), .out8(out_2[23]), .out9(out_2[22]),
    .out10(out_2[21]), .out11(out_2[20]), .out12(out_2[19]), .out13(out_2[18]), .out14(out_2[17]),
    .out15(out_2[16]), .out16(out_2[15]), .out17(out_2[14]), .out18(out_2[13]), .out19(out_2[12]),
    .out20(out_2[11]), .out21(out_2[10]), .out22(out_2[9]), .out23(out_2[8]), .out24(out_2[7]),
    .out25(out_2[6]), .out26(out_2[5]), .out27(out_2[4]), .out28(out_2[3]), .out29(out_2[2]),
    .out30(out_2[1]), .out31(out_2[0]), .sel(negator_1_out));  // open: en
  Shifter #(.width(32)) shifter_5 (.in(shifter_1_out), .\dist (5'b00001), .out(shifter_5_out));
  Shifter #(.width(32), .shift("lr")) shifter_6 (.in(shifter_2_out), .\dist (5'b00001), .out(shifter_6_out));
  Shifter #(.width(32)) shifter_7 (.in(shifter_3_out), .\dist (5'b00001), .out(shifter_7_out));
  Shifter #(.width(32), .shift("lr")) shifter_8 (.in(shifter_4_out), .\dist (5'b00001), .out(shifter_8_out));
  assign out_3 = shifter_5_out | out_2 | shifter_6_out;  // OR_Gate or_1, 32 bits wide
  assign out_5 = shifter_7_out | shifter_3_out | out_2 | shifter_4_out | shifter_8_out;  // OR_Gate or_2, 32 bits wide

  assign out_4 = out_3;
  assign out_6 = out_2;
  assign out_7 = out_2;
  assign out_8 = out_2;
endmodule

module \скорость  (
  input  in_1,
  input  in_2,
  output out_3
);

  wire j_k_ff_1_q, j_k_ff_2_q, j_k_ff_3_q;
  wire [1:0] counter_1_q;

  J_K_Flip_Flop j_k_ff_1 (.J(1'b1), .clk(in_1), .K(1'b1), .Q(j_k_ff_1_q), .en(1'b1));  // open: Qn, preset, reset
  J_K_Flip_Flop j_k_ff_2 (.J(1'b1), .clk(j_k_ff_1_q), .K(1'b1), .Q(j_k_ff_2_q), .en(1'b1));  // open: Qn, preset, reset
  J_K_Flip_Flop j_k_ff_3 (.J(1'b1), .clk(j_k_ff_2_q), .K(1'b1), .Q(j_k_ff_3_q), .en(1'b1));  // open: Qn, preset, reset
  Counter #(.width(2), .max('h3)) counter_1 (
    .D(counter_1_q), .count(1'b1), .Q(counter_1_q), .clk(in_2));  // open: load, carry, clr
  Multiplexer #(.select(2)) multiplexer_1 (
    .in0(j_k_ff_3_q), .in1(j_k_ff_2_q), .in2(j_k_ff_1_q), .in3(in_1), .out(out_3), .sel(counter_1_q),
    .en(1'b1));
endmodule

module \сдвиг1  (
  input  [31:0] in_1,
  input  in_2,
  output [31:0] out_3
);

  Shift_Register #(.length(32)) shift_register_1 (
    .shift(1'b1), .in(in_1[31]), .clk(in_2), .q0(out_3[0]), .q1(out_3[1]), .q2(out_3[2]), .q3(out_3[3]),
    .q4(out_3[4]), .q5(out_3[5]), .q6(out_3[6]), .q7(out_3[7]), .q8(out_3[8]), .q9(out_3[9]),
    .q10(out_3[10]), .q11(out_3[11]), .q12(out_3[12]), .q13(out_3[13]), .q14(out_3[14]), .q15(out_3[15]),
    .q16(out_3[16]), .q17(out_3[17]), .q18(out_3[18]), .q19(out_3[19]), .q20(out_3[20]), .q21(out_3[21]),
    .q22(out_3[22]), .q23(out_3[23]), .q24(out_3[24]), .q25(out_3[25]), .q26(out_3[26]), .q27(out_3[27]),
    .q28(out_3[28]), .q29(out_3[29]), .q30(out_3[30]), .q31(out_3[31]));  // open: out, load, clr, d0, d1, d2, d3, d4, d5, d6, d7, d8, d9, d10, d11, d12, d13, d14, d15, d16, d17, d18, d19, d20, d21, d22, d23, d24, d25, d26, d27, d28, d29, d30, d31

  // Other names for the same wires on the sheet: _0 = out_3[0]; _1 = out_3[1]; _2 = out_3[2]; _3 = out_3[3];
  //   _4 = out_3[4]; _5 = out_3[5]; _6 = out_3[6]; _7 = out_3[7]; _8 = out_3[8]; _9 = out_3[9]; _10 = out_3[10];
  //   _11 = out_3[11]; _12 = out_3[12]; _13 = out_3[13]; _14 = out_3[14]; _15 = out_3[15]; _16 = out_3[16];
  //   _17 = out_3[17]; _18 = out_3[18]; _19 = out_3[19]; _20 = out_3[20]; _21 = out_3[21]; _22 = out_3[22];
  //   _23 = out_3[23]; _24 = out_3[24]; _25 = out_3[25]; _26 = out_3[26]; _27 = out_3[27]; _28 = out_3[28];
  //   _29 = out_3[29]; _30 = out_3[30]; _31 = out_3[31]
endmodule

module \инкримент  (
  input  [4:0] X,
  output [4:0] R,
  output Cout
);

  wire [4:1] and_1_out;

  assign {Cout, and_1_out} = {and_1_out, 1'b1} & X;  // AND_Gate and_1, 5 bits wide
  assign R = X ^ {and_1_out, 1'b1};  // XOR_Gate xor_1, 5 bits wide
endmodule

module \сдвиг_э_та  (
  input  [31:0] in_1,
  input  [31:0] in_2,
  input  [31:0] in_3,
  input  [31:0] in_4,
  input  in_5,
  input  [31:0] in_6,
  input  [31:0] in_7,
  input  [31:0] in_8,
  output [31:0] out_9,
  output [31:0] out_10,
  output [31:0] out_11,
  output [31:0] out_12,
  output [31:0] out_13,
  output [31:0] out_14,
  output [31:0] out_15
);

  \сдвиг1  \u_сдвиг1_1  (.in_1(in_1), .in_2(in_5), .out_3(out_9));
  \сдвиг1  \u_сдвиг1_2  (.in_1(in_2), .in_2(in_5), .out_3(out_10));
  \сдвиг1  \u_сдвиг1_3  (.in_1(in_3), .in_2(in_5), .out_3(out_11));
  \сдвиг1  \u_сдвиг1_4  (.in_1(in_4), .in_2(in_5), .out_3(out_12));
  \сдвиг1  \u_сдвиг1_5  (.in_1(in_6), .in_2(in_5), .out_3(out_13));
  \сдвиг1  \u_сдвиг1_6  (.in_1(in_7), .in_2(in_5), .out_3(out_14));
  \сдвиг1  \u_сдвиг1_7  (.in_1(in_8), .in_2(in_5), .out_3(out_15));
endmodule

module \кактус2  (
  input  in_1,
  output [31:0] out_2,
  output [31:0] out_3,
  output [31:0] out_4,
  output [31:0] out_5,
  output [31:0] out_6,
  output [31:0] out_7,
  output [31:0] out_8
);

  wire [4:0] counter_1_q, negator_1_out, subtractor_1_out;
  wire [31:0] decoder_1_out31, shifter_1_out, shifter_3_out, shifter_4_out;

  Subtractor #(.width(5)) subtractor_1 (.a(counter_1_q), .b(5'b00100), .out(subtractor_1_out));  // open: bin, bout
  Counter #(.width(5), .max('h1f)) counter_1 (
    .D(subtractor_1_out), .count(1'b1), .Q(counter_1_q), .clk(in_1));  // open: load, carry, clr
  Negator #(.width(5)) negator_1 (.in(subtractor_1_out), .out(negator_1_out));
  Shifter #(.width(32)) shifter_1 (.in(decoder_1_out31), .\dist (5'b00001), .out(shifter_1_out));
  Decoder #(.select(5)) decoder_1 (
    .out0(decoder_1_out31[31]), .out1(decoder_1_out31[30]), .out2(decoder_1_out31[29]),
    .out3(decoder_1_out31[28]), .out4(decoder_1_out31[27]), .out5(decoder_1_out31[26]),
    .out6(decoder_1_out31[25]), .out7(decoder_1_out31[24]), .out8(decoder_1_out31[23]),
    .out9(decoder_1_out31[22]), .out10(decoder_1_out31[21]), .out11(decoder_1_out31[20]),
    .out12(decoder_1_out31[19]), .out13(decoder_1_out31[18]), .out14(decoder_1_out31[17]),
    .out15(decoder_1_out31[16]), .out16(decoder_1_out31[15]), .out17(decoder_1_out31[14]),
    .out18(decoder_1_out31[13]), .out19(decoder_1_out31[12]), .out20(decoder_1_out31[11]),
    .out21(decoder_1_out31[10]), .out22(decoder_1_out31[9]), .out23(decoder_1_out31[8]),
    .out24(decoder_1_out31[7]), .out25(decoder_1_out31[6]), .out26(decoder_1_out31[5]),
    .out27(decoder_1_out31[4]), .out28(decoder_1_out31[3]), .out29(decoder_1_out31[2]),
    .out30(decoder_1_out31[1]), .out31(decoder_1_out31[0]), .sel(negator_1_out));  // open: en
  Shifter #(.width(32)) shifter_2 (.in(shifter_1_out), .\dist (5'b00001), .out(out_2));
  Shifter #(.width(32)) shifter_3 (.in(out_2), .\dist (5'b00001), .out(shifter_3_out));
  Shifter #(.width(32)) shifter_4 (.in(shifter_3_out), .\dist (5'b00001), .out(shifter_4_out));
  assign out_3 = decoder_1_out31 | out_2 | shifter_4_out;  // OR_Gate or_1, 32 bits wide
  assign out_5 = out_3 | shifter_1_out | shifter_3_out;  // OR_Gate or_2, 32 bits wide

  assign out_4 = out_3;
  assign out_6 = out_2;
  assign out_7 = out_2;
  assign out_8 = out_2;
endmodule

module \main2_дорога  (
  input  in_1
);

  wire clock, clock_1_out;
  wire [31:0] m1_c0, m1_c1, m1_c2, m1_c3, m1_c4, m1_c5, m1_c6, m1_r0, m1_r1, m1_r2, m2_c0, m2_c1, m2_c2,
       m2_c3, m2_c4, m2_c5, m2_c6, m2_r0, m2_r1, m2_r2, \дорога_1_out_2 , \дорога_1_out_3 , \дорога_1_out_4 ,
       \кактус2_1_out_2 , \кактус2_1_out_3 , \кактус2_1_out_4 , \кактус2_1_out_5 , \кактус2_1_out_6 ,
       \кактус2_1_out_7 , \кактус2_1_out_8 ;

  \скорость  \u_скорость_1  (.in_1(clock_1_out), .in_2(in_1), .out_3(clock));
  Clock clock_1 (.out(clock_1_out));
  \сдвиг_э_та  \u_сдвиг_э_та_1  (
    .in_5(clock), .in_1(\кактус2_1_out_2 ), .in_2(\кактус2_1_out_3 ), .in_3(\кактус2_1_out_4 ),
    .in_4(\кактус2_1_out_5 ), .in_6(\кактус2_1_out_6 ), .in_7(\кактус2_1_out_7 ), .in_8(\кактус2_1_out_8 ),
    .out_9(m1_c6), .out_10(m1_c5), .out_11(m1_c4), .out_12(m1_c3), .out_13(m1_c2), .out_14(m1_c1),
    .out_15(m1_c0));
  \кактус2  \u_кактус2_1  (
    .in_1(clock), .out_2(\кактус2_1_out_2 ), .out_3(\кактус2_1_out_3 ), .out_4(\кактус2_1_out_4 ),
    .out_5(\кактус2_1_out_5 ), .out_6(\кактус2_1_out_6 ), .out_7(\кактус2_1_out_7 ), .out_8(\кактус2_1_out_8 ));
  \сдвиг_э_та  \u_сдвиг_э_та_2  (
    .in_5(clock), .in_1(m1_c6), .in_2(m1_c5), .in_3(m1_c4), .in_4(m1_c3), .in_6(m1_c2), .in_7(m1_c1),
    .in_8(m1_c0), .out_9(m2_c6), .out_10(m2_c5), .out_11(m2_c4), .out_12(m2_c3), .out_13(m2_c2),
    .out_14(m2_c1), .out_15(m2_c0));
  DotMatrix #(.inputtype("row"), .matrixcols(32), .matrixrows(32)) dotmatrix_1 (
    .row0({32{1'b0}}), .row1({32{1'b0}}), .row2({32{1'b0}}), .row3({32{1'b0}}), .row4({32{1'b0}}),
    .row5({32{1'b0}}), .row6({32{1'b0}}), .row7({32{1'b0}}), .row8({32{1'b0}}), .row9({32{1'b0}}),
    .row10({32{1'b0}}), .row11({32{1'b0}}), .row12({32{1'b0}}), .row13({32{1'b0}}), .row14({32{1'b0}}),
    .row15({32{1'b0}}), .row16({32{1'b0}}), .row17({32{1'b0}}), .row18({32{1'b0}}), .row19({32{1'b0}}),
    .row20({32{1'b0}}), .row21({32{1'b0}}), .row22({32{1'b0}}), .row23({32{1'b0}}), .row24({32{1'b0}}),
    .row25(m2_c6), .row26(m2_c5), .row27(m2_c4), .row28(m2_c3), .row29(m2_c2), .row30(m2_c1), .row31(m2_c0));
  DotMatrix #(.inputtype("row"), .matrixcols(32), .matrixrows(3)) dotmatrix_2 (
    .row0(m2_r2), .row1(m2_r1), .row2(m2_r0));
  \дорога  \u_дорога_1  (.in_1(clock), .out_2(\дорога_1_out_2 ), .out_3(\дорога_1_out_3 ), .out_4(\дорога_1_out_4 ));
  \сдвиг_э_та  \u_сдвиг_э_та_3  (
    .in_5(clock), .in_6(\дорога_1_out_2 ), .in_7(\дорога_1_out_3 ), .in_8(\дорога_1_out_4 ), .out_13(m1_r2),
    .out_14(m1_r1), .out_15(m1_r0));  // open: in_1, in_2, in_3, in_4, out_9, out_10, out_11, out_12
  \сдвиг_э_та  \u_сдвиг_э_та_4  (
    .in_5(clock), .in_6(m1_r2), .in_7(m1_r1), .in_8(m1_r0), .out_13(m2_r2), .out_14(m2_r1), .out_15(m2_r0));  // open: in_1, in_2, in_3, in_4, out_9, out_10, out_11, out_12
  DotMatrix #(.inputtype("row"), .matrixcols(32), .matrixrows(32)) dotmatrix_3 (
    .row0({32{1'b0}}), .row1({32{1'b0}}), .row2({32{1'b0}}), .row3({32{1'b0}}), .row4({32{1'b0}}),
    .row5({32{1'b0}}), .row6({32{1'b0}}), .row7({32{1'b0}}), .row8({32{1'b0}}), .row9({32{1'b0}}),
    .row10({32{1'b0}}), .row11({32{1'b0}}), .row12({32{1'b0}}), .row13({32{1'b0}}), .row14({32{1'b0}}),
    .row15({32{1'b0}}), .row16({32{1'b0}}), .row17({32{1'b0}}), .row18({32{1'b0}}), .row19({32{1'b0}}),
    .row20({32{1'b0}}), .row21({32{1'b0}}), .row22({32{1'b0}}), .row23({32{1'b0}}), .row24({32{1'b0}}),
    .row25(m1_c6), .row26(m1_c5), .row27(m1_c4), .row28(m1_c3), .row29(m1_c2), .row30(m1_c1), .row31(m1_c0));
  DotMatrix #(.inputtype("row"), .matrixcols(32), .matrixrows(3)) dotmatrix_4 (
    .row0(m1_r2), .row1(m1_r1), .row2(m1_r0));
endmodule

module \дорога  (
  input  in_1,
  output [31:0] out_2,
  output [31:0] out_3,
  output [31:0] out_4
);

  wire [4:0] counter_1_q, negator_1_out, subtractor_1_out;
  wire [31:0] decoder_1_out31, shifter_1_out, shifter_2_out, shifter_3_out;

  Subtractor #(.width(5)) subtractor_1 (.a(counter_1_q), .b(5'b11001), .out(subtractor_1_out));  // open: bin, bout
  Counter #(.width(5), .max('h1f)) counter_1 (
    .D(subtractor_1_out), .count(1'b1), .Q(counter_1_q), .clk(in_1));  // open: load, carry, clr
  Negator #(.width(5)) negator_1 (.in(subtractor_1_out), .out(negator_1_out));
  Decoder #(.select(5)) decoder_1 (
    .out0(decoder_1_out31[31]), .out1(decoder_1_out31[30]), .out2(decoder_1_out31[29]),
    .out3(decoder_1_out31[28]), .out4(decoder_1_out31[27]), .out5(decoder_1_out31[26]),
    .out6(decoder_1_out31[25]), .out7(decoder_1_out31[24]), .out8(decoder_1_out31[23]),
    .out9(decoder_1_out31[22]), .out10(decoder_1_out31[21]), .out11(decoder_1_out31[20]),
    .out12(decoder_1_out31[19]), .out13(decoder_1_out31[18]), .out14(decoder_1_out31[17]),
    .out15(decoder_1_out31[16]), .out16(decoder_1_out31[15]), .out17(decoder_1_out31[14]),
    .out18(decoder_1_out31[13]), .out19(decoder_1_out31[12]), .out20(decoder_1_out31[11]),
    .out21(decoder_1_out31[10]), .out22(decoder_1_out31[9]), .out23(decoder_1_out31[8]),
    .out24(decoder_1_out31[7]), .out25(decoder_1_out31[6]), .out26(decoder_1_out31[5]),
    .out27(decoder_1_out31[4]), .out28(decoder_1_out31[3]), .out29(decoder_1_out31[2]),
    .out30(decoder_1_out31[1]), .out31(decoder_1_out31[0]), .sel(negator_1_out));  // open: en
  Shifter #(.width(32), .shift("lr")) shifter_1 (.in(decoder_1_out31), .\dist (5'b00001), .out(shifter_1_out));
  Shifter #(.width(32)) shifter_2 (.in(decoder_1_out31), .\dist (5'b00001), .out(shifter_2_out));
  Shifter #(.width(32)) shifter_3 (.in(shifter_2_out), .\dist (5'b00001), .out(shifter_3_out));
  assign out_2 = shifter_1_out | shifter_2_out | shifter_3_out | decoder_1_out31;  // OR_Gate or_1, 32 bits wide

  assign out_3 = out_2;
  assign out_4 = out_2;
endmodule

module \птерадаптель  (
  input  [31:0] in_1,
  input  [31:0] in_2,
  input  in_3,
  input  [31:0] in_4,
  input  [31:0] in_5,
  input  [31:0] in_6,
  input  [31:0] in_7,
  output [31:0] out_8,
  output [31:0] out_9,
  output [31:0] out_10,
  output [31:0] out_11,
  output [31:0] out_12,
  output [31:0] out_13
);

  wire clock_1_out;
  wire [4:0] counter_1_q, negator_1_out, subtractor_1_out;
  wire [31:0] shift_0, shift_1, shift_2, shift_3, shift_4, shift_5, shift_6, shift_7, shift_8, shift_9,
       shift_10, shift_11, shift_12, shift_13;

  Counter #(.width(5), .max('h1f)) counter_1 (
    .D(subtractor_1_out), .count(1'b1), .Q(counter_1_q), .clk(clock_1_out));  // open: load, carry, clr
  Clock clock_1 (.out(clock_1_out));
  Shifter #(.width(32)) shifter_1 (.in(shift_0), .\dist (5'b00001), .out(shift_1));
  Subtractor #(.width(5)) subtractor_1 (.a(counter_1_q), .b(5'b10000), .out(subtractor_1_out));  // open: bin, bout
  assign out_8 = shift_3 | shift_4 | shift_5;  // OR_Gate or_1, 32 bits wide
  assign out_9 = out_8 | shift_6 | shift_7 | shift_10 | shift_11;  // OR_Gate or_2, 32 bits wide
  assign out_10 = shift_4 | shift_5 | shift_6 | shift_7 | shift_8 | shift_10 | shift_11 | shift_12 | shift_13;  // OR_Gate or_3, 32 bits wide
  Shifter #(.width(32)) shifter_2 (.in(shift_1), .\dist (5'b00001), .out(shift_2));
  Decoder #(.select(5)) decoder_1 (
    .out0(shift_0[31]), .out1(shift_0[30]), .out2(shift_0[29]), .out3(shift_0[28]), .out4(shift_0[27]),
    .out5(shift_0[26]), .out6(shift_0[25]), .out7(shift_0[24]), .out8(shift_0[23]), .out9(shift_0[22]),
    .out10(shift_0[21]), .out11(shift_0[20]), .out12(shift_0[19]), .out13(shift_0[18]), .out14(shift_0[17]),
    .out15(shift_0[16]), .out16(shift_0[15]), .out17(shift_0[14]), .out18(shift_0[13]), .out19(shift_0[12]),
    .out20(shift_0[11]), .out21(shift_0[10]), .out22(shift_0[9]), .out23(shift_0[8]), .out24(shift_0[7]),
    .out25(shift_0[6]), .out26(shift_0[5]), .out27(shift_0[4]), .out28(shift_0[3]), .out29(shift_0[2]),
    .out30(shift_0[1]), .out31(shift_0[0]), .sel(negator_1_out));  // open: en
  Negator #(.width(5)) negator_1 (.in(subtractor_1_out), .out(negator_1_out));
  Shifter #(.width(32)) shifter_3 (.in(shift_2), .\dist (5'b00001), .out(shift_3));
  Shifter #(.width(32)) shifter_4 (.in(shift_3), .\dist (5'b00001), .out(shift_4));
  // OR_Gate or_4 is placed but not wired
  Shifter #(.width(32)) shifter_5 (.in(shift_4), .\dist (5'b00001), .out(shift_5));
  assign out_11 = shift_0 | shift_1 | shift_2 | shift_3 | shift_4 | shift_5 | shift_6 | shift_7 | shift_8 | shift_9 | shift_10;  // OR_Gate or_5, 32 bits wide
  assign out_12 = shift_3 | shift_4 | shift_5 | shift_6 | shift_10 | shift_11 | shift_12 | shift_13;  // OR_Gate or_6, 32 bits wide
  Shifter #(.width(32)) shifter_6 (.in(shift_5), .\dist (5'b00001), .out(shift_6));
  Shifter #(.width(32)) shifter_7 (.in(shift_6), .\dist (5'b00001), .out(shift_7));
  Shifter #(.width(32)) shifter_8 (.in(shift_7), .\dist (5'b00001), .out(shift_8));
  Shifter #(.width(32)) shifter_9 (.in(shift_8), .\dist (5'b00001), .out(shift_9));
  assign out_13 = shift_2 | shift_3 | shift_4 | shift_5;  // OR_Gate or_7, 32 bits wide
  Shifter #(.width(32)) shifter_10 (.in(shift_9), .\dist (5'b00001), .out(shift_10));
  Shifter #(.width(32)) shifter_11 (.in(shift_10), .\dist (5'b00001), .out(shift_11));
  Shifter #(.width(32)) shifter_12 (.in(shift_11), .\dist (5'b00001), .out(shift_12));
  Shifter #(.width(32)) shifter_13 (.in(shift_12), .\dist (5'b00001), .out(shift_13));
  DotMatrix #(.inputtype("row"), .matrixcols(32), .matrixrows(12)) dotmatrix_1 (
    .row0(out_8), .row1(out_9), .row2(out_10), .row3(out_11), .row4(out_12), .row5(out_13));  // open: row6, row7, row8, row9, row10, row11
  DotMatrix #(.inputtype("row"), .matrixcols(32), .matrixrows(12)) dotmatrix_2 (
    .row6(in_1), .row7(in_2), .row8(in_4), .row9(in_5), .row10(in_6), .row11(in_7));  // open: row0, row1, row2, row3, row4, row5

  // Other names for the same wires on the sheet: line1[31:0] = out_8; line2[31:0] = out_9; line3[31:0] = out_10;
  //   line4[31:0] = out_11; line5[31:0] = out_12; line6[31:0] = out_13
endmodule

module \управление_картинкой  (
  input  clock,
  output \птерадаптель ,
  output \какстус 
);

  wire comparator_1_eq, comparator_1_gt, comparator_1_lt, comparator_2_lt, or_1_out;
  wire [31:0] counter_1_q;

  Counter #(.width(32), .max('hffffffff)) counter_1 (
    .D(counter_1_q), .count(1'b1), .Q(counter_1_q), .clk(clock), .clr(comparator_2_lt));  // open: load, carry
  Comparator #(.width(32), .mode("unsigned")) comparator_1 (
    .a(32'h5), .b(counter_1_q), .gt(comparator_1_gt), .eq(comparator_1_eq), .lt(comparator_1_lt));
  and and_1 (\какстус , clock, comparator_1_gt);
  or or_1 (or_1_out, comparator_1_eq, comparator_1_lt);
  Comparator #(.width(32), .mode("unsigned")) comparator_2 (
    .a(32'h16), .b(counter_1_q), .lt(comparator_2_lt));  // open: gt, eq
  and and_2 (\птерадаптель , comparator_2_lt, or_1_out);
endmodule
