// Logisim project кактус_копия_фон_3.circ as structural Verilog: 39 circuits, main circuit main
module main (
  input  in_1
);

  wire and_1_out, and_2_out, and_3_out, choose, clear, clock, clock_1_out, clock_2, clock_2_out, clock_3,
       clock_dino, comparator_1_eq, comparator_2_eq, comparator_3_eq, comparator_4_eq, comparator_6_eq,
       comparator_7_eq, comparator_8_eq, comparator_9_eq, counter_2_carry, game_over, jump, keyboard_1_avail,
       not_1_out, not_2_out, not_3_out, not_4_out, not_5_out, or_1_out, or_2_out, rest, sit_down, stop1,
       stop2, \дино_1_jump_out , \или32_1_out_98 ;
  wire [1:0] lcount;
  wire [3:0] count1, count2, count3, count4, \лидеры_cdm_8_1_out_22 , \лидеры_cdm_8_1_out_23 ;
  wire [4:0] counter_3_q, vec_adr;
  wire [6:0] keyboard_1_data;
  wire [7:0] counter_1_q, \жизни_1_live1 , \жизни_1_live2 , \жизни_1_live3 , \жизни_1_live4 ,
       \жизни_1_live5 , \жизни_1_live6 , \жизни_1_live7 , \жизни_1_live8 , \жизни_1_live9 , \жизни_1_live10 ,
       \жизни_1_live11 , \жизни_1_live12 , \жизни_1_live13 , \жизни_1_live14 , \жизни_1_live15 ,
       \жизни_1_live16 , \жизни_1_live17 , \жизни_1_live18 , \жизни_1_live19 , \жизни_1_live20 ,
       \жизни_1_live21 , \жизни_1_live22 , \жизни_1_live23 , \жизни_1_live24 , \жизни_1_live25 ;
  wire [13:0] c;
  wire [31:0] m1_0, m1_1, m1_2, m1_3, m1_4, m1_5, m1_6, m1_7, m1_8, m1_9, m1_10, m1_11, m1_12, m1_13, m1_14,
       m1_15, m1_16, m1_17, m1_18, m1_19, m1_20, m1_21, m1_22, m1_23, m1_55, m1_c0, m1_c1, m1_c2, m1_c3,
       m1_c4, m1_c5, m1_c6, m1_r0, m1_r1, m1_r2, m2_0, m2_1, m2_2, m2_3, m2_4, m2_5, m2_6, m2_7, m2_8, m2_9,
       m2_10, m2_11, m2_12, m2_13, m2_14, m2_15, m2_16, m2_17, m2_18, m2_19, m2_20, m2_21, m2_22, m2_23,
       m2_55, m2_c0, m2_c1, m2_c2, m2_c3, m2_c4, m2_c5, m2_c6, m2_r0, m2_r1, m2_r2, m3_0, m3_1, m3_2, m3_3,
       m3_4, m3_5, m3_6, m3_7, m3_8, m3_9, m3_10, m3_11, m3_12, m3_13, m3_14, m3_15, m3_16, m3_17, m3_18,
       m3_19, m3_20, m3_21, m3_22, m3_23, m3_55, m3_c0, m3_c1, m3_c2, m3_c3, m3_c4, m3_c5, m3_c6, m3_r0,
       m3_r1, m3_r2, \вверхняя_часть_карты_1_out_3 , \вверхняя_часть_карты_1_out_4 ,
       \вверхняя_часть_карты_1_out_5 , \вверхняя_часть_карты_1_out_6 , \вверхняя_часть_карты_1_out_7 ,
       \вверхняя_часть_карты_1_out_8 , \вверхняя_часть_карты_1_out_9 , \вверхняя_часть_карты_1_out_10 ,
       \вверхняя_часть_карты_1_out_11 , \вверхняя_часть_карты_1_out_12 , \вверхняя_часть_карты_1_out_13 ,
       \вверхняя_часть_карты_1_out_14 , \вверхняя_часть_карты_1_out_15 , \вверхняя_часть_карты_1_out_16 ,
       \вверхняя_часть_карты_1_out_17 , \дино_1_out_6 , \дино_1_out_7 , \дино_1_out_8 , \дино_1_out_9 ,
       \дино_1_out_10 , \дино_1_out_11 , \дино_1_out_12 , \дино_1_out_13 , \дино_1_out_14 , \дино_1_out_15 ,
       \дино_1_out_16 , \дино_1_out_17 , \дино_1_out_18 , \дино_1_out_20 , \дино_1_out_21 , \дино_1_out_22 ,
       \дино_1_out_23 , \дино_1_out_24 , \дино_1_out_25 , \дино_1_out_26 , \дино_1_out_27 , \дино_1_out_28 ,
       \дино_1_out_29 , \дино_1_out_30 , \дино_1_out_31 , \дино_1_out_32 , \дино_1_out_33 , \дино_1_out_34 ,
       \дино_1_out_35 , \дино_1_out_36 , \дино_1_out_37 , \дино_1_out_38 , \нижняя_часть_карты_1_out_3 ,
       \нижняя_часть_карты_1_out_4 , \нижняя_часть_карты_1_out_5 , \нижняя_часть_карты_1_out_6 ,
       \нижняя_часть_карты_1_out_7 , \нижняя_часть_карты_1_out_8 , \нижняя_часть_карты_1_out_9 ,
       \нижняя_часть_карты_1_out_10 , \нижняя_часть_карты_1_out_11 , \нижняя_часть_карты_1_out_12 ,
       \сдвиг_карты_2_out_43 , \сдвиг_карты_2_out_44 , \сдвиг_карты_2_out_45 , \сдвиг_карты_2_out_46 ,
       \сдвиг_карты_2_out_47 , \сдвиг_карты_2_out_48 , \сдвиг_карты_2_out_49 , \сдвиг_карты_2_out_50 ,
       \сдвиг_карты_2_out_51 , \сдвиг_карты_2_out_52 , \сдвиг_карты_2_out_53 , \сдвиг_карты_2_out_54 ,
       \сдвиг_карты_2_out_55 , \сдвиг_карты_2_out_56 , \сдвиг_карты_2_out_57 , \сдвиг_карты_2_out_58 ,
       \сдвиг_карты_2_out_59 , \сдвиг_карты_2_out_60 , \сдвиг_карты_2_out_61 , \сдвиг_карты_2_out_62 ,
       \сдвиг_карты_2_out_63 , \сдвиг_карты_2_out_64 , \сдвиг_карты_2_out_65 , \сдвиг_карты_2_out_66 ,
       \сдвиг_карты_2_out_67 , \сдвиг_карты_2_out_68 , \сдвиг_карты_2_out_69 , \сдвиг_карты_2_out_70 ,
       \сдвиг_карты_2_out_71 , \сдвиг_карты_2_out_72 , \сдвиг_карты_2_out_73 , \сдвиг_карты_2_out_74 ,
       \сдвиг_карты_2_out_75 , \сдвиг_карты_2_out_76 , \сдвиг_карты_2_out_77 ,
       \удаление_препятствий_1_out_38 , \удаление_препятствий_1_out_39 , \удаление_препятствий_1_out_40 ,
       \удаление_препятствий_1_out_41 , \удаление_препятствий_1_out_42 , \удаление_препятствий_1_out_43 ,
       \удаление_препятствий_1_out_44 , \удаление_препятствий_1_out_45 , \удаление_препятствий_1_out_46 ,
       \удаление_препятствий_1_out_47 , \удаление_препятствий_1_out_48 , \удаление_препятствий_1_out_49 ,
       \удаление_препятствий_1_out_50 , \удаление_препятствий_1_out_51 , \удаление_препятствий_1_out_52 ,
       \удаление_препятствий_1_out_53 , \удаление_препятствий_1_out_54 , \удаление_препятствий_1_out_55 ,
       \удаление_препятствий_1_out_56 , \удаление_препятствий_1_out_57 , \удаление_препятствий_1_out_58 ,
       \удаление_препятствий_1_out_59 , \удаление_препятствий_1_out_60 , \удаление_препятствий_1_out_61 ,
       \удаление_препятствий_1_out_62 , \удаление_препятствий_1_out_63 , \удаление_препятствий_1_out_64 ,
       \удаление_препятствий_1_out_65 , \удаление_препятствий_1_out_66 , \удаление_препятствий_1_out_67 ,
       \удаление_препятствий_1_out_68 , \удаление_препятствий_1_out_69 ;

  \счетчик  \u_счетчик_1  (.clock(and_1_out), .count4(count4), .count3(count3), .count2(count2), .count1(count1));
  and and_1 (and_1_out, clock_dino, ~game_over);  // AND_Gate
  Clock clock_1 (.out(clock_1_out));
  Keyboard keyboard_1 (.clk(clock_2_out), .re(1'b1), .avail(keyboard_1_avail), .data(keyboard_1_data));  // open: clr
  Clock u_clock_2 (.out(clock_2_out));
  \скорость2  \u_скорость2_1  (.clock(clock_1_out), .del(5'b00001), .out_3(clock_dino));
  \скорость2  \u_скорость2_2  (.clock(clock_1_out), .del(vec_adr), .out_3(clock));
  \подсчет_жизней  \u_подсчет_жизней_1  (
    .clock_dino(clock_1_out), .stop1(stop1), .stop2(stop2), .rest(rest), .lcount(lcount),
    .game_over(game_over));
  \вверхняя_часть_карты  \u_вверхняя_часть_карты_1  (
    .clock(clock), .out_3(\вверхняя_часть_карты_1_out_3 ), .out_4(\вверхняя_часть_карты_1_out_4 ),
    .out_5(\вверхняя_часть_карты_1_out_5 ), .out_6(\вверхняя_часть_карты_1_out_6 ),
    .out_7(\вверхняя_часть_карты_1_out_7 ), .out_8(\вверхняя_часть_карты_1_out_8 ),
    .out_9(\вверхняя_часть_карты_1_out_9 ), .out_10(\вверхняя_часть_карты_1_out_10 ),
    .out_11(\вверхняя_часть_карты_1_out_11 ), .out_12(\вверхняя_часть_карты_1_out_12 ),
    .out_13(\вверхняя_часть_карты_1_out_13 ), .out_14(\вверхняя_часть_карты_1_out_14 ),
    .out_15(\вверхняя_часть_карты_1_out_15 ), .out_16(\вверхняя_часть_карты_1_out_16 ),
    .out_17(\вверхняя_часть_карты_1_out_17 ));  // open: game_over
  \нижняя_часть_карты  \u_нижняя_часть_карты_1  (
    .clock(clock_2), .out_3(\нижняя_часть_карты_1_out_3 ), .out_4(\нижняя_часть_карты_1_out_4 ),
    .out_5(\нижняя_часть_карты_1_out_5 ), .out_6(\нижняя_часть_карты_1_out_6 ),
    .out_7(\нижняя_часть_карты_1_out_7 ), .out_8(\нижняя_часть_карты_1_out_8 ),
    .out_9(\нижняя_часть_карты_1_out_9 ), .out_10(\нижняя_часть_карты_1_out_10 ),
    .out_11(\нижняя_часть_карты_1_out_11 ), .out_12(\нижняя_часть_карты_1_out_12 ));  // open: game_over
  Hex_Digit_Display hex_digit_display_1 (.value(count1));  // open: dp
  Hex_Digit_Display hex_digit_display_2 (.value(count2));  // open: dp
  \game_over_фон  \game_over_фон_1  (
    .clock(clock), .game_over(game_over), .in_3({32{1'b0}}), .out_38(m1_0), .in_4({32{1'b0}}), .out_39(m1_1),
    .in_5({32{1'b0}}), .out_40(m1_2), .in_6({32{1'b0}}), .out_41(m1_3), .in_7({32{1'b0}}), .out_42(m1_4),
    .in_8({32{1'b0}}), .out_43(m1_55), .in_9({32{1'b0}}), .out_44(m1_5), .in_10({32{1'b0}}), .out_45(m1_6),
    .in_11({32{1'b0}}), .out_46(m1_7), .in_12({32{1'b0}}), .out_47(m1_8),
    .in_13(\вверхняя_часть_карты_1_out_3 ), .out_48(m1_9), .in_14(\вверхняя_часть_карты_1_out_4 ),
    .out_49(m1_10), .in_15(\вверхняя_часть_карты_1_out_5 ), .out_50(m1_11),
    .in_16(\вверхняя_часть_карты_1_out_6 ), .out_51(m1_12), .in_17(\вверхняя_часть_карты_1_out_7 ),
    .out_52(m1_13), .in_18(\вверхняя_часть_карты_1_out_8 ), .out_53(m1_14),
    .in_19(\вверхняя_часть_карты_1_out_9 ), .out_54(m1_15), .in_20(\вверхняя_часть_карты_1_out_10 ),
    .out_55(m1_16), .in_21(\вверхняя_часть_карты_1_out_11 ), .out_56(m1_17),
    .in_22(\вверхняя_часть_карты_1_out_12 ), .out_57(m1_18), .in_23(\вверхняя_часть_карты_1_out_13 ),
    .out_58(m1_19), .in_24(\вверхняя_часть_карты_1_out_14 ), .out_59(m1_20),
    .in_25(\вверхняя_часть_карты_1_out_15 ), .out_60(m1_21), .in_26(\вверхняя_часть_карты_1_out_16 ),
    .out_61(m1_22), .in_27(\вверхняя_часть_карты_1_out_17 ), .out_62(m1_23),
    .in_28(\нижняя_часть_карты_1_out_3 ), .out_63(m1_c6), .in_29(\нижняя_часть_карты_1_out_4 ),
    .out_64(m1_c5), .in_30(\нижняя_часть_карты_1_out_5 ), .out_65(m1_c4),
    .in_31(\нижняя_часть_карты_1_out_6 ), .out_66(m1_c3), .in_32(\нижняя_часть_карты_1_out_7 ),
    .out_67(m1_c2), .in_33(\нижняя_часть_карты_1_out_8 ), .out_68(m1_c1),
    .in_34(\нижняя_часть_карты_1_out_9 ), .out_69(m1_c0), .in_35(\нижняя_часть_карты_1_out_10 ),
    .out_70(m1_r2), .in_36(\нижняя_часть_карты_1_out_11 ), .out_71(m1_r1),
    .in_37(\нижняя_часть_карты_1_out_12 ), .out_72(m1_r0));
  Hex_Digit_Display hex_digit_display_3 (.value(count3));  // open: dp
  Hex_Digit_Display hex_digit_display_4 (.value(count4));  // open: dp
  Counter #(.max('h4), .trigger("falling")) counter_1 (
    .Q(counter_1_q), .clk(clock), .clr(clock_2));  // open: load, D, count, carry
  DotMatrix #(.inputtype("row"), .matrixcols(32), .matrixrows(32)) dotmatrix_1 (
    .row0(m3_0), .row1(m3_1), .row2(m3_2), .row3(m3_3), .row4(m3_4), .row5(m3_55), .row6(m3_5), .row7(m3_6),
    .row8(m3_7), .row9(m3_8), .row10(m3_9), .row11(m3_10), .row12(m3_11), .row13(m3_12), .row14(m3_13),
    .row15(m3_14), .row16(m3_15), .row17(m3_16), .row18(m3_17), .row19(m3_18), .row20(m3_19), .row21(m3_20),
    .row22(m3_21), .row23(m3_22), .row24(m3_23), .row25(m3_c6), .row26(m3_c5), .row27(m3_c4), .row28(m3_c3),
    .row29(m3_c2), .row30(m3_c1), .row31(m3_c0));
  DotMatrix #(.inputtype("row"), .matrixcols(32), .matrixrows(3)) dotmatrix_2 (
    .row0(m3_r2), .row1(m3_r1), .row2(m3_r0));
  Comparator #(.width(7)) comparator_1 (.a(keyboard_1_data), .b(7'b0100000), .eq(comparator_1_eq));  // open: gt, lt
  Comparator #(.width(7)) comparator_2 (.a(keyboard_1_data), .b(7'b1110011), .eq(comparator_2_eq));  // open: gt, lt
  Comparator #(.width(7)) comparator_3 (.a(keyboard_1_data), .b(7'b1100011), .eq(comparator_3_eq));  // open: gt, lt
  Comparator #(.width(7)) comparator_4 (.a(keyboard_1_data), .b(7'b1111000), .eq(comparator_4_eq));  // open: gt, lt
  \сдвиг_карты  \u_сдвиг_карты_1  (
    .in_3(m1_0), .in_4(m1_6), .in_5(m1_13), .in_6(m1_20), .in_7(m1_c3), .in_8(m1_1), .in_9(m1_7),
    .in_10(m1_14), .in_11(m1_21), .in_12(m1_c2), .in_13(m1_2), .in_14(m1_8), .in_15(m1_15), .in_16(m1_22),
    .in_17(m1_c1), .in_18(m1_3), .in_19(m1_9), .in_20(m1_16), .in_21(m1_23), .in_22(m1_c0), .in_23(m1_4),
    .in_24(m1_10), .in_25(m1_17), .in_26(m1_c6), .in_27(m1_r2), .in_28(m1_55), .in_29(m1_11), .in_30(m1_18),
    .in_31(m1_c5), .in_32(m1_r1), .in_33(m1_5), .in_34(m1_12), .in_35(m1_19), .in_36(m1_c4), .in_37(m1_r0),
    .in_38(clock), .in_41(clock), .in_39(clock), .in_40(clock), .in_42(clock_2), .out_43(m2_0),
    .out_44(m2_6), .out_45(m2_13), .out_46(m2_20), .out_47(m2_c3), .out_48(m2_1), .out_49(m2_7),
    .out_50(m2_14), .out_51(m2_21), .out_52(m2_c2), .out_53(m2_2), .out_54(m2_8), .out_55(m2_15),
    .out_56(m2_22), .out_57(m2_c1), .out_58(m2_3), .out_59(m2_9), .out_60(m2_16), .out_61(m2_23),
    .out_62(m2_c0), .out_63(m2_4), .out_64(m2_10), .out_65(m2_17), .out_66(m2_c6), .out_67(m2_r2),
    .out_68(m2_55), .out_69(m2_11), .out_70(m2_18), .out_71(m2_c5), .out_72(m2_r1), .out_73(m2_5),
    .out_74(m2_12), .out_75(m2_19), .out_76(m2_c4), .out_77(m2_r0));  // open: in_1, in_2
  Comparator comparator_5 (.a(counter_1_q), .b(8'h3), .eq(clock_2));  // open: gt, lt
  D_Flip_Flop d_ff_1 (
    .clk(clock_2_out), .D(1'b1), .Q(jump), .en(comparator_1_eq), .reset(\дино_1_jump_out ));  // open: Qn, preset
  D_Flip_Flop d_ff_2 (
    .clk(clock_2_out), .D(1'b1), .Q(choose), .en(comparator_3_eq), .reset(comparator_4_eq));  // open: Qn, preset
  Comparator #(.width(7)) comparator_6 (.a(keyboard_1_data), .b(7'b1110010), .eq(comparator_6_eq));  // open: gt, lt
  not not_1 (not_1_out, not_4_out);
  not not_2 (not_2_out, game_over);
  not not_3 (not_3_out, not_1_out);
  not not_4 (not_4_out, not_2_out);
  D_Flip_Flop d_ff_3 (
    .clk(clock_2_out), .D(1'b1), .Q(sit_down), .en(comparator_2_eq), .reset(\дино_1_jump_out ));  // open: Qn, preset
  D_Flip_Flop d_ff_4 (.clk(clock_1_out), .D(1'b1), .Q(rest), .en(comparator_6_eq), .reset(clear));  // open: Qn, preset
  not not_5 (not_5_out, not_3_out);
  or or_1 (or_1_out, stop2, stop1);
  \сдвиг_карты  \u_сдвиг_карты_2  (
    .in_3(m2_0), .in_4(m2_6), .in_5(m2_13), .in_6(m2_20), .in_7(m2_c3), .in_8(m2_1), .in_9(m2_7),
    .in_10(m2_14), .in_11(m2_21), .in_12(m2_c2), .in_13(m2_2), .in_14(m2_8), .in_15(m2_15), .in_16(m2_22),
    .in_17(m2_c1), .in_18(m2_3), .in_19(m2_9), .in_20(m2_16), .in_21(m2_23), .in_22(m2_c0), .in_23(m2_4),
    .in_24(m2_10), .in_25(m2_17), .in_26(m2_c6), .in_27(m2_r2), .in_28(m2_55), .in_29(m2_11), .in_30(m2_18),
    .in_31(m2_c5), .in_32(m2_r1), .in_33(m2_5), .in_34(m2_12), .in_35(m2_19), .in_36(m2_c4), .in_37(m2_r0),
    .in_38(clock), .in_41(clock), .in_39(clock), .in_40(clock), .in_42(clock_2),
    .out_43(\сдвиг_карты_2_out_43 ), .out_44(\сдвиг_карты_2_out_44 ), .out_45(\сдвиг_карты_2_out_45 ),
    .out_46(\сдвиг_карты_2_out_46 ), .out_47(\сдвиг_карты_2_out_47 ), .out_48(\сдвиг_карты_2_out_48 ),
    .out_49(\сдвиг_карты_2_out_49 ), .out_50(\сдвиг_карты_2_out_50 ), .out_51(\сдвиг_карты_2_out_51 ),
    .out_52(\сдвиг_карты_2_out_52 ), .out_53(\сдвиг_карты_2_out_53 ), .out_54(\сдвиг_карты_2_out_54 ),
    .out_55(\сдвиг_карты_2_out_55 ), .out_56(\сдвиг_карты_2_out_56 ), .out_57(\сдвиг_карты_2_out_57 ),
    .out_58(\сдвиг_карты_2_out_58 ), .out_59(\сдвиг_карты_2_out_59 ), .out_60(\сдвиг_карты_2_out_60 ),
    .out_61(\сдвиг_карты_2_out_61 ), .out_62(\сдвиг_карты_2_out_62 ), .out_63(\сдвиг_карты_2_out_63 ),
    .out_64(\сдвиг_карты_2_out_64 ), .out_65(\сдвиг_карты_2_out_65 ), .out_66(\сдвиг_карты_2_out_66 ),
    .out_67(\сдвиг_карты_2_out_67 ), .out_68(\сдвиг_карты_2_out_68 ), .out_69(\сдвиг_карты_2_out_69 ),
    .out_70(\сдвиг_карты_2_out_70 ), .out_71(\сдвиг_карты_2_out_71 ), .out_72(\сдвиг_карты_2_out_72 ),
    .out_73(\сдвиг_карты_2_out_73 ), .out_74(\сдвиг_карты_2_out_74 ), .out_75(\сдвиг_карты_2_out_75 ),
    .out_76(\сдвиг_карты_2_out_76 ), .out_77(\сдвиг_карты_2_out_77 ));  // open: in_1, in_2
  DotMatrix #(.inputtype("row"), .matrixcols(32), .matrixrows(32)) dotmatrix_3 (
    .row0(m2_0), .row1(m2_1), .row2(m2_2), .row3(m2_3), .row4(m2_4), .row5(m2_5), .row6(m2_5), .row7(m2_6),
    .row8(m2_7), .row9(m2_8), .row10(m2_9), .row11(m2_10), .row12(m2_11), .row13(m2_12), .row14(m2_13),
    .row15(m2_14), .row16(m2_15), .row17(m2_16), .row18(m2_17), .row19(m2_18), .row20(m2_19), .row21(m2_20),
    .row22(m2_21), .row23(m2_22), .row24(m2_23), .row25(m2_c6), .row26(m2_c5), .row27(m2_c4), .row28(m2_c3),
    .row29(m2_c2), .row30(m2_c1), .row31(m2_c0));
  DotMatrix #(.inputtype("row"), .matrixcols(32), .matrixrows(3)) dotmatrix_4 (
    .row0(m2_r2), .row1(m2_r1), .row2(m2_r0));
  Comparator #(.width(4)) comparator_7 (.a(count3), .b(4'b0000), .eq(comparator_7_eq));  // open: gt, lt
  Comparator #(.width(4)) comparator_8 (.a(count3), .b(4'b0101), .eq(comparator_8_eq));  // open: gt, lt
  Comparator #(.width(4)) comparator_9 (.a(count4), .b(4'b0000), .eq(comparator_9_eq));  // open: gt, lt
  \дино  \u_дино_1  (
    .jump(jump), .Game_Over(game_over), .clock(clock_dino), .out_6(\дино_1_out_6 ), .sit_down(sit_down),
    .out_7(\дино_1_out_7 ), .choose(choose), .out_8(\дино_1_out_8 ), .out_9(\дино_1_out_9 ),
    .out_10(\дино_1_out_10 ), .out_11(\дино_1_out_11 ), .out_12(\дино_1_out_12 ), .out_13(\дино_1_out_13 ),
    .out_14(\дино_1_out_14 ), .out_15(\дино_1_out_15 ), .out_16(\дино_1_out_16 ), .out_17(\дино_1_out_17 ),
    .out_18(\дино_1_out_18 ), .out_20(\дино_1_out_20 ), .out_21(\дино_1_out_21 ), .out_22(\дино_1_out_22 ),
    .out_23(\дино_1_out_23 ), .out_24(\дино_1_out_24 ), .out_25(\дино_1_out_25 ), .out_26(\дино_1_out_26 ),
    .out_27(\дино_1_out_27 ), .out_28(\дино_1_out_28 ), .out_29(\дино_1_out_29 ), .out_30(\дино_1_out_30 ),
    .out_31(\дино_1_out_31 ), .out_32(\дино_1_out_32 ), .out_33(\дино_1_out_33 ), .out_34(\дино_1_out_34 ),
    .out_35(\дино_1_out_35 ), .out_36(\дино_1_out_36 ), .out_37(\дино_1_out_37 ), .out_38(\дино_1_out_38 ),
    .jump_out(\дино_1_jump_out ));
  \удаление_препятствий  \u_удаление_препятствий_1  (
    .clock(clock_3), .game_over(or_1_out), .in_3(\сдвиг_карты_2_out_43 ),
    .out_38(\удаление_препятствий_1_out_38 ), .in_4(\сдвиг_карты_2_out_48 ),
    .out_39(\удаление_препятствий_1_out_39 ), .in_5(\сдвиг_карты_2_out_53 ),
    .out_40(\удаление_препятствий_1_out_40 ), .in_6(\сдвиг_карты_2_out_58 ),
    .out_41(\удаление_препятствий_1_out_41 ), .in_7(\сдвиг_карты_2_out_63 ),
    .out_42(\удаление_препятствий_1_out_42 ), .in_8(\сдвиг_карты_2_out_68 ),
    .out_43(\удаление_препятствий_1_out_43 ), .in_9(\сдвиг_карты_2_out_73 ),
    .out_44(\удаление_препятствий_1_out_44 ), .in_10(\сдвиг_карты_2_out_44 ),
    .out_45(\удаление_препятствий_1_out_45 ), .in_11(\сдвиг_карты_2_out_49 ),
    .out_46(\удаление_препятствий_1_out_46 ), .in_12(\сдвиг_карты_2_out_54 ),
    .out_47(\удаление_препятствий_1_out_47 ), .in_13(\сдвиг_карты_2_out_59 ),
    .out_48(\удаление_препятствий_1_out_48 ), .in_14(\сдвиг_карты_2_out_64 ),
    .out_49(\удаление_препятствий_1_out_49 ), .in_15(\сдвиг_карты_2_out_69 ),
    .out_50(\удаление_препятствий_1_out_50 ), .in_16(\сдвиг_карты_2_out_74 ),
    .out_51(\удаление_препятствий_1_out_51 ), .in_17(\сдвиг_карты_2_out_45 ),
    .out_52(\удаление_препятствий_1_out_52 ), .in_18(\сдвиг_карты_2_out_50 ),
    .out_53(\удаление_препятствий_1_out_53 ), .in_19(\сдвиг_карты_2_out_55 ),
    .out_54(\удаление_препятствий_1_out_54 ), .in_20(\сдвиг_карты_2_out_60 ),
    .out_55(\удаление_препятствий_1_out_55 ), .in_21(\сдвиг_карты_2_out_65 ),
    .out_56(\удаление_препятствий_1_out_56 ), .in_22(\сдвиг_карты_2_out_70 ),
    .out_57(\удаление_препятствий_1_out_57 ), .in_23(\сдвиг_карты_2_out_75 ),
    .out_58(\удаление_препятствий_1_out_58 ), .in_24(\сдвиг_карты_2_out_46 ),
    .out_59(\удаление_препятствий_1_out_59 ), .in_25(\сдвиг_карты_2_out_51 ),
    .out_60(\удаление_препятствий_1_out_60 ), .in_26(\сдвиг_карты_2_out_56 ),
    .out_61(\удаление_препятствий_1_out_61 ), .in_27(\сдвиг_карты_2_out_61 ),
    .out_62(\удаление_препятствий_1_out_62 ), .in_28(\сдвиг_карты_2_out_66 ),
    .out_63(\удаление_препятствий_1_out_63 ), .in_29(\сдвиг_карты_2_out_71 ),
    .out_64(\удаление_препятствий_1_out_64 ), .in_30(\сдвиг_карты_2_out_76 ),
    .out_65(\удаление_препятствий_1_out_65 ), .in_31(\сдвиг_карты_2_out_47 ),
    .out_66(\удаление_препятствий_1_out_66 ), .in_32(\сдвиг_карты_2_out_52 ),
    .out_67(\удаление_препятствий_1_out_67 ), .in_33(\сдвиг_карты_2_out_57 ),
    .out_68(\удаление_препятствий_1_out_68 ), .in_34(\сдвиг_карты_2_out_62 ),
    .out_69(\удаление_препятствий_1_out_69 ), .in_35(\сдвиг_карты_2_out_67 ), .out_70(m3_r2),
    .in_36(\сдвиг_карты_2_out_72 ), .out_71(m3_r1), .in_37(\сдвиг_карты_2_out_77 ), .out_72(m3_r0));
  \или32  \u_или32_1  (
    .in_1(\дино_1_out_6 ), .in_2(\дино_1_out_7 ), .in_3(\дино_1_out_8 ), .in_4(\дино_1_out_9 ),
    .in_5(\дино_1_out_10 ), .in_6(\дино_1_out_11 ), .in_7(\дино_1_out_12 ), .in_8(\дино_1_out_13 ),
    .in_9(\дино_1_out_14 ), .in_10(\дино_1_out_15 ), .in_11(\дино_1_out_16 ), .in_12(\дино_1_out_17 ),
    .in_13(\дино_1_out_18 ), .in_14(\дино_1_out_20 ), .in_15(\дино_1_out_21 ), .in_16(\дино_1_out_22 ),
    .in_17(\дино_1_out_23 ), .in_18(\дино_1_out_24 ), .in_19(\дино_1_out_25 ), .in_20(\дино_1_out_26 ),
    .in_21(\дино_1_out_27 ), .in_22(\дино_1_out_28 ), .in_23(\дино_1_out_29 ), .in_24(\дино_1_out_30 ),
    .in_25(\дино_1_out_31 ), .in_26(\дино_1_out_32 ), .in_27(\дино_1_out_33 ), .in_28(\дино_1_out_34 ),
    .in_29(\дино_1_out_35 ), .in_30(\дино_1_out_36 ), .in_31(\дино_1_out_37 ), .in_32(\дино_1_out_38 ),
    .in_33(\удаление_препятствий_1_out_38 ), .in_34(\удаление_препятствий_1_out_39 ),
    .in_35(\удаление_препятствий_1_out_40 ), .in_36(\удаление_препятствий_1_out_41 ),
    .in_37(\удаление_препятствий_1_out_42 ), .in_38(\удаление_препятствий_1_out_43 ),
    .in_39(\удаление_препятствий_1_out_44 ), .in_40(\удаление_препятствий_1_out_45 ),
    .in_41(\удаление_препятствий_1_out_46 ), .in_42(\удаление_препятствий_1_out_47 ),
    .in_43(\удаление_препятствий_1_out_48 ), .in_44(\удаление_препятствий_1_out_49 ),
    .in_45(\удаление_препятствий_1_out_50 ), .in_46(\удаление_препятствий_1_out_51 ),
    .in_47(\удаление_препятствий_1_out_52 ), .in_48(\удаление_препятствий_1_out_53 ),
    .in_49(\удаление_препятствий_1_out_54 ), .in_50(\удаление_препятствий_1_out_55 ),
    .in_51(\удаление_препятствий_1_out_56 ), .in_52(\удаление_препятствий_1_out_57 ),
    .in_53(\удаление_препятствий_1_out_58 ), .in_54(\удаление_препятствий_1_out_59 ),
    .in_55(\удаление_препятствий_1_out_60 ), .in_56(\удаление_препятствий_1_out_61 ),
    .in_57(\удаление_препятствий_1_out_62 ), .in_58(\удаление_препятствий_1_out_63 ),
    .in_59(\удаление_препятствий_1_out_64 ), .in_60(\удаление_препятствий_1_out_65 ),
    .in_61(\удаление_препятствий_1_out_66 ), .in_62(\удаление_препятствий_1_out_67 ),
    .in_63(\удаление_препятствий_1_out_68 ), .in_64(\удаление_препятствий_1_out_69 ), .out_65(m3_0),
    .out_66(m3_1), .out_67(m3_2), .out_68(m3_3), .out_69(m3_4), .out_71(m3_55), .out_72(m3_5), .out_73(m3_6),
    .out_74(m3_7), .out_75(m3_8), .out_76(m3_9), .out_77(m3_10), .out_78(m3_11), .out_79(m3_12),
    .out_80(m3_13), .out_81(m3_14), .out_82(m3_15), .out_83(m3_16), .out_84(m3_17), .out_85(m3_18),
    .out_86(m3_19), .out_87(m3_20), .out_88(m3_21), .out_89(m3_22), .out_90(m3_23), .out_91(m3_c6),
    .out_92(m3_c5), .out_93(m3_c4), .out_94(m3_c3), .out_95(m3_c2), .out_96(m3_c1), .out_97(m3_c0),
    .stop(stop1), .out_98(\или32_1_out_98 ));
  or or_2 (or_2_out, comparator_7_eq, comparator_8_eq);
  Multiplexer multiplexer_1 (.in0(clock), .in1(clock_2), .out(clock_3), .sel(\или32_1_out_98 ), .en(1'b1));
  and and_2 (and_2_out, or_2_out, comparator_9_eq);
  \коллизии_ямы  \u_коллизии_ямы_1  (.in_1(\дино_1_out_38 ), .in_2(m3_r2), .stop(stop2));
  DotMatrix #(.inputtype("row"), .matrixcols(32), .matrixrows(32)) dotmatrix_5 (
    .row0(m1_0), .row1(m1_1), .row2(m1_2), .row3(m1_3), .row4(m1_4), .row5(m1_5), .row6(m1_5), .row7(m1_6),
    .row8(m1_7), .row9(m1_8), .row10(m1_9), .row11(m1_10), .row12(m1_11), .row13(m1_12), .row14(m1_13),
    .row15(m1_14), .row16(m1_15), .row17(m1_16), .row18(m1_17), .row19(m1_18), .row20(m1_19), .row21(m1_20),
    .row22(m1_21), .row23(m1_22), .row24(m1_23), .row25(m1_c6), .row26(m1_c5), .row27(m1_c4), .row28(m1_c3),
    .row29(m1_c2), .row30(m1_c1), .row31(m1_c0));
  DotMatrix #(.inputtype("row"), .matrixcols(32), .matrixrows(3)) dotmatrix_6 (
    .row0(m1_r2), .row1(m1_r1), .row2(m1_r0));
  Counter #(.width(9), .max('h1ff)) counter_2 (
    .count(1'b1), .carry(counter_2_carry), .clk(clock_2_out));  // open: load, D, Q, clr
  Counter #(.width(5), .max('hf), .ongoal("stay")) counter_3 (
    .count(1'b1), .Q(counter_3_q), .clk(and_2_out));  // open: load, D, carry, clr
  Hex_Digit_Display hex_digit_display_5 ();  // open: value, dp
  Hex_Digit_Display hex_digit_display_6 ();  // open: value, dp
  Counter #(.width(14), .max('h3fff)) counter_4 (.count(1'b1), .Q(c), .clk(and_3_out));  // open: load, D, carry, clr
  and and_3 (and_3_out, clock_2, ~game_over);  // AND_Gate
  Subtractor #(.width(5)) subtractor_1 (.a(5'b10000), .b(counter_3_q), .out(vec_adr));  // open: bin, bout
  Hex_Digit_Display hex_digit_display_7 ();  // open: value, dp
  Hex_Digit_Display hex_digit_display_8 ();  // open: value, dp
  DotMatrix #(.matrixcols(25), .matrixrows(8)) dotmatrix_7 (
    .col0(\жизни_1_live1 ), .col1(\жизни_1_live2 ), .col2(\жизни_1_live3 ), .col3(\жизни_1_live4 ),
    .col4(\жизни_1_live5 ), .col5(\жизни_1_live6 ), .col6(\жизни_1_live7 ), .col7(\жизни_1_live8 ),
    .col8(\жизни_1_live9 ), .col9(\жизни_1_live10 ), .col10(\жизни_1_live11 ), .col11(\жизни_1_live12 ),
    .col12(\жизни_1_live13 ), .col13(\жизни_1_live14 ), .col14(\жизни_1_live15 ), .col15(\жизни_1_live16 ),
    .col16(\жизни_1_live17 ), .col17(\жизни_1_live18 ), .col18(\жизни_1_live19 ), .col19(\жизни_1_live20 ),
    .col20(\жизни_1_live21 ), .col21(\жизни_1_live22 ), .col22(\жизни_1_live23 ), .col23(\жизни_1_live24 ),
    .col24(\жизни_1_live25 ));
  \жизни  \u_жизни_1  (
    .in_1(lcount), .live1(\жизни_1_live1 ), .live2(\жизни_1_live2 ), .live3(\жизни_1_live3 ),
    .live4(\жизни_1_live4 ), .live5(\жизни_1_live5 ), .live6(\жизни_1_live6 ), .live7(\жизни_1_live7 ),
    .live8(\жизни_1_live8 ), .live9(\жизни_1_live9 ), .live10(\жизни_1_live10 ), .live11(\жизни_1_live11 ),
    .live12(\жизни_1_live12 ), .live13(\жизни_1_live13 ), .live14(\жизни_1_live14 ),
    .live15(\жизни_1_live15 ), .live16(\жизни_1_live16 ), .live17(\жизни_1_live17 ),
    .live18(\жизни_1_live18 ), .live19(\жизни_1_live19 ), .live20(\жизни_1_live20 ),
    .live21(\жизни_1_live21 ), .live22(\жизни_1_live22 ), .live23(\жизни_1_live23 ),
    .live24(\жизни_1_live24 ), .live25(\жизни_1_live25 ));
  and and_4 (clear, rest, counter_2_carry);
  Hex_Digit_Display hex_digit_display_9 ();  // open: value, dp
  Hex_Digit_Display hex_digit_display_10 ();  // open: value, dp
  Hex_Digit_Display hex_digit_display_11 ();  // open: value, dp
  Hex_Digit_Display hex_digit_display_12 ();  // open: value, dp
  Hex_Digit_Display hex_digit_display_13 ();  // open: value, dp
  Hex_Digit_Display hex_digit_display_14 ();  // open: value, dp
  Hex_Digit_Display hex_digit_display_15 ();  // open: value, dp
  Hex_Digit_Display hex_digit_display_16 ();  // open: value, dp
  Hex_Digit_Display hex_digit_display_17 ();  // open: value, dp
  Hex_Digit_Display hex_digit_display_18 ();  // open: value, dp
  Hex_Digit_Display hex_digit_display_19 ();  // open: value, dp
  Hex_Digit_Display hex_digit_display_20 ();  // open: value, dp
  \лидеры_cdm_8  \u_лидеры_cdm_8_1  (
    .recent_result(c), .losesignal(game_over), .out_22(\лидеры_cdm_8_1_out_22 ),
    .out_23(\лидеры_cdm_8_1_out_23 ), .tact(clock_2));  // open: out_4, out_9, out_14, out_5, out_10, out_15, out_6, out_11, out_16, out_7, out_12, out_17, out_8, out_13, out_18, out_19, out_20, out_21
  Hex_Digit_Display hex_digit_display_21 ();  // open: value, dp
  Hex_Digit_Display hex_digit_display_22 ();  // open: value, dp
  Hex_Digit_Display hex_digit_display_23 (.value(\лидеры_cdm_8_1_out_23 ));  // open: dp
  Hex_Digit_Display hex_digit_display_24 (.value(\лидеры_cdm_8_1_out_22 ));  // open: dp

  // Other names for the same wires on the sheet: seil = in_1
endmodule

module \сдвиг1  (
  input  [31:0] in_1,
  input  in_2,
  input  game_over,
  output [31:0] out_4
);

  Shift_Register #(.length(32)) shift_register_1 (
    .shift(1'b1), .in(in_1[31]), .clk(in_2), .clr(game_over), .q0(out_4[0]), .q1(out_4[1]), .q2(out_4[2]),
    .q3(out_4[3]), .q4(out_4[4]), .q5(out_4[5]), .q6(out_4[6]), .q7(out_4[7]), .q8(out_4[8]), .q9(out_4[9]),
    .q10(out_4[10]), .q11(out_4[11]), .q12(out_4[12]), .q13(out_4[13]), .q14(out_4[14]), .q15(out_4[15]),
    .q16(out_4[16]), .q17(out_4[17]), .q18(out_4[18]), .q19(out_4[19]), .q20(out_4[20]), .q21(out_4[21]),
    .q22(out_4[22]), .q23(out_4[23]), .q24(out_4[24]), .q25(out_4[25]), .q26(out_4[26]), .q27(out_4[27]),
    .q28(out_4[28]), .q29(out_4[29]), .q30(out_4[30]), .q31(out_4[31]));  // open: out, load, d0, d1, d2, d3, d4, d5, d6, d7, d8, d9, d10, d11, d12, d13, d14, d15, d16, d17, d18, d19, d20, d21, d22, d23, d24, d25, d26, d27, d28, d29, d30, d31

  // Other names for the same wires on the sheet: _0 = out_4[0]; _1 = out_4[1]; _2 = out_4[2]; _3 = out_4[3];
  //   _4 = out_4[4]; _5 = out_4[5]; _6 = out_4[6]; _7 = out_4[7]; _8 = out_4[8]; _9 = out_4[9]; _10 = out_4[10];
  //   _11 = out_4[11]; _12 = out_4[12]; _13 = out_4[13]; _14 = out_4[14]; _15 = out_4[15]; _16 = out_4[16];
  //   _17 = out_4[17]; _18 = out_4[18]; _19 = out_4[19]; _20 = out_4[20]; _21 = out_4[21]; _22 = out_4[22];
  //   _23 = out_4[23]; _24 = out_4[24]; _25 = out_4[25]; _26 = out_4[26]; _27 = out_4[27]; _28 = out_4[28];
  //   _29 = out_4[29]; _30 = out_4[30]; _31 = out_4[31]
endmodule

module \инкримент  (
  input  [7:0] X,
  output [7:0] R,
  output Cout
);

  wire [7:1] and_1_out;

  assign {Cout, and_1_out} = {and_1_out, 1'b1} & X;  // AND_Gate and_1, 8 bits wide
  assign R = X ^ {and_1_out, 1'b1};  // XOR_Gate xor_1, 8 bits wide
endmodule

module \сдвиг_э_та  (
  input  [31:0] in_1,
  input  [31:0] in_2,
  input  [31:0] in_3,
  input  [31:0] in_4,
  input  game_over,
  input  in_6,
  input  [31:0] in_7,
  input  [31:0] in_8,
  input  [31:0] in_9,
  output [31:0] out_10,
  output [31:0] out_11,
  output [31:0] out_12,
  output [31:0] out_13,
  output [31:0] out_14,
  output [31:0] out_15,
  output [31:0] out_16
);

  \сдвиг1  \u_сдвиг1_1  (.in_1(in_1), .in_2(in_6), .out_4(out_10), .game_over(game_over));
  \сдвиг1  \u_сдвиг1_2  (.in_1(in_2), .in_2(in_6), .out_4(out_11), .game_over(game_over));
  \сдвиг1  \u_сдвиг1_3  (.in_1(in_3), .in_2(in_6), .out_4(out_12), .game_over(game_over));
  \сдвиг1  \u_сдвиг1_4  (.in_1(in_4), .in_2(in_6), .out_4(out_13), .game_over(game_over));
  \сдвиг1  \u_сдвиг1_5  (.in_1(in_7), .in_2(in_6), .out_4(out_14), .game_over(game_over));
  \сдвиг1  \u_сдвиг1_6  (.in_1(in_8), .in_2(in_6), .out_4(out_15), .game_over(game_over));
  \сдвиг1  \u_сдвиг1_7  (.in_1(in_9), .in_2(in_6), .out_4(out_16), .game_over(game_over));
endmodule

module \кактус2  (
  input  in_1,
  output [31:0] out_2,
  output [31:0] out_3,
  output [31:0] out_4,
  output [31:0] out_5,
  output [31:0] out_6,
  output [31:0] out_7,
  output [31:0] out_8
);

  wire [4:0] counter_1_q, negator_1_out, subtractor_1_out;
  wire [31:0] decoder_1_out31, shifter_1_out, shifter_3_out, shifter_4_out;

  Subtractor #(.width(5)) subtractor_1 (.a(counter_1_q), .b(5'b00100), .out(subtractor_1_out));  // open: bin, bout
  Counter #(.width(5), .max('h1f)) counter_1 (
    .D(subtractor_1_out), .count(1'b1), .Q(counter_1_q), .clk(in_1));  // open: load, carry, clr
  Negator #(.width(5)) negator_1 (.in(subtractor_1_out), .out(negator_1_out));
  Shifter #(.width(32)) shifter_1 (.in(decoder_1_out31), .\dist (5'b00001), .out(shifter_1_out));
  Decoder #(.select(5)) decoder_1 (
    .out0(decoder_1_out31[31]), .out1(decoder_1_out31[30]), .out2(decoder_1_out31[29]),
    .out3(decoder_1_out31[28]), .out4(decoder_1_out31[27]), .out5(decoder_1_out31[26]),
    .out6(decoder_1_out31[25]), .out7(decoder_1_out31[24]), .out8(decoder_1_out31[23]),
    .out9(decoder_1_out31[22]), .out10(decoder_1_out31[21]), .out11(decoder_1_out31[20]),
    .out12(decoder_1_out31[19]), .out13(decoder_1_out31[18]), .out14(decoder_1_out31[17]),
    .out15(decoder_1_out31[16]), .out16(decoder_1_out31[15]), .out17(decoder_1_out31[14]),
    .out18(decoder_1_out31[13]), .out19(decoder_1_out31[12]), .out20(decoder_1_out31[11]),
    .out21(decoder_1_out31[10]), .out22(decoder_1_out31[9]), .out23(decoder_1_out31[8]),
    .out24(decoder_1_out31[7]), .out25(decoder_1_out31[6]), .out26(decoder_1_out31[5]),
    .out27(decoder_1_out31[4]), .out28(decoder_1_out31[3]), .out29(decoder_1_out31[2]),
    .out30(decoder_1_out31[1]), .out31(decoder_1_out31[0]), .sel(negator_1_out));  // open: en
  Shifter #(.width(32)) shifter_2 (.in(shifter_1_out), .\dist (5'b00001), .out(out_2));
  Shifter #(.width(32)) shifter_3 (.in(out_2), .\dist (5'b00001), .out(shifter_3_out));
  Shifter #(.width(32)) shifter_4 (.in(shifter_3_out), .\dist (5'b00001), .out(shifter_4_out));
  assign out_3 = decoder_1_out31 | out_2 | shifter_4_out;  // OR_Gate or_1, 32 bits wide
  assign out_5 = out_3 | shifter_1_out | shifter_3_out;  // OR_Gate or_2, 32 bits wide

  assign out_4 = out_3;
  assign out_6 = out_2;
  assign out_7 = out_2;
  assign out_8 = out_2;
endmodule

module \дорога  (
  input  in_1,
  output [31:0] out_2,
  output [31:0] out_3,
  output [31:0] out_4
);

  wire [4:0] counter_1_q, negator_1_out, subtractor_1_out;
  wire [31:0] decoder_1_out31, shifter_1_out, shifter_2_out, shifter_3_out;

  Subtractor #(.width(5)) subtractor_1 (.a(counter_1_q), .b(5'b11001), .out(subtractor_1_out));  // open: bin, bout
  Counter #(.width(5), .max('h1f)) counter_1 (
    .D(subtractor_1_out), .count(1'b1), .Q(counter_1_q), .clk(in_1));  // open: load, carry, clr
  Decoder #(.select(5)) decoder_1 (
    .out0(decoder_1_out31[31]), .out1(decoder_1_out31[30]), .out2(decoder_1_out31[29]),
    .out3(decoder_1_out31[28]), .out4(decoder_1_out31[27]), .out5(decoder_1_out31[26]),
    .out6(decoder_1_out31[25]), .out7(decoder_1_out31[24]), .out8(decoder_1_out31[23]),
    .out9(decoder_1_out31[22]), .out10(decoder_1_out31[21]), .out11(decoder_1_out31[20]),
    .out12(decoder_1_out31[19]), .out13(decoder_1_out31[18]), .out14(decoder_1_out31[17]),
    .out15(decoder_1_out31[16]), .out16(decoder_1_out31[15]), .out17(decoder_1_out31[14]),
    .out18(decoder_1_out31[13]), .out19(decoder_1_out31[12]), .out20(decoder_1_out31[11]),
    .out21(decoder_1_out31[10]), .out22(decoder_1_out31[9]), .out23(decoder_1_out31[8]),
    .out24(decoder_1_out31[7]), .out25(decoder_1_out31[6]), .out26(decoder_1_out31[5]),
    .out27(decoder_1_out31[4]), .out28(decoder_1_out31[3]), .out29(decoder_1_out31[2]),
    .out30(decoder_1_out31[1]), .out31(decoder_1_out31[0]), .sel(negator_1_out));  // open: en
  Negator #(.width(5)) negator_1 (.in(subtractor_1_out), .out(negator_1_out));
  Shifter #(.width(32), .shift("lr")) shifter_1 (.in(decoder_1_out31), .\dist (5'b00001), .out(shifter_1_out));
  Shifter #(.width(32)) shifter_2 (.in(decoder_1_out31), .\dist (5'b00001), .out(shifter_2_out));
  Shifter #(.width(32)) shifter_3 (.in(shifter_2_out), .\dist (5'b00001), .out(shifter_3_out));
  assign out_2 = shifter_1_out | shifter_2_out | shifter_3_out | decoder_1_out31;  // OR_Gate or_1, 32 bits wide

  assign out_3 = out_2;
  assign out_4 = out_2;
endmodule

module \птерадаптель  (
  input  in_1,
  output [31:0] out_2,
  output [31:0] out_3,
  output [31:0] out_4,
  output [31:0] out_5,
  output [31:0] out_6,
  output [31:0] out_7
);

  wire [4:0] counter_1_q, negator_1_out, subtractor_1_out;
  wire [31:0] shift_0, shift_1, shift_2, shift_3, shift_4, shift_5, shift_6, shift_7, shift_8, shift_9,
       shift_10, shift_11, shift_12, shift_13;

  Counter #(.width(5), .max('h1f)) counter_1 (
    .D(subtractor_1_out), .count(1'b1), .Q(counter_1_q), .clk(in_1));  // open: load, carry, clr
  Shifter #(.width(32)) shifter_1 (.in(shift_0), .\dist (5'b00001), .out(shift_1));
  Subtractor #(.width(5)) subtractor_1 (.a(counter_1_q), .b(5'b10000), .out(subtractor_1_out));  // open: bin, bout
  assign out_2 = shift_3 | shift_4 | shift_5;  // OR_Gate or_1, 32 bits wide
  assign out_3 = out_2 | shift_6 | shift_7 | shift_10 | shift_11;  // OR_Gate or_2, 32 bits wide
  assign out_4 = shift_4 | shift_5 | shift_6 | shift_7 | shift_8 | shift_10 | shift_11 | shift_12 | shift_13;  // OR_Gate or_3, 32 bits wide
  Shifter #(.width(32)) shifter_2 (.in(shift_1), .\dist (5'b00001), .out(shift_2));
  Negator #(.width(5)) negator_1 (.in(subtractor_1_out), .out(negator_1_out));
  Decoder #(.select(5)) decoder_1 (
    .out0(shift_0[31]), .out1(shift_0[30]), .out2(shift_0[29]), .out3(shift_0[28]), .out4(shift_0[27]),
    .out5(shift_0[26]), .out6(shift_0[25]), .out7(shift_0[24]), .out8(shift_0[23]), .out9(shift_0[22]),
    .out10(shift_0[21]), .out11(shift_0[20]), .out12(shift_0[19]), .out13(shift_0[18]), .out14(shift_0[17]),
    .out15(shift_0[16]), .out16(shift_0[15]), .out17(shift_0[14]), .out18(shift_0[13]), .out19(shift_0[12]),
    .out20(shift_0[11]), .out21(shift_0[10]), .out22(shift_0[9]), .out23(shift_0[8]), .out24(shift_0[7]),
    .out25(shift_0[6]), .out26(shift_0[5]), .out27(shift_0[4]), .out28(shift_0[3]), .out29(shift_0[2]),
    .out30(shift_0[1]), .out31(shift_0[0]), .sel(negator_1_out));  // open: en
  Shifter #(.width(32)) shifter_3 (.in(shift_2), .\dist (5'b00001), .out(shift_3));
  Shifter #(.width(32)) shifter_4 (.in(shift_3), .\dist (5'b00001), .out(shift_4));
  // OR_Gate or_4 is placed but not wired
  Shifter #(.width(32)) shifter_5 (.in(shift_4), .\dist (5'b00001), .out(shift_5));
  assign out_5 = shift_0 | shift_1 | shift_2 | shift_3 | shift_4 | shift_5 | shift_6 | shift_7 | shift_8 | shift_9 | shift_10;  // OR_Gate or_5, 32 bits wide
  assign out_6 = shift_3 | shift_4 | shift_5 | shift_6 | shift_10 | shift_11 | shift_12 | shift_13;  // OR_Gate or_6, 32 bits wide
  Shifter #(.width(32)) shifter_6 (.in(shift_5), .\dist (5'b00001), .out(shift_6));
  Shifter #(.width(32)) shifter_7 (.in(shift_6), .\dist (5'b00001), .out(shift_7));
  Shifter #(.width(32)) shifter_8 (.in(shift_7), .\dist (5'b00001), .out(shift_8));
  Shifter #(.width(32)) shifter_9 (.in(shift_8), .\dist (5'b00001), .out(shift_9));
  assign out_7 = shift_2 | shift_3 | shift_4 | shift_5;  // OR_Gate or_7, 32 bits wide
  Shifter #(.width(32)) shifter_10 (.in(shift_9), .\dist (5'b00001), .out(shift_10));
  Shifter #(.width(32)) shifter_11 (.in(shift_10), .\dist (5'b00001), .out(shift_11));
  Shifter #(.width(32)) shifter_12 (.in(shift_11), .\dist (5'b00001), .out(shift_12));
  Shifter #(.width(32)) shifter_13 (.in(shift_12), .\dist (5'b00001), .out(shift_13));
  DotMatrix #(.inputtype("row"), .matrixcols(32), .matrixrows(12)) dotmatrix_1 (
    .row0(out_2), .row1(out_3), .row2(out_4), .row3(out_5), .row4(out_6), .row5(out_7));  // open: row6, row7, row8, row9, row10, row11

  // Other names for the same wires on the sheet: line1[31:0] = out_2; line2[31:0] = out_3; line3[31:0] = out_4;
  //   line4[31:0] = out_5; line5[31:0] = out_6; line6[31:0] = out_7
endmodule

module \скорость2  (
  input  [4:0] del,
  input  clock,
  output out_3
);

  wire comparator_1_eq, d_ff_1_q;
  wire [4:0] counter_1_q;

  Counter #(.width(5), .max('h1f)) counter_1 (
    .D(counter_1_q), .count(1'b1), .Q(counter_1_q), .clk(clock), .clr(d_ff_1_q));  // open: load, carry
  D_Flip_Flop d_ff_1 (.clk(clock), .D(comparator_1_eq), .Q(d_ff_1_q), .en(1'b1));  // open: Qn, preset, reset
  Comparator #(.width(5)) comparator_1 (.a(counter_1_q), .b(del), .eq(comparator_1_eq));  // open: gt, lt
  T_Flip_Flop t_ff_1 (.clk(comparator_1_eq), .T(1'b1), .Q(out_3), .en(1'b1));  // open: Qn, preset, reset
endmodule

module \карта_1  (
  input  in_1,
  output [31:0] out_2,
  output [31:0] out_3,
  output [31:0] out_4,
  output [31:0] out_5,
  output [31:0] out_6,
  output [31:0] out_7,
  output [31:0] out_8,
  output [31:0] out_9,
  output [31:0] out_10,
  output [31:0] out_11,
  output [31:0] out_12,
  output [31:0] out_13,
  output [31:0] out_14,
  output [31:0] out_15,
  output [31:0] out_16,
  output [31:0] out_17,
  output [31:0] out_18,
  output [31:0] out_19,
  output [31:0] out_20,
  output [31:0] out_21,
  output [31:0] out_22,
  output [31:0] out_23,
  output [31:0] out_24,
  output [31:0] out_25,
  output [31:0] out_26,
  output [31:0] out_27,
  output [31:0] out_28,
  output [31:0] out_29,
  output [31:0] out_30,
  output [31:0] out_31,
  output [31:0] out_32,
  output [31:0] out_33,
  output [31:0] out_34,
  output [31:0] out_35,
  output [31:0] out_36
);

  wire [31:0] \дорога_1_out_2 , \дорога_1_out_3 , \дорога_1_out_4 , \кактус2_1_out_2 , \кактус2_1_out_3 ,
       \кактус2_1_out_4 , \кактус2_1_out_5 , \кактус2_1_out_6 , \кактус2_1_out_7 , \кактус2_1_out_8 ;

  \сдвиг_э_та  \u_сдвиг_э_та_1  (
    .in_6(in_1), .in_1(\кактус2_1_out_2 ), .in_2(\кактус2_1_out_3 ), .in_3(\кактус2_1_out_4 ),
    .in_4(\кактус2_1_out_5 ), .in_7(\кактус2_1_out_6 ), .in_8(\кактус2_1_out_7 ), .in_9(\кактус2_1_out_8 ),
    .out_10(out_25), .out_11(out_30), .out_12(out_35), .out_13(out_6), .out_14(out_11), .out_15(out_16),
    .out_16(out_21));  // open: game_over
  \кактус2  \u_кактус2_1  (
    .in_1(in_1), .out_2(\кактус2_1_out_2 ), .out_3(\кактус2_1_out_3 ), .out_4(\кактус2_1_out_4 ),
    .out_5(\кактус2_1_out_5 ), .out_6(\кактус2_1_out_6 ), .out_7(\кактус2_1_out_7 ), .out_8(\кактус2_1_out_8 ));
  \дорога  \u_дорога_1  (.in_1(in_1), .out_2(\дорога_1_out_2 ), .out_3(\дорога_1_out_3 ), .out_4(\дорога_1_out_4 ));
  \сдвиг_э_та  \u_сдвиг_э_та_2  (
    .in_6(in_1), .in_7(\дорога_1_out_2 ), .in_8(\дорога_1_out_3 ), .in_9(\дорога_1_out_4 ), .out_14(out_26),
    .out_15(out_31), .out_16(out_36));  // open: in_1, in_2, in_3, in_4, out_10, out_11, out_12, out_13, game_over
  DotMatrix #(.inputtype("row"), .matrixcols(32), .matrixrows(32)) dotmatrix_1 (
    .row0({32{1'b0}}), .row1({32{1'b0}}), .row2({32{1'b0}}), .row3({32{1'b0}}), .row4({32{1'b0}}),
    .row5({32{1'b0}}), .row6({32{1'b0}}), .row7({32{1'b0}}), .row8({32{1'b0}}), .row9({32{1'b0}}),
    .row10({32{1'b0}}), .row11({32{1'b0}}), .row12({32{1'b0}}), .row13({32{1'b0}}), .row14({32{1'b0}}),
    .row15({32{1'b0}}), .row16({32{1'b0}}), .row17({32{1'b0}}), .row18({32{1'b0}}), .row19({32{1'b0}}),
    .row20({32{1'b0}}), .row21({32{1'b0}}), .row22({32{1'b0}}), .row23({32{1'b0}}), .row24({32{1'b0}}),
    .row25(out_25), .row26(out_30), .row27(out_35), .row28(out_6), .row29(out_11), .row30(out_16),
    .row31(out_21));
  DotMatrix #(.inputtype("row"), .matrixcols(32), .matrixrows(3)) dotmatrix_2 (
    .row0(out_26), .row1(out_31), .row2(out_36));

  assign out_2 = {32{1'b0}};
  assign out_3 = {32{1'b0}};
  assign out_4 = {32{1'b0}};
  assign out_5 = {32{1'b0}};
  assign out_7 = {32{1'b0}};
  assign out_8 = {32{1'b0}};
  assign out_9 = {32{1'b0}};
  assign out_10 = {32{1'b0}};
  assign out_12 = {32{1'b0}};
  assign out_13 = {32{1'b0}};
  assign out_14 = {32{1'b0}};
  assign out_15 = {32{1'b0}};
  assign out_17 = {32{1'b0}};
  assign out_18 = {32{1'b0}};
  assign out_19 = {32{1'b0}};
  assign out_20 = {32{1'b0}};
  assign out_22 = {32{1'b0}};
  assign out_23 = {32{1'b0}};
  assign out_24 = {32{1'b0}};
  assign out_27 = {32{1'b0}};
  assign out_28 = {32{1'b0}};
  assign out_29 = {32{1'b0}};
  assign out_32 = {32{1'b0}};
  assign out_33 = {32{1'b0}};
  assign out_34 = {32{1'b0}};

  // Other names for the same wires on the sheet: clock = in_1; m1_c0[31:0] = out_21; m1_c1[31:0] = out_16;
  //   m1_c2[31:0] = out_11; m1_c3[31:0] = out_6; m1_c4[31:0] = out_35; m1_c5[31:0] = out_30; m1_c6[31:0] = out_25;
  //   m1_r0[31:0] = out_36; m1_r1[31:0] = out_31; m1_r2[31:0] = out_26
endmodule

module \сдвиг_карты  (
  input  in_1,
  input  in_2,
  input  [31:0] in_3,
  input  [31:0] in_4,
  input  [31:0] in_5,
  input  [31:0] in_6,
  input  [31:0] in_7,
  input  [31:0] in_8,
  input  [31:0] in_9,
  input  [31:0] in_10,
  input  [31:0] in_11,
  input  [31:0] in_12,
  input  [31:0] in_13,
  input  [31:0] in_14,
  input  [31:0] in_15,
  input  [31:0] in_16,
  input  [31:0] in_17,
  input  [31:0] in_18,
  input  [31:0] in_19,
  input  [31:0] in_20,
  input  [31:0] in_21,
  input  [31:0] in_22,
  input  [31:0] in_23,
  input  [31:0] in_24,
  input  [31:0] in_25,
  input  [31:0] in_26,
  input  [31:0] in_27,
  input  [31:0] in_28,
  input  [31:0] in_29,
  input  [31:0] in_30,
  input  [31:0] in_31,
  input  [31:0] in_32,
  input  [31:0] in_33,
  input  [31:0] in_34,
  input  [31:0] in_35,
  input  [31:0] in_36,
  input  [31:0] in_37,
  input  in_38,
  input  in_39,
  input  in_40,
  input  in_41,
  input  in_42,
  output [31:0] out_43,
  output [31:0] out_44,
  output [31:0] out_45,
  output [31:0] out_46,
  output [31:0] out_47,
  output [31:0] out_48,
  output [31:0] out_49,
  output [31:0] out_50,
  output [31:0] out_51,
  output [31:0] out_52,
  output [31:0] out_53,
  output [31:0] out_54,
  output [31:0] out_55,
  output [31:0] out_56,
  output [31:0] out_57,
  output [31:0] out_58,
  output [31:0] out_59,
  output [31:0] out_60,
  output [31:0] out_61,
  output [31:0] out_62,
  output [31:0] out_63,
  output [31:0] out_64,
  output [31:0] out_65,
  output [31:0] out_66,
  output [31:0] out_67,
  output [31:0] out_68,
  output [31:0] out_69,
  output [31:0] out_70,
  output [31:0] out_71,
  output [31:0] out_72,
  output [31:0] out_73,
  output [31:0] out_74,
  output [31:0] out_75,
  output [31:0] out_76,
  output [31:0] out_77
);

  wire [31:0] _0, _1, _2, _3, _4, _5, _6, _7, _8, _9;

  Multiplexer #(.width(32)) multiplexer_1 (.in0({32{1'b0}}), .in1(in_3), .out(_0), .sel(in_1), .en(1'b1));
  Multiplexer #(.width(32)) multiplexer_2 (.in0({32{1'b0}}), .in1(in_8), .out(_1), .sel(in_1), .en(1'b1));
  Multiplexer #(.width(32)) multiplexer_3 (.in0({32{1'b0}}), .in1(in_13), .out(_2), .sel(in_1), .en(1'b1));
  Multiplexer #(.width(32)) multiplexer_4 (.in0({32{1'b0}}), .in1(in_18), .out(_3), .sel(in_1), .en(1'b1));
  Multiplexer #(.width(32)) multiplexer_5 (.in0({32{1'b0}}), .in1(in_23), .out(_4), .sel(in_1), .en(1'b1));
  Multiplexer #(.width(32)) multiplexer_6 (.in0({32{1'b0}}), .in1(in_28), .out(_5), .sel(in_1), .en(1'b1));
  Multiplexer #(.width(32)) multiplexer_7 (.in0({32{1'b0}}), .in1(in_33), .out(_6), .sel(in_1), .en(1'b1));
  \сдвиг1  \u_сдвиг1_1  (.in_1(_0), .in_2(in_38), .out_4(out_43), .game_over(in_2));
  \сдвиг1  \u_сдвиг1_2  (.in_1(_1), .in_2(in_38), .out_4(out_48), .game_over(in_2));
  \сдвиг1  \u_сдвиг1_3  (.in_1(_2), .in_2(in_38), .out_4(out_53), .game_over(in_2));
  \сдвиг1  \u_сдвиг1_4  (.in_1(_3), .in_2(in_38), .out_4(out_58), .game_over(in_2));
  \сдвиг1  \u_сдвиг1_5  (.in_1(_4), .in_2(in_38), .out_4(out_63), .game_over(in_2));
  \сдвиг1  \u_сдвиг1_6  (.in_1(_5), .in_2(in_38), .out_4(out_68), .game_over(in_2));
  \сдвиг1  \u_сдвиг1_7  (.in_1(_6), .in_2(in_38), .out_4(out_73), .game_over(in_2));
  Multiplexer #(.width(32)) multiplexer_8 (.in0({32{1'b0}}), .in1(in_4), .out(_7), .sel(in_1), .en(1'b1));
  Multiplexer #(.width(32)) multiplexer_9 (.in0({32{1'b0}}), .in1(in_9), .out(_8), .sel(in_1), .en(1'b1));
  Multiplexer #(.width(32)) multiplexer_10 (.in0({32{1'b0}}), .in1(in_14), .out(_9), .sel(in_1), .en(1'b1));
  \сдвиг1  \u_сдвиг1_8  (.in_1(_7), .in_2(in_41), .out_4(out_44), .game_over(in_2));
  \сдвиг1  \u_сдвиг1_9  (.in_1(_8), .in_2(in_41), .out_4(out_49), .game_over(in_2));
  \сдвиг1  \u_сдвиг1_10  (.in_1(_9), .in_2(in_41), .out_4(out_54), .game_over(in_2));
  \сдвиг1  \u_сдвиг1_11  (.in_1(in_19), .in_2(in_41), .out_4(out_59), .game_over(in_2));
  \сдвиг1  \u_сдвиг1_12  (.in_1(in_24), .in_2(in_41), .out_4(out_64), .game_over(in_2));
  \сдвиг1  \u_сдвиг1_13  (.in_1(in_29), .in_2(in_41), .out_4(out_69), .game_over(in_2));
  \сдвиг1  \u_сдвиг1_14  (.in_1(in_34), .in_2(in_41), .out_4(out_74), .game_over(in_2));
  \сдвиг1  \u_сдвиг1_15  (.in_1(in_5), .in_2(in_39), .out_4(out_45), .game_over(in_2));
  \сдвиг1  \u_сдвиг1_16  (.in_1(in_10), .in_2(in_39), .out_4(out_50), .game_over(in_2));
  \сдвиг1  \u_сдвиг1_17  (.in_1(in_15), .in_2(in_39), .out_4(out_55), .game_over(in_2));
  \сдвиг1  \u_сдвиг1_18  (.in_1(in_20), .in_2(in_39), .out_4(out_60), .game_over(in_2));
  \сдвиг1  \u_сдвиг1_19  (.in_1(in_25), .in_2(in_39), .out_4(out_65), .game_over(in_2));
  \сдвиг1  \u_сдвиг1_20  (.in_1(in_30), .in_2(in_39), .out_4(out_70), .game_over(in_2));
  \сдвиг1  \u_сдвиг1_21  (.in_1(in_35), .in_2(in_39), .out_4(out_75), .game_over(in_2));
  \сдвиг1  \u_сдвиг1_22  (.in_1(in_6), .in_2(in_40), .out_4(out_46), .game_over(in_2));
  \сдвиг1  \u_сдвиг1_23  (.in_1(in_11), .in_2(in_40), .out_4(out_51), .game_over(in_2));
  \сдвиг1  \u_сдвиг1_24  (.in_1(in_16), .in_2(in_40), .out_4(out_56), .game_over(in_2));
  \сдвиг1  \u_сдвиг1_25  (.in_1(in_21), .in_2(in_40), .out_4(out_61), .game_over(in_2));
  \сдвиг1  \u_сдвиг1_26  (.in_1(in_7), .in_2(in_42), .out_4(out_47), .game_over(in_2));
  \сдвиг1  \u_сдвиг1_27  (.in_1(in_12), .in_2(in_42), .out_4(out_52), .game_over(in_2));
  \сдвиг1  \u_сдвиг1_28  (.in_1(in_17), .in_2(in_42), .out_4(out_57), .game_over(in_2));
  \сдвиг1  \u_сдвиг1_29  (.in_1(in_22), .in_2(in_42), .out_4(out_62), .game_over(in_2));
  \сдвиг1  \u_сдвиг1_30  (.in_1(in_27), .in_2(in_42), .out_4(out_67), .game_over(in_2));
  \сдвиг1  \u_сдвиг1_31  (.in_1(in_32), .in_2(in_42), .out_4(out_72), .game_over(in_2));
  \сдвиг1  \u_сдвиг1_32  (.in_1(in_37), .in_2(in_42), .out_4(out_77), .game_over(in_2));
  \сдвиг1  \u_сдвиг1_33  (.in_1(in_26), .in_2(in_42), .out_4(out_66), .game_over(in_2));
  \сдвиг1  \u_сдвиг1_34  (.in_1(in_31), .in_2(in_42), .out_4(out_71), .game_over(in_2));
  \сдвиг1  \u_сдвиг1_35  (.in_1(in_36), .in_2(in_42), .out_4(out_76), .game_over(in_2));

  // Other names for the same wires on the sheet: _0_2[31:0] = out_43; _1_2[31:0] = out_48; _2_2[31:0] = out_53;
  //   _3_2[31:0] = out_58; _4_2[31:0] = out_63; _5_2[31:0] = out_68; _6_2[31:0] = out_73; _7_2[31:0] = out_44;
  //   _8_2[31:0] = out_49; _9_2[31:0] = out_54; _10[31:0] = in_19; _10_2[31:0] = out_59; _11[31:0] = in_24;
  //   _11_2[31:0] = out_64; _12[31:0] = in_29; _12_2[31:0] = out_69; _13[31:0] = in_34; _13_2[31:0] = out_74;
  //   _14[31:0] = in_5; _14_2[31:0] = out_45; _15[31:0] = in_10; _15_2[31:0] = out_50; _16[31:0] = in_15;
  //   _16_2[31:0] = out_55; _17[31:0] = in_20; _17_2[31:0] = out_60; _18[31:0] = in_25; _18_2[31:0] = out_65;
  //   _19[31:0] = in_30; _19_2[31:0] = out_70; _20[31:0] = in_35; _20_2[31:0] = out_75; _21[31:0] = in_6;
  //   _21_2[31:0] = out_46; _22[31:0] = in_11; _22_2[31:0] = out_51; _23[31:0] = in_16; _23_2[31:0] = out_56;
  //   _24[31:0] = in_21; _24_2[31:0] = out_61; _25[31:0] = in_26; _25_2[31:0] = out_66; _26[31:0] = in_31;
  //   _26_2[31:0] = out_71; _27[31:0] = in_36; _27_2[31:0] = out_76; _28[31:0] = in_7; _28_2[31:0] = out_47;
  //   _29[31:0] = in_12; _29_2[31:0] = out_52; _30[31:0] = in_17; _30_2[31:0] = out_57; _31[31:0] = in_22;
  //   _31_2[31:0] = out_62; _32[31:0] = in_27; _32_2[31:0] = out_67; _33[31:0] = in_32; _33_2[31:0] = out_72;
  //   _34[31:0] = in_37; _34_2[31:0] = out_77; clear = in_2; game_over = in_1
endmodule

module MUX (
  input  [31:0] Input_0,
  input  sel,
  input  [31:0] Input_1,
  output [31:0] Output
);

  wire [31:0] and_1_out, and_2_out;
  wire [31:31] not_1_out;

  not not_1 (not_1_out[31], sel);
  assign and_1_out = Input_0 & {32{not_1_out[31]}};  // AND_Gate and_1, 32 bits wide
  assign and_2_out = {32{sel}} & Input_1;  // AND_Gate and_2, 32 bits wide
  assign Output = and_1_out | and_2_out;  // OR_Gate or_1, 32 bits wide
endmodule

module MUX_35 (
  input  in_1,
  input  [31:0] in_2,
  input  [31:0] in_3,
  input  [31:0] in_4,
  input  [31:0] in_5,
  input  [31:0] in_6,
  input  [31:0] in_7,
  input  [31:0] in_8,
  input  [31:0] in_9,
  input  [31:0] in_10,
  input  [31:0] in_11,
  input  [31:0] in_12,
  input  [31:0] in_13,
  input  [31:0] in_14,
  input  [31:0] in_15,
  input  [31:0] in_16,
  input  [31:0] in_17,
  input  [31:0] in_18,
  input  [31:0] in_19,
  input  [31:0] in_20,
  input  [31:0] in_21,
  input  [31:0] in_22,
  input  [31:0] in_23,
  input  [31:0] in_24,
  input  [31:0] in_25,
  input  [31:0] in_26,
  input  [31:0] in_27,
  input  [31:0] in_28,
  input  [31:0] in_29,
  input  [31:0] in_30,
  input  [31:0] in_31,
  input  [31:0] in_32,
  input  [31:0] in_33,
  input  [31:0] in_34,
  input  [31:0] in_35,
  input  [31:0] in_36,
  input  [31:0] in_37,
  input  [31:0] in_38,
  input  [31:0] in_39,
  input  [31:0] in_40,
  input  [31:0] in_41,
  input  [31:0] in_42,
  input  [31:0] in_43,
  input  [31:0] in_44,
  input  [31:0] in_45,
  input  [31:0] in_46,
  input  [31:0] in_47,
  input  [31:0] in_48,
  input  [31:0] in_49,
  input  [31:0] in_50,
  input  [31:0] in_51,
  input  [31:0] in_52,
  input  [31:0] in_53,
  input  [31:0] in_54,
  input  [31:0] in_55,
  input  [31:0] in_56,
  input  [31:0] in_57,
  input  [31:0] in_58,
  input  [31:0] in_59,
  input  [31:0] in_60,
  input  [31:0] in_61,
  input  [31:0] in_62,
  input  [31:0] in_63,
  input  [31:0] in_64,
  input  [31:0] in_65,
  input  [31:0] in_66,
  input  [31:0] in_67,
  input  [31:0] in_68,
  input  [31:0] in_69,
  input  [31:0] in_70,
  input  [31:0] in_71,
  output [31:0] out_72,
  output [31:0] out_73,
  output [31:0] out_74,
  output [31:0] out_75,
  output [31:0] out_76,
  output [31:0] out_77,
  output [31:0] out_78,
  output [31:0] out_79,
  output [31:0] out_80,
  output [31:0] out_81,
  output [31:0] out_82,
  output [31:0] out_83,
  output [31:0] out_84,
  output [31:0] out_85,
  output [31:0] out_86,
  output [31:0] out_87,
  output [31:0] out_88,
  output [31:0] out_89,
  output [31:0] out_90,
  output [31:0] out_91,
  output [31:0] out_92,
  output [31:0] out_93,
  output [31:0] out_94,
  output [31:0] out_95,
  output [31:0] out_96,
  output [31:0] out_97,
  output [31:0] out_98,
  output [31:0] out_99,
  output [31:0] out_100,
  output [31:0] out_101,
  output [31:0] out_102,
  output [31:0] out_103,
  output [31:0] out_104,
  output [31:0] out_105,
  output [31:0] out_106
);

  MUX mux_1 (.Input_0(in_2), .sel(in_1), .Input_1(in_3), .Output(out_72));
  MUX mux_2 (.Input_0(in_4), .sel(in_1), .Input_1(in_5), .Output(out_73));
  MUX mux_3 (.Input_0(in_6), .sel(in_1), .Input_1(in_7), .Output(out_74));
  MUX mux_4 (.Input_0(in_8), .sel(in_1), .Input_1(in_9), .Output(out_75));
  MUX mux_5 (.Input_0(in_10), .sel(in_1), .Input_1(in_11), .Output(out_76));
  MUX mux_6 (.Input_0(in_12), .sel(in_1), .Input_1(in_13), .Output(out_77));
  MUX mux_7 (.Input_0(in_14), .sel(in_1), .Input_1(in_15), .Output(out_78));
  MUX mux_8 (.Input_0(in_16), .sel(in_1), .Input_1(in_17), .Output(out_79));
  MUX mux_9 (.Input_0(in_18), .sel(in_1), .Input_1(in_19), .Output(out_80));
  MUX mux_10 (.Input_0(in_20), .sel(in_1), .Input_1(in_21), .Output(out_81));
  MUX mux_11 (.Input_0(in_22), .sel(in_1), .Input_1(in_23), .Output(out_82));
  MUX mux_12 (.Input_0(in_24), .sel(in_1), .Input_1(in_25), .Output(out_83));
  MUX mux_13 (.Input_0(in_26), .sel(in_1), .Input_1(in_27), .Output(out_84));
  MUX mux_14 (.Input_0(in_28), .sel(in_1), .Input_1(in_29), .Output(out_85));
  MUX mux_15 (.Input_0(in_30), .sel(in_1), .Input_1(in_31), .Output(out_86));
  MUX mux_16 (.Input_0(in_32), .sel(in_1), .Input_1(in_33), .Output(out_87));
  MUX mux_17 (.Input_0(in_34), .sel(in_1), .Input_1(in_35), .Output(out_88));
  MUX mux_18 (.Input_0(in_36), .sel(in_1), .Input_1(in_37), .Output(out_89));
  MUX mux_19 (.Input_0(in_38), .sel(in_1), .Input_1(in_39), .Output(out_90));
  MUX mux_20 (.Input_0(in_40), .sel(in_1), .Input_1(in_41), .Output(out_91));
  MUX mux_21 (.Input_0(in_42), .sel(in_1), .Input_1(in_43), .Output(out_92));
  MUX mux_22 (.Input_0(in_44), .sel(in_1), .Input_1(in_45), .Output(out_93));
  MUX mux_23 (.Input_0(in_46), .sel(in_1), .Input_1(in_47), .Output(out_94));
  MUX mux_24 (.Input_0(in_48), .sel(in_1), .Input_1(in_49), .Output(out_95));
  MUX mux_25 (.Input_0(in_50), .sel(in_1), .Input_1(in_51), .Output(out_96));
  MUX mux_26 (.Input_0(in_52), .sel(in_1), .Input_1(in_53), .Output(out_97));
  MUX mux_27 (.Input_0(in_54), .sel(in_1), .Input_1(in_55), .Output(out_98));
  MUX mux_28 (.Input_0(in_56), .sel(in_1), .Input_1(in_57), .Output(out_99));
  MUX mux_29 (.Input_0(in_58), .sel(in_1), .Input_1(in_59), .Output(out_100));
  MUX mux_30 (.Input_0(in_60), .sel(in_1), .Input_1(in_61), .Output(out_101));
  MUX mux_31 (.Input_0(in_62), .sel(in_1), .Input_1(in_63), .Output(out_102));
  MUX mux_32 (.Input_0(in_64), .sel(in_1), .Input_1(in_65), .Output(out_103));
  MUX mux_33 (.Input_0(in_66), .sel(in_1), .Input_1(in_67), .Output(out_104));
  MUX mux_34 (.Input_0(in_68), .sel(in_1), .Input_1(in_69), .Output(out_105));
  MUX mux_35 (.Input_0(in_70), .sel(in_1), .Input_1(in_71), .Output(out_106));
endmodule

module \дино  (
  input  jump,
  input  Game_Over,
  input  clock,
  input  sit_down,
  input  choose,
  output [31:0] out_6,
  output [31:0] out_7,
  output [31:0] out_8,
  output [31:0] out_9,
  output [31:0] out_10,
  output [31:0] out_11,
  output [31:0] out_12,
  output [31:0] out_13,
  output [31:0] out_14,
  output [31:0] out_15,
  output [31:0] out_16,
  output [31:0] out_17,
  output [31:0] out_18,
  output jump_out,
  output [31:0] out_20,
  output [31:0] out_21,
  output [31:0] out_22,
  output [31:0] out_23,
  output [31:0] out_24,
  output [31:0] out_25,
  output [31:0] out_26,
  output [31:0] out_27,
  output [31:0] out_28,
  output [31:0] out_29,
  output [31:0] out_30,
  output [31:0] out_31,
  output [31:0] out_32,
  output [31:0] out_33,
  output [31:0] out_34,
  output [31:0] out_35,
  output [31:0] out_36,
  output [31:0] out_37,
  output [31:0] out_38
);

  wire fall_1_clean_2, fall_1_st_j, jump_1_fall;
  wire [31:0] D1, D2, D3, D4, D5, D6, D7, D8, D9, f1, f2, f3, f4, f5, f6, f7, f8, f9, f10, f11, f12, f13,
       f14, f15, fall_1_d1, fall_1_d2, fall_1_d3, fall_1_d4, fall_1_d5, fall_1_d6, fall_1_d7, fall_1_d8,
       fall_1_d9, fall_1_f1, fall_1_f2, fall_1_f3, fall_1_f4, fall_1_f5, fall_1_f6, fall_1_f7, fall_1_f8,
       fall_1_f9, fall_1_f10, fall_1_f11, fall_1_f12, fall_1_f13, fall_1_f14, fall_1_f15, jump_1_d1,
       jump_1_d2, jump_1_d3, jump_1_d4, jump_1_d5, jump_1_d6, jump_1_d7, jump_1_d8, jump_1_d9, jump_1_f1,
       jump_1_f2, jump_1_f3, jump_1_f4, jump_1_f5, jump_1_f6, jump_1_f7, jump_1_f8, jump_1_f9, jump_1_f10,
       jump_1_f11, jump_1_f12, jump_1_f13, jump_1_f14, jump_1_f15;

  dino dino_1 (
    .stop(Game_Over), .sit_down(sit_down), .jump(jump_out), .fall(jump_1_fall), .choose(choose),
    .clock(clock), .out_33(out_38), .out_34(out_37), .out_35(out_36), .out_36(out_35), .out_37(out_34),
    .out_38(out_33), .out_39(out_32), .out_40(out_31), .out_41(out_30), .out_42(out_29), .out_43(out_28),
    .out_44(out_27), .out_45(out_26), .out_46(out_25), .out_47(out_24), .out_48(out_23), .out_49(out_22),
    .out_50(out_21), .out_51(out_20), .out_52(out_18), .out_53(out_17), .out_54(out_16), .out_55(out_15),
    .out_31(out_14), .out_32(out_13), .out_56(out_12), .out_57(out_11), .out_58(out_10), .out_59(out_9),
    .out_60(out_8), .out_61(out_7), .out_62(out_6), .in_7(D1), .in_8(D2), .in_9(D3), .in_10(D4), .in_11(D5),
    .in_12(D6), .in_13(D7), .in_14(D8), .in_15(D9), .in_16(f1), .in_17(f2), .in_18(f3), .in_19(f4),
    .in_20(f5), .in_21(f6), .in_22(f7), .in_23(f8), .in_24(f9), .in_25(f10), .in_26(f11), .in_27(f12),
    .in_28(f13), .in_29(f14), .in_30(f15));
  DotMatrix #(.inputtype("row"), .matrixcols(32), .matrixrows(32)) dotmatrix_1 (
    .row0(out_6), .row1(out_7), .row2(out_8), .row3(out_9), .row4(out_10), .row5(out_11), .row6(out_12),
    .row7(out_13), .row8(out_14), .row9(out_15), .row10(out_16), .row11(out_17), .row12(out_18),
    .row13(out_20), .row14(out_21), .row15(out_22), .row16(out_23), .row17(out_24), .row18(out_25),
    .row19(out_26), .row20(out_27), .row21(out_28), .row22(out_29), .row23(out_30), .row24(out_31),
    .row25(out_32), .row26(out_33), .row27(out_34), .row28(out_35), .row29(out_36), .row30(out_37),
    .row31(out_38));
  jump jump_1 (
    .choose(choose), .clock(clock), .jump(jump), .clean(fall_1_st_j), .d1(jump_1_d1), .d2(jump_1_d2),
    .d3(jump_1_d3), .d4(jump_1_d4), .d5(jump_1_d5), .d6(jump_1_d6), .d7(jump_1_d7), .d8(jump_1_d8),
    .d9(jump_1_d9), .f1(jump_1_f1), .f2(jump_1_f2), .f3(jump_1_f3), .f4(jump_1_f4), .f5(jump_1_f5),
    .f6(jump_1_f6), .f7(jump_1_f7), .f8(jump_1_f8), .f9(jump_1_f9), .f10(jump_1_f10), .f11(jump_1_f11),
    .f12(jump_1_f12), .f13(jump_1_f13), .f14(jump_1_f14), .f15(jump_1_f15), .fall(jump_1_fall),
    .jump_out(jump_out));
  Multiplexer #(.width(32)) multiplexer_1 (
    .in0(jump_1_f15), .in1(fall_1_d1), .out(f15), .sel(jump_1_fall));  // open: en
  Multiplexer #(.width(32)) multiplexer_2 (
    .in0(jump_1_f14), .in1(fall_1_d2), .out(f14), .sel(jump_1_fall));  // open: en
  Multiplexer #(.width(32)) multiplexer_3 (
    .in0(jump_1_f13), .in1(fall_1_d3), .out(f13), .sel(jump_1_fall));  // open: en
  Multiplexer #(.width(32)) multiplexer_4 (
    .in0(jump_1_f12), .in1(fall_1_d4), .out(f12), .sel(jump_1_fall));  // open: en
  fall fall_1 (
    .clock(clock), .fall(jump_1_fall), .clean(fall_1_clean_2), .f15_in(jump_1_f14), .f14_in(jump_1_f13),
    .f13_in(jump_1_f12), .f12_in(jump_1_f11), .f11_in(jump_1_f10), .f10_in(jump_1_f9), .f9_in(jump_1_f8),
    .f8_in(jump_1_f7), .f7_in(jump_1_f6), .f6_in(jump_1_f5), .d1(fall_1_d1), .d2(fall_1_d2), .d3(fall_1_d3),
    .d4(fall_1_d4), .d5(fall_1_d5), .d6(fall_1_d6), .d7(fall_1_d7), .d8(fall_1_d8), .d9(fall_1_d9),
    .f1(fall_1_f1), .f2(fall_1_f2), .f3(fall_1_f3), .f4(fall_1_f4), .f5(fall_1_f5), .f6(fall_1_f6),
    .f7(fall_1_f7), .f8(fall_1_f8), .f9(fall_1_f9), .f10(fall_1_f10), .f11(fall_1_f11), .f12(fall_1_f12),
    .f13(fall_1_f13), .f14(fall_1_f14), .f15(fall_1_f15), .clean_2(fall_1_clean_2), .st_j(fall_1_st_j));
  Multiplexer #(.width(32)) multiplexer_5 (
    .in0(jump_1_f11), .in1(fall_1_d5), .out(f11), .sel(jump_1_fall));  // open: en
  Multiplexer #(.width(32)) multiplexer_6 (
    .in0(jump_1_f10), .in1(fall_1_d6), .out(f10), .sel(jump_1_fall));  // open: en
  Multiplexer #(.width(32)) multiplexer_7 (.in0(jump_1_f9), .in1(fall_1_d7), .out(f9), .sel(jump_1_fall));  // open: en
  Multiplexer #(.width(32)) multiplexer_8 (.in0(jump_1_f8), .in1(fall_1_d8), .out(f8), .sel(jump_1_fall));  // open: en
  Multiplexer #(.width(32)) multiplexer_9 (.in0(jump_1_f7), .in1(fall_1_d9), .out(f7), .sel(jump_1_fall));  // open: en
  Multiplexer #(.width(32)) multiplexer_10 (.in0(jump_1_f6), .in1(fall_1_f1), .out(f6), .sel(jump_1_fall));  // open: en
  Multiplexer #(.width(32)) multiplexer_11 (.in0(jump_1_f5), .in1(fall_1_f2), .out(f5), .sel(jump_1_fall));  // open: en
  Multiplexer #(.width(32)) multiplexer_12 (.in0(jump_1_f4), .in1(fall_1_f3), .out(f4), .sel(jump_1_fall));  // open: en
  Multiplexer #(.width(32)) multiplexer_13 (.in0(jump_1_f2), .in1(fall_1_f5), .out(f2), .sel(jump_1_fall));  // open: en
  Multiplexer #(.width(32)) multiplexer_14 (.in0(jump_1_f3), .in1(fall_1_f4), .out(f3), .sel(jump_1_fall));  // open: en
  Multiplexer #(.width(32)) multiplexer_15 (.in0(jump_1_f1), .in1(fall_1_f6), .out(f1), .sel(jump_1_fall));  // open: en
  Multiplexer #(.width(32)) multiplexer_16 (.in0(jump_1_d9), .in1(fall_1_f7), .out(D9), .sel(jump_1_fall));  // open: en
  Multiplexer #(.width(32)) multiplexer_17 (.in0(jump_1_d8), .in1(fall_1_f8), .out(D8), .sel(jump_1_fall));  // open: en
  Multiplexer #(.width(32)) multiplexer_18 (.in0(jump_1_d7), .in1(fall_1_f9), .out(D7), .sel(jump_1_fall));  // open: en
  Multiplexer #(.width(32)) multiplexer_19 (
    .in0(jump_1_d6), .in1(fall_1_f10), .out(D6), .sel(jump_1_fall));  // open: en
  Multiplexer #(.width(32)) multiplexer_20 (
    .in0(jump_1_d5), .in1(fall_1_f11), .out(D5), .sel(jump_1_fall));  // open: en
  Multiplexer #(.width(32)) multiplexer_21 (
    .in0(jump_1_d4), .in1(fall_1_f12), .out(D4), .sel(jump_1_fall));  // open: en
  Multiplexer #(.width(32)) multiplexer_22 (
    .in0(jump_1_d3), .in1(fall_1_f13), .out(D3), .sel(jump_1_fall));  // open: en
  Multiplexer #(.width(32)) multiplexer_23 (
    .in0(jump_1_d2), .in1(fall_1_f14), .out(D2), .sel(jump_1_fall));  // open: en
  Multiplexer #(.width(32)) multiplexer_24 (
    .in0(jump_1_d1), .in1(fall_1_f15), .out(D1), .sel(jump_1_fall));  // open: en

  // Other names for the same wires on the sheet: v1[31:0] = out_38; v2[31:0] = out_37; v3[31:0] = out_36;
  //   v4[31:0] = out_35; v5[31:0] = out_34; v6[31:0] = out_33; v7[31:0] = out_32; v8[31:0] = out_31;
  //   v9[31:0] = out_30; v10[31:0] = out_29; v11[31:0] = out_28; v12[31:0] = out_27; v13[31:0] = out_26;
  //   v14[31:0] = out_25; v15[31:0] = out_24; v16[31:0] = out_23; v17[31:0] = out_22; v18[31:0] = out_21;
  //   v19[31:0] = out_20; v20[31:0] = out_18; v21[31:0] = out_17; v22[31:0] = out_16; v23[31:0] = out_15;
  //   v24[31:0] = out_14; v25[31:0] = out_13; v26[31:0] = out_12; v27[31:0] = out_11; v28[31:0] = out_10;
  //   v29[31:0] = out_9; v30[31:0] = out_8; v31[31:0] = out_7; v32[31:0] = out_6
endmodule

module \или32  (
  input  [31:0] in_1,
  input  [31:0] in_2,
  input  [31:0] in_3,
  input  [31:0] in_4,
  input  [31:0] in_5,
  input  [31:0] in_6,
  input  [31:0] in_7,
  input  [31:0] in_8,
  input  [31:0] in_9,
  input  [31:0] in_10,
  input  [31:0] in_11,
  input  [31:0] in_12,
  input  [31:0] in_13,
  input  [31:0] in_14,
  input  [31:0] in_15,
  input  [31:0] in_16,
  input  [31:0] in_17,
  input  [31:0] in_18,
  input  [31:0] in_19,
  input  [31:0] in_20,
  input  [31:0] in_21,
  input  [31:0] in_22,
  input  [31:0] in_23,
  input  [31:0] in_24,
  input  [31:0] in_25,
  input  [31:0] in_26,
  input  [31:0] in_27,
  input  [31:0] in_28,
  input  [31:0] in_29,
  input  [31:0] in_30,
  input  [31:0] in_31,
  input  [31:0] in_32,
  input  [31:0] in_33,
  input  [31:0] in_34,
  input  [31:0] in_35,
  input  [31:0] in_36,
  input  [31:0] in_37,
  input  [31:0] in_38,
  input  [31:0] in_39,
  input  [31:0] in_40,
  input  [31:0] in_41,
  input  [31:0] in_42,
  input  [31:0] in_43,
  input  [31:0] in_44,
  input  [31:0] in_45,
  input  [31:0] in_46,
  input  [31:0] in_47,
  input  [31:0] in_48,
  input  [31:0] in_49,
  input  [31:0] in_50,
  input  [31:0] in_51,
  input  [31:0] in_52,
  input  [31:0] in_53,
  input  [31:0] in_54,
  input  [31:0] in_55,
  input  [31:0] in_56,
  input  [31:0] in_57,
  input  [31:0] in_58,
  input  [31:0] in_59,
  input  [31:0] in_60,
  input  [31:0] in_61,
  input  [31:0] in_62,
  input  [31:0] in_63,
  input  [31:0] in_64,
  output [31:0] out_65,
  output [31:0] out_66,
  output [31:0] out_67,
  output [31:0] out_68,
  output [31:0] out_69,
  output stop,
  output [31:0] out_71,
  output [31:0] out_72,
  output [31:0] out_73,
  output [31:0] out_74,
  output [31:0] out_75,
  output [31:0] out_76,
  output [31:0] out_77,
  output [31:0] out_78,
  output [31:0] out_79,
  output [31:0] out_80,
  output [31:0] out_81,
  output [31:0] out_82,
  output [31:0] out_83,
  output [31:0] out_84,
  output [31:0] out_85,
  output [31:0] out_86,
  output [31:0] out_87,
  output [31:0] out_88,
  output [31:0] out_89,
  output [31:0] out_90,
  output [31:0] out_91,
  output [31:0] out_92,
  output [31:0] out_93,
  output [31:0] out_94,
  output [31:0] out_95,
  output [31:0] out_96,
  output [31:0] out_97,
  output out_98
);

  assign out_65 = in_1 | in_33;  // OR_Gate or_1, 32 bits wide
  assign out_66 = in_2 | in_34;  // OR_Gate or_2, 32 bits wide
  assign out_67 = in_3 | in_35;  // OR_Gate or_3, 32 bits wide
  assign out_68 = in_4 | in_36;  // OR_Gate or_4, 32 bits wide
  assign out_69 = in_5 | in_37;  // OR_Gate or_5, 32 bits wide
  assign out_71 = in_6 | in_38;  // OR_Gate or_6, 32 bits wide
  assign out_72 = in_7 | in_39;  // OR_Gate or_7, 32 bits wide
  assign out_73 = in_8 | in_40;  // OR_Gate or_8, 32 bits wide
  assign out_74 = in_9 | in_41;  // OR_Gate or_9, 32 bits wide
  assign out_75 = in_10 | in_42;  // OR_Gate or_10, 32 bits wide
  assign out_76 = in_11 | in_43;  // OR_Gate or_11, 32 bits wide
  assign out_77 = in_12 | in_44;  // OR_Gate or_12, 32 bits wide
  assign out_78 = in_13 | in_45;  // OR_Gate or_13, 32 bits wide
  assign out_79 = in_14 | in_46;  // OR_Gate or_14, 32 bits wide
  assign out_80 = in_15 | in_47;  // OR_Gate or_15, 32 bits wide
  assign out_81 = in_16 | in_48;  // OR_Gate or_16, 32 bits wide
  assign out_82 = in_17 | in_49;  // OR_Gate or_17, 32 bits wide
  assign out_83 = in_18 | in_50;  // OR_Gate or_18, 32 bits wide
  assign out_84 = in_19 | in_51;  // OR_Gate or_19, 32 bits wide
  assign out_85 = in_20 | in_52;  // OR_Gate or_20, 32 bits wide
  assign out_86 = in_21 | in_53;  // OR_Gate or_21, 32 bits wide
  assign out_87 = in_22 | in_54;  // OR_Gate or_22, 32 bits wide
  assign out_88 = in_23 | in_55;  // OR_Gate or_23, 32 bits wide
  assign out_89 = in_24 | in_56;  // OR_Gate or_24, 32 bits wide
  assign out_90 = in_25 | in_57;  // OR_Gate or_25, 32 bits wide
  assign out_91 = in_26 | in_58;  // OR_Gate or_26, 32 bits wide
  assign out_92 = in_27 | in_59;  // OR_Gate or_27, 32 bits wide
  assign out_93 = in_28 | in_60;  // OR_Gate or_28, 32 bits wide
  assign out_94 = in_29 | in_61;  // OR_Gate or_29, 32 bits wide
  assign out_95 = in_30 | in_62;  // OR_Gate or_30, 32 bits wide
  assign out_96 = in_31 | in_63;  // OR_Gate or_31, 32 bits wide
  assign out_97 = in_32 | in_64;  // OR_Gate or_32, 32 bits wide
  \коллизии_кактусы  \u_коллизии_кактусы_1  (
    .in_1(in_1), .in_2(in_33), .in_3(in_2), .in_4(in_34), .in_5(in_3), .in_6(in_35), .in_7(in_4),
    .in_8(in_36), .in_9(in_5), .in_10(in_37), .in_11(in_6), .in_12(in_38), .in_13(in_7), .in_14(in_39),
    .in_15(in_8), .in_16(in_40), .in_17(in_9), .in_18(in_41), .in_19(in_10), .in_20(in_42), .in_21(in_11),
    .in_22(in_43), .in_23(in_12), .in_24(in_44), .in_25(in_13), .in_26(in_45), .in_27(in_14), .in_28(in_46),
    .in_29(in_15), .in_30(in_47), .in_31(in_16), .in_32(in_48), .in_33(in_17), .in_34(in_49), .in_35(in_18),
    .in_36(in_50), .in_37(in_19), .in_38(in_51), .in_39(in_20), .in_40(in_52), .in_41(in_21), .in_42(in_53),
    .in_43(in_22), .in_44(in_54), .in_45(in_23), .in_46(in_55), .in_47(in_24), .in_48(in_56), .in_49(in_25),
    .in_50(in_57), .in_51(in_26), .in_52(in_58), .in_53(in_27), .in_54(in_59), .in_55(in_28), .in_56(in_60),
    .in_57(in_29), .in_58(in_61), .in_59(in_30), .in_60(in_62), .in_61(in_31), .in_62(in_63), .in_63(in_32),
    .in_64(in_64), .out_65(stop), .out_66(out_98));
endmodule

module jump (
  input  choose,
  input  clock,
  input  jump,
  input  clean,
  output [31:0] d1,
  output [31:0] d2,
  output [31:0] d3,
  output [31:0] d4,
  output [31:0] d5,
  output [31:0] d6,
  output [31:0] d7,
  output [31:0] d8,
  output [31:0] d9,
  output [31:0] f1,
  output [31:0] f2,
  output [31:0] f3,
  output [31:0] f4,
  output [31:0] f5,
  output [31:0] f6,
  output [31:0] f7,
  output [31:0] f8,
  output [31:0] f9,
  output [31:0] f10,
  output [31:0] f11,
  output [31:0] f12,
  output [31:0] f13,
  output [31:0] f14,
  output [31:0] f15,
  output fall,
  output jump_out
);

  wire and_1_out, and_2_out, and_3_out, comparator_1_eq, comparator_2_eq, comparator_3_eq, comparator_4_eq,
       multiplexer_1_out, multiplexer_2_out, not_1_out, not_2_out;
  wire [7:0] adder_1_out, counter_1_q, multiplexer_12_out, register_10_q;
  wire [31:0] counter_2_q, multiplexer_3_out, multiplexer_4_out, multiplexer_5_out, multiplexer_6_out,
       multiplexer_7_out, multiplexer_8_out, multiplexer_9_out, multiplexer_10_out, multiplexer_11_out,
       \дино_выбор_1_d1 , \дино_выбор_1_d2 , \дино_выбор_1_d3 , \дино_выбор_1_d4 , \дино_выбор_1_d5 ,
       \дино_выбор_1_d6 , \дино_выбор_1_d7 , \дино_выбор_1_d8 , \дино_выбор_1_d9 ;

  and and_1 (and_1_out, jump, and_2_out);
  \дино_выбор  \u_дино_выбор_1  (
    .choose(choose), .d1(\дино_выбор_1_d1 ), .d2(\дино_выбор_1_d2 ), .d3(\дино_выбор_1_d3 ),
    .d4(\дино_выбор_1_d4 ), .d5(\дино_выбор_1_d5 ), .d6(\дино_выбор_1_d6 ), .d7(\дино_выбор_1_d7 ),
    .d8(\дино_выбор_1_d8 ), .d9(\дино_выбор_1_d9 ));
  not not_1 (not_1_out, jump);
  Counter #(.max('h1f), .trigger("falling")) counter_1 (
    .Q(counter_1_q), .clk(clock), .clr(comparator_1_eq));  // open: load, D, count, carry
  Multiplexer multiplexer_1 (
    .in0(comparator_1_eq), .in1(comparator_4_eq), .out(multiplexer_1_out), .sel(fall));  // open: en
  and and_2 (and_2_out, comparator_1_eq, multiplexer_1_out);
  Counter #(.width(32), .max('hffffffff), .trigger("falling")) counter_2 (
    .Q(counter_2_q), .clk(and_1_out), .clr(and_3_out));  // open: load, D, count, carry
  and and_3 (and_3_out, clean, not_1_out);
  Comparator comparator_1 (.a(counter_1_q), .b(adder_1_out), .eq(comparator_1_eq));  // open: gt, lt
  Multiplexer multiplexer_2 (.in0(1'b0), .in1(and_2_out), .out(multiplexer_2_out), .sel(jump_out));  // open: en
  Multiplexer #(.width(32)) multiplexer_3 (
    .in0({32{1'b0}}), .in1(\дино_выбор_1_d1 ), .out(multiplexer_3_out), .sel(comparator_2_eq));  // open: en
  Comparator #(.width(32)) comparator_2 (
    .a(counter_2_q), .b({32{1'b0}}), .gt(jump_out), .eq(comparator_2_eq));  // open: lt
  Register #(.width(32)) register_1 (.D(multiplexer_3_out), .en(and_2_out), .Q(d1), .clk(and_2_out));  // open: clr
  Multiplexer #(.width(32)) multiplexer_4 (
    .in0(d1), .in1(\дино_выбор_1_d2 ), .out(multiplexer_4_out), .sel(comparator_2_eq));  // open: en
  not not_2 (not_2_out, jump_out);
  Register #(.width(32)) register_2 (.D(multiplexer_5_out), .en(and_2_out), .Q(d3), .clk(and_2_out));  // open: clr
  Register #(.width(32)) register_3 (.D(multiplexer_4_out), .en(and_2_out), .Q(d2), .clk(and_2_out));  // open: clr
  Multiplexer #(.width(32)) multiplexer_5 (
    .in0(d2), .in1(\дино_выбор_1_d3 ), .out(multiplexer_5_out), .sel(comparator_2_eq));  // open: en
  Register #(.width(32)) register_4 (.D(multiplexer_6_out), .en(and_2_out), .Q(d4), .clk(and_2_out));  // open: clr
  Multiplexer #(.width(32)) multiplexer_6 (
    .in0(d3), .in1(\дино_выбор_1_d4 ), .out(multiplexer_6_out), .sel(comparator_2_eq));  // open: en
  Register #(.width(32)) register_5 (.D(multiplexer_7_out), .en(and_2_out), .Q(d5), .clk(and_2_out));  // open: clr
  Register #(.width(32)) register_6 (.D(multiplexer_8_out), .en(and_2_out), .Q(d6), .clk(and_2_out));  // open: clr
  Multiplexer #(.width(32)) multiplexer_7 (
    .in0(d4), .in1(\дино_выбор_1_d5 ), .out(multiplexer_7_out), .sel(comparator_2_eq));  // open: en
  Multiplexer #(.width(32)) multiplexer_8 (
    .in0(d5), .in1(\дино_выбор_1_d6 ), .out(multiplexer_8_out), .sel(comparator_2_eq));  // open: en
  Register #(.width(32)) register_7 (.D(multiplexer_9_out), .en(and_2_out), .Q(d7), .clk(and_2_out));  // open: clr
  Multiplexer #(.width(32)) multiplexer_9 (
    .in0(d6), .in1(\дино_выбор_1_d7 ), .out(multiplexer_9_out), .sel(comparator_2_eq));  // open: en
  Adder adder_1 (.a(multiplexer_12_out), .b(8'h2), .out(adder_1_out));  // open: cin, cout
  Register #(.width(32)) register_8 (.D(multiplexer_10_out), .en(and_2_out), .Q(d8), .clk(and_2_out));  // open: clr
  Register #(.width(32)) register_9 (.D(multiplexer_11_out), .en(and_2_out), .Q(d9), .clk(and_2_out));  // open: clr
  Multiplexer #(.width(32)) multiplexer_10 (
    .in0(d7), .in1(\дино_выбор_1_d8 ), .out(multiplexer_10_out), .sel(comparator_2_eq));  // open: en
  Register register_10 (
    .D(adder_1_out), .en(multiplexer_2_out), .Q(register_10_q), .clk(multiplexer_2_out), .clr(and_3_out));
  Register #(.width(32)) register_11 (.D(d9), .en(and_2_out), .Q(f1), .clk(and_2_out), .clr(not_2_out));
  Register #(.width(32)) register_12 (.D(f1), .en(and_2_out), .Q(f2), .clk(and_2_out), .clr(not_2_out));
  Multiplexer #(.width(32)) multiplexer_11 (
    .in0(d8), .in1(\дино_выбор_1_d9 ), .out(multiplexer_11_out), .sel(comparator_2_eq));  // open: en
  Comparator comparator_3 (.a(register_10_q), .b({8{1'b0}}), .eq(comparator_3_eq));  // open: gt, lt
  Register #(.width(32)) register_13 (.D(f2), .en(and_2_out), .Q(f3), .clk(and_2_out), .clr(not_2_out));
  Register #(.width(32)) register_14 (.D(f4), .en(and_2_out), .Q(f5), .clk(and_2_out), .clr(not_2_out));
  Register #(.width(32)) register_15 (.D(f3), .en(and_2_out), .Q(f4), .clk(and_2_out), .clr(not_2_out));
  Multiplexer #(.width(8)) multiplexer_12 (
    .in0(register_10_q), .in1({8{1'b0}}), .out(multiplexer_12_out), .sel(comparator_3_eq));  // open: en
  Register #(.width(32)) register_16 (.D(f5), .en(and_2_out), .Q(f6), .clk(and_2_out), .clr(not_2_out));
  not not_3 (fall, comparator_4_eq);
  Comparator #(.width(32)) comparator_4 (.a(f14), .b({32{1'b0}}), .eq(comparator_4_eq));  // open: gt, lt
  Register #(.width(32)) register_17 (.D(f7), .en(and_2_out), .Q(f8), .clk(and_2_out), .clr(not_2_out));
  Register #(.width(32)) register_18 (.D(f6), .en(and_2_out), .Q(f7), .clk(and_2_out), .clr(not_2_out));
  Register #(.width(32)) register_19 (.D(f9), .en(and_2_out), .Q(f10), .clk(and_2_out), .clr(not_2_out));
  Register #(.width(32)) register_20 (.D(f8), .en(and_2_out), .Q(f9), .clk(and_2_out), .clr(not_2_out));
  Register #(.width(32)) register_21 (.D(f11), .en(and_2_out), .Q(f12), .clk(and_2_out), .clr(not_2_out));
  Register #(.width(32)) register_22 (.D(f10), .en(and_2_out), .Q(f11), .clk(and_2_out), .clr(not_2_out));
  Register #(.width(32)) register_23 (.D(f12), .en(and_2_out), .Q(f13), .clk(and_2_out), .clr(not_2_out));
  Register #(.width(32)) register_24 (.D(f13), .en(and_2_out), .Q(f14), .clk(and_2_out), .clr(not_2_out));
  Register #(.width(32)) register_25 (.D(f14), .en(and_2_out), .Q(f15), .clk(and_2_out), .clr(not_2_out));
  Register #(.width(32)) register_26 (.D(f15), .en(and_2_out), .clk(and_2_out), .clr(not_2_out));  // open: Q
endmodule

module fall (
  input  clock,
  input  fall,
  input  clean,
  input  [31:0] f15_in,
  input  [31:0] f14_in,
  input  [31:0] f13_in,
  input  [31:0] f12_in,
  input  [31:0] f11_in,
  input  [31:0] f10_in,
  input  [31:0] f9_in,
  input  [31:0] f8_in,
  input  [31:0] f7_in,
  input  [31:0] f6_in,
  output [31:0] d1,
  output [31:0] d2,
  output [31:0] d3,
  output [31:0] d4,
  output [31:0] d5,
  output [31:0] d6,
  output [31:0] d7,
  output [31:0] d8,
  output [31:0] d9,
  output [31:0] f1,
  output [31:0] f2,
  output [31:0] f3,
  output [31:0] f4,
  output [31:0] f5,
  output [31:0] f6,
  output [31:0] f7,
  output [31:0] f8,
  output [31:0] f9,
  output [31:0] f10,
  output [31:0] f11,
  output [31:0] f12,
  output [31:0] f13,
  output [31:0] f14,
  output [31:0] f15,
  output clean_2,
  output st_j
);

  wire and_1_out, and_2_out, and_3_out, comparator_1_eq, comparator_1_gt, comparator_2_eq, comparator_3_eq,
       comparator_4_eq, comparator_5_eq, multiplexer_1_out, not_1_out, not_2_out;
  wire [7:0] counter_1_q, multiplexer_12_out, register_9_q, subtractor_1_out;
  wire [31:0] counter_2_q, multiplexer_2_out, multiplexer_3_out, multiplexer_4_out, multiplexer_5_out,
       multiplexer_6_out, multiplexer_7_out, multiplexer_8_out, multiplexer_9_out, multiplexer_10_out,
       multiplexer_11_out, register_26_q;

  and and_1 (and_1_out, fall, and_3_out);
  not not_1 (not_1_out, fall);
  and and_2 (and_2_out, not_1_out, clean);
  Counter #(.max('h1f), .trigger("falling")) counter_1 (
    .Q(counter_1_q), .clk(clock), .clr(comparator_2_eq));  // open: load, D, count, carry
  Multiplexer multiplexer_1 (
    .in0(comparator_2_eq), .in1(comparator_5_eq), .out(multiplexer_1_out), .sel(clean_2));  // open: en
  and and_3 (and_3_out, comparator_2_eq, multiplexer_1_out);
  Counter #(.width(32), .max('hffffffff), .trigger("falling")) counter_2 (
    .Q(counter_2_q), .clk(and_1_out), .clr(and_2_out));  // open: load, D, count, carry
  Comparator #(.width(32)) comparator_1 (
    .a(counter_2_q), .b({32{1'b0}}), .gt(comparator_1_gt), .eq(comparator_1_eq));  // open: lt
  Comparator comparator_2 (.a(counter_1_q), .b(subtractor_1_out), .eq(comparator_2_eq));  // open: gt, lt
  Multiplexer #(.width(32)) multiplexer_2 (
    .in0({32{1'b0}}), .in1(f15_in), .out(multiplexer_2_out), .sel(comparator_1_eq));  // open: en
  not not_2 (not_2_out, comparator_1_gt);
  Register #(.width(32)) register_1 (.D(multiplexer_2_out), .en(and_3_out), .Q(d1), .clk(and_3_out));  // open: clr
  Multiplexer #(.width(32)) multiplexer_3 (
    .in0(d1), .in1(f14_in), .out(multiplexer_3_out), .sel(comparator_1_eq));  // open: en
  Register #(.width(32)) register_2 (.D(multiplexer_3_out), .en(and_3_out), .Q(d2), .clk(and_3_out));  // open: clr
  Register #(.width(32)) register_3 (.D(multiplexer_4_out), .en(and_3_out), .Q(d3), .clk(and_3_out));  // open: clr
  Multiplexer #(.width(32)) multiplexer_4 (
    .in0(d2), .in1(f13_in), .out(multiplexer_4_out), .sel(comparator_1_eq));  // open: en
  Register #(.width(32)) register_4 (.D(multiplexer_6_out), .en(and_3_out), .Q(d4), .clk(and_3_out));  // open: clr
  Register #(.width(32)) register_5 (.D(multiplexer_5_out), .en(and_3_out), .Q(d5), .clk(and_3_out));  // open: clr
  Multiplexer #(.width(32)) multiplexer_5 (
    .in0(d4), .in1(f11_in), .out(multiplexer_5_out), .sel(comparator_1_eq));  // open: en
  Multiplexer #(.width(32)) multiplexer_6 (
    .in0(d3), .in1(f12_in), .out(multiplexer_6_out), .sel(comparator_1_eq));  // open: en
  Register #(.width(32)) register_6 (.D(multiplexer_7_out), .en(and_3_out), .Q(d6), .clk(and_3_out));  // open: clr
  Multiplexer #(.width(32)) multiplexer_7 (
    .in0(d5), .in1(f10_in), .out(multiplexer_7_out), .sel(comparator_1_eq));  // open: en
  Subtractor subtractor_1 (.a(multiplexer_12_out), .b(8'h2), .out(subtractor_1_out));  // open: bin, bout
  Register #(.width(32)) register_7 (.D(multiplexer_9_out), .en(and_3_out), .Q(d8), .clk(and_3_out));  // open: clr
  Register #(.width(32)) register_8 (.D(multiplexer_8_out), .en(and_3_out), .Q(d7), .clk(and_3_out));  // open: clr
  Multiplexer #(.width(32)) multiplexer_8 (
    .in0(d6), .in1(f9_in), .out(multiplexer_8_out), .sel(comparator_1_eq));  // open: en
  Register register_9 (.D(subtractor_1_out), .en(and_3_out), .Q(register_9_q), .clk(and_3_out), .clr(and_2_out));
  Register #(.width(32)) register_10 (.D(multiplexer_10_out), .en(and_3_out), .Q(d9), .clk(and_3_out));  // open: clr
  Multiplexer #(.width(32)) multiplexer_9 (
    .in0(d7), .in1(f8_in), .out(multiplexer_9_out), .sel(comparator_1_eq));  // open: en
  Multiplexer #(.width(32)) multiplexer_10 (
    .in0(d8), .in1(f7_in), .out(multiplexer_10_out), .sel(comparator_1_eq));  // open: en
  Comparator comparator_3 (.a(register_9_q), .b({8{1'b0}}), .eq(comparator_3_eq));  // open: gt, lt
  Register #(.width(32)) register_11 (.D(f1), .en(and_3_out), .Q(f2), .clk(and_3_out), .clr(not_2_out));
  Register #(.width(32)) register_12 (.D(multiplexer_11_out), .en(and_3_out), .Q(f1), .clk(and_3_out));  // open: clr
  Register #(.width(32)) register_13 (.D(f2), .en(and_3_out), .Q(f3), .clk(and_3_out), .clr(not_2_out));
  Register #(.width(32)) register_14 (.D(f3), .en(and_3_out), .Q(f4), .clk(and_3_out), .clr(not_2_out));
  Multiplexer #(.width(32)) multiplexer_11 (
    .in0(d9), .in1(f6_in), .out(multiplexer_11_out), .sel(comparator_1_eq));  // open: en
  Multiplexer #(.width(8)) multiplexer_12 (
    .in0(register_9_q), .in1(8'h1e), .out(multiplexer_12_out), .sel(comparator_3_eq));  // open: en
  Register #(.width(32)) register_15 (.D(f4), .en(and_3_out), .Q(f5), .clk(and_3_out), .clr(not_2_out));
  Register #(.width(32)) register_16 (.D(f6), .en(and_3_out), .Q(f7), .clk(and_3_out), .clr(not_2_out));
  Register #(.width(32)) register_17 (.D(f5), .en(and_3_out), .Q(f6), .clk(and_3_out), .clr(not_2_out));
  Register #(.width(32)) register_18 (.D(f7), .en(and_3_out), .Q(f8), .clk(and_3_out), .clr(not_2_out));
  Register #(.width(32)) register_19 (.D(f9), .en(and_3_out), .Q(f10), .clk(and_3_out), .clr(not_2_out));
  Register #(.width(32)) register_20 (.D(f8), .en(and_3_out), .Q(f9), .clk(and_3_out), .clr(not_2_out));
  Comparator #(.width(32)) comparator_4 (.a(f15), .b({32{1'b0}}), .eq(comparator_4_eq));  // open: gt, lt
  not not_3 (st_j, comparator_4_eq);
  Register #(.width(32)) register_21 (.D(f11), .en(and_3_out), .Q(f12), .clk(and_3_out), .clr(not_2_out));
  Register #(.width(32)) register_22 (.D(f10), .en(and_3_out), .Q(f11), .clk(and_3_out), .clr(not_2_out));
  Register #(.width(32)) register_23 (.D(f12), .en(and_3_out), .Q(f13), .clk(and_3_out), .clr(not_2_out));
  not not_4 (clean_2, comparator_5_eq);
  Comparator #(.width(32)) comparator_5 (.a(register_26_q), .b({32{1'b0}}), .eq(comparator_5_eq));  // open: gt, lt
  Register #(.width(32)) register_24 (.D(f14), .en(and_3_out), .Q(f15), .clk(and_3_out), .clr(not_2_out));
  Register #(.width(32)) register_25 (.D(f13), .en(and_3_out), .Q(f14), .clk(and_3_out), .clr(not_2_out));
  Register #(.width(32)) register_26 (.D(f15), .en(and_3_out), .Q(register_26_q), .clk(and_3_out), .clr(not_2_out));
endmodule

module dino (
  input  stop,
  input  sit_down,
  input  jump,
  input  fall,
  input  choose,
  input  clock,
  input  [31:0] in_7,
  input  [31:0] in_8,
  input  [31:0] in_9,
  input  [31:0] in_10,
  input  [31:0] in_11,
  input  [31:0] in_12,
  input  [31:0] in_13,
  input  [31:0] in_14,
  input  [31:0] in_15,
  input  [31:0] in_16,
  input  [31:0] in_17,
  input  [31:0] in_18,
  input  [31:0] in_19,
  input  [31:0] in_20,
  input  [31:0] in_21,
  input  [31:0] in_22,
  input  [31:0] in_23,
  input  [31:0] in_24,
  input  [31:0] in_25,
  input  [31:0] in_26,
  input  [31:0] in_27,
  input  [31:0] in_28,
  input  [31:0] in_29,
  input  [31:0] in_30,
  output [31:0] out_31,
  output [31:0] out_32,
  output [31:0] out_33,
  output [31:0] out_34,
  output [31:0] out_35,
  output [31:0] out_36,
  output [31:0] out_37,
  output [31:0] out_38,
  output [31:0] out_39,
  output [31:0] out_40,
  output [31:0] out_41,
  output [31:0] out_42,
  output [31:0] out_43,
  output [31:0] out_44,
  output [31:0] out_45,
  output [31:0] out_46,
  output [31:0] out_47,
  output [31:0] out_48,
  output [31:0] out_49,
  output [31:0] out_50,
  output [31:0] out_51,
  output [31:0] out_52,
  output [31:0] out_53,
  output [31:0] out_54,
  output [31:0] out_55,
  output [31:0] out_56,
  output [31:0] out_57,
  output [31:0] out_58,
  output [31:0] out_59,
  output [31:0] out_60,
  output [31:0] out_61,
  output [31:0] out_62
);

  wire and_1_out, not_1_out, or_1_out;
  wire [31:0] multiplexer_3_out, multiplexer_6_out, multiplexer_7_out, multiplexer_8_out, multiplexer_9_out,
       multiplexer_10_out, multiplexer_13_out, multiplexer_14_out, multiplexer_15_out, multiplexer_16_out,
       multiplexer_19_out, multiplexer_20_out, multiplexer_21_out, multiplexer_24_out, multiplexer_25_out,
       multiplexer_26_out, multiplexer_29_out;

  Multiplexer #(.width(32)) multiplexer_1 (
    .in0(multiplexer_7_out), .in1({32{1'b0}}), .out(out_33), .sel(stop));  // open: en
  Multiplexer #(.width(32)) multiplexer_2 (
    .in0(multiplexer_6_out), .in1({32{1'b0}}), .out(out_34), .sel(stop));  // open: en
  and and_1 (and_1_out, sit_down, not_1_out);
  not not_1 (not_1_out, or_1_out);
  or or_1 (or_1_out, jump, fall);
  Multiplexer #(.width(32)) multiplexer_3 (
    .in0(32'hc800000), .in1(32'h5800000), .out(multiplexer_3_out), .sel(clock));  // open: en
  Multiplexer #(.width(32)) multiplexer_4 (
    .in0(multiplexer_13_out), .in1({32{1'b0}}), .out(out_35), .sel(stop));  // open: en
  Multiplexer #(.width(32)) multiplexer_5 (
    .in0(multiplexer_14_out), .in1({32{1'b0}}), .out(out_36), .sel(stop));  // open: en
  Multiplexer #(.width(32)) multiplexer_6 (
    .in0(multiplexer_8_out), .in1(multiplexer_8_out), .out(multiplexer_6_out), .sel(and_1_out));  // open: en
  Multiplexer #(.width(32)) multiplexer_7 (
    .in0(multiplexer_9_out), .in1(multiplexer_9_out), .out(multiplexer_7_out), .sel(and_1_out));  // open: en
  Multiplexer #(.width(32)) multiplexer_8 (
    .in0(multiplexer_10_out), .in1(in_8), .out(multiplexer_8_out), .sel(or_1_out));  // open: en
  Multiplexer #(.width(32)) multiplexer_9 (
    .in0(multiplexer_3_out), .in1(in_7), .out(multiplexer_9_out), .sel(or_1_out));  // open: en
  Multiplexer #(.width(32)) multiplexer_10 (
    .in0(32'h9800000), .in1(32'hd000000), .out(multiplexer_10_out), .sel(clock));  // open: en
  Multiplexer #(.width(32)) multiplexer_11 (
    .in0(multiplexer_19_out), .in1({32{1'b0}}), .out(out_37), .sel(stop));  // open: en
  Multiplexer #(.width(32)) multiplexer_12 (
    .in0(multiplexer_20_out), .in1({32{1'b0}}), .out(out_38), .sel(stop));  // open: en
  Multiplexer #(.width(32)) multiplexer_13 (
    .in0(in_9), .in1(multiplexer_16_out), .out(multiplexer_13_out), .sel(and_1_out));  // open: en
  Multiplexer #(.width(32)) multiplexer_14 (
    .in0(in_10), .in1(multiplexer_15_out), .out(multiplexer_14_out), .sel(and_1_out));  // open: en
  Multiplexer #(.width(32)) multiplexer_15 (
    .in0(32'h3fe00000), .in1({32{1'b0}}), .out(multiplexer_15_out), .sel(or_1_out));  // open: en
  Multiplexer #(.width(32)) multiplexer_16 (
    .in0(32'h1ff80000), .in1({32{1'b0}}), .out(multiplexer_16_out), .sel(or_1_out));  // open: en
  Multiplexer #(.width(32)) multiplexer_17 (
    .in0(multiplexer_24_out), .in1({32{1'b0}}), .out(out_39), .sel(stop));  // open: en
  Multiplexer #(.width(32)) multiplexer_18 (
    .in0(multiplexer_25_out), .in1({32{1'b0}}), .out(out_40), .sel(stop));  // open: en
  Multiplexer #(.width(32)) multiplexer_19 (
    .in0(in_11), .in1(multiplexer_21_out), .out(multiplexer_19_out), .sel(and_1_out));  // open: en
  Multiplexer #(.width(32)) multiplexer_20 (
    .in0(in_12), .in1(multiplexer_26_out), .out(multiplexer_20_out), .sel(and_1_out));  // open: en
  Multiplexer #(.width(32)) multiplexer_21 (
    .in0(32'h4f780000), .in1({32{1'b0}}), .out(multiplexer_21_out), .sel(or_1_out));  // open: en
  Multiplexer #(.width(32)) multiplexer_22 (
    .in0(multiplexer_29_out), .in1({32{1'b0}}), .out(out_41), .sel(stop));  // open: en
  Multiplexer #(.width(32)) multiplexer_23 (.in0(in_16), .in1({32{1'b0}}), .out(out_42), .sel(stop));  // open: en
  Multiplexer #(.width(32)) multiplexer_24 (
    .in0(in_13), .in1({32{1'b0}}), .out(multiplexer_24_out), .sel(and_1_out));  // open: en
  Multiplexer #(.width(32)) multiplexer_25 (
    .in0(in_14), .in1({32{1'b0}}), .out(multiplexer_25_out), .sel(and_1_out));  // open: en
  Multiplexer #(.width(32)) multiplexer_26 (
    .in0({32{1'b0}}), .in1({32{1'b0}}), .out(multiplexer_26_out), .sel(or_1_out));  // open: en
  Multiplexer #(.width(32)) multiplexer_27 (.in0(in_18), .in1({32{1'b0}}), .out(out_44), .sel(stop));  // open: en
  Multiplexer #(.width(32)) multiplexer_28 (.in0(in_17), .in1({32{1'b0}}), .out(out_43), .sel(stop));  // open: en
  Multiplexer #(.width(32)) multiplexer_29 (
    .in0(in_15), .in1({32{1'b0}}), .out(multiplexer_29_out), .sel(and_1_out));  // open: en
  Multiplexer #(.width(32)) multiplexer_30 (.in0(in_20), .in1({32{1'b0}}), .out(out_46), .sel(stop));  // open: en
  Multiplexer #(.width(32)) multiplexer_31 (.in0(in_19), .in1({32{1'b0}}), .out(out_45), .sel(stop));  // open: en
  Multiplexer #(.width(32)) multiplexer_32 (.in0(in_22), .in1({32{1'b0}}), .out(out_48), .sel(stop));  // open: en
  Multiplexer #(.width(32)) multiplexer_33 (.in0(in_21), .in1({32{1'b0}}), .out(out_47), .sel(stop));  // open: en
  Multiplexer #(.width(32)) multiplexer_34 (.in0(in_23), .in1({32{1'b0}}), .out(out_49), .sel(stop));  // open: en
  Multiplexer #(.width(32)) multiplexer_35 (.in0(in_24), .in1({32{1'b0}}), .out(out_50), .sel(stop));  // open: en
  Multiplexer #(.width(32)) multiplexer_36 (.in0(in_26), .in1({32{1'b0}}), .out(out_52), .sel(stop));  // open: en
  Multiplexer #(.width(32)) multiplexer_37 (.in0(in_25), .in1({32{1'b0}}), .out(out_51), .sel(stop));  // open: en
  Multiplexer #(.width(32)) multiplexer_38 (.in0(in_27), .in1({32{1'b0}}), .out(out_53), .sel(stop));  // open: en
  Multiplexer #(.width(32)) multiplexer_39 (.in0(in_28), .in1({32{1'b0}}), .out(out_54), .sel(stop));  // open: en
  Multiplexer #(.width(32)) multiplexer_40 (.in0(in_30), .in1({32{1'b0}}), .out(out_31), .sel(stop));  // open: en
  Multiplexer #(.width(32)) multiplexer_41 (.in0(in_29), .in1({32{1'b0}}), .out(out_55), .sel(stop));  // open: en
  Multiplexer #(.width(32)) multiplexer_42 (.in0({32{1'b0}}), .in1({32{1'b0}}), .out(out_32), .sel(stop));  // open: en
  Multiplexer #(.width(32)) multiplexer_43 (.in0({32{1'b0}}), .in1({32{1'b0}}), .out(out_56), .sel(stop));  // open: en
  Multiplexer #(.width(32)) multiplexer_44 (.in0({32{1'b0}}), .in1({32{1'b0}}), .out(out_57), .sel(stop));  // open: en
  Multiplexer #(.width(32)) multiplexer_45 (.in0({32{1'b0}}), .in1({32{1'b0}}), .out(out_58), .sel(stop));  // open: en
  Multiplexer #(.width(32)) multiplexer_46 (.in0({32{1'b0}}), .in1({32{1'b0}}), .out(out_60), .sel(stop));  // open: en
  Multiplexer #(.width(32)) multiplexer_47 (.in0({32{1'b0}}), .in1({32{1'b0}}), .out(out_59), .sel(stop));  // open: en
  Multiplexer #(.width(32)) multiplexer_48 (.in0({32{1'b0}}), .in1({32{1'b0}}), .out(out_62), .sel(stop));  // open: en
  Multiplexer #(.width(32)) multiplexer_49 (.in0({32{1'b0}}), .in1({32{1'b0}}), .out(out_61), .sel(stop));  // open: en

  // Other names for the same wires on the sheet: D1[31:0] = in_7; D2[31:0] = in_8; D3[31:0] = in_9; D4[31:0] = in_10;
  //   D5[31:0] = in_11; D6[31:0] = in_12; D7[31:0] = in_13; D8[31:0] = in_14; D9[31:0] = in_15; f1[31:0] = in_16;
  //   f2[31:0] = in_17; f3[31:0] = in_18; f4[31:0] = in_19; f5[31:0] = in_20; f6[31:0] = in_21; f7[31:0] = in_22;
  //   f8[31:0] = in_23; f9[31:0] = in_24; f10[31:0] = in_25; f11[31:0] = in_26; f12[31:0] = in_27; f13[31:0] = in_28;
  //   f14[31:0] = in_29; f15[31:0] = in_30
endmodule

module \счетчик  (
  input  clock,
  output [3:0] count4,
  output [3:0] count3,
  output [3:0] count2,
  output [3:0] count1
);

  wire and_1_out, and_2_out, comparator_1_eq, counter_2_carry, counter_3_carry, counter_4_carry;
  wire [4:0] counter_1_q;

  Counter #(.width(5), .max('h1f)) counter_1 (.Q(counter_1_q), .clk(clock));  // open: load, D, count, carry, clr
  Comparator #(.width(5)) comparator_1 (.a(counter_1_q), .b({5{1'b1}}), .eq(comparator_1_eq));  // open: gt, lt
  Counter #(.width(4), .max('h9)) counter_2 (
    .Q(count4), .carry(counter_2_carry), .clk(comparator_1_eq));  // open: load, D, count, clr
  Counter #(.width(4), .max('h9)) counter_3 (
    .count(counter_2_carry), .Q(count3), .carry(counter_3_carry), .clk(comparator_1_eq));  // open: load, D, clr
  Counter #(.width(4), .max('h9)) counter_4 (
    .count(and_1_out), .Q(count2), .carry(counter_4_carry), .clk(comparator_1_eq));  // open: load, D, clr
  and and_1 (and_1_out, counter_3_carry, counter_2_carry);
  Counter #(.width(4), .max('h9)) counter_5 (
    .count(and_2_out), .Q(count1), .clk(comparator_1_eq));  // open: load, D, carry, clr
  and and_2 (and_2_out, counter_4_carry, and_1_out);
endmodule

module \коллизии_кактусы  (
  input  [31:0] in_1,
  input  [31:0] in_2,
  input  [31:0] in_3,
  input  [31:0] in_4,
  input  [31:0] in_5,
  input  [31:0] in_6,
  input  [31:0] in_7,
  input  [31:0] in_8,
  input  [31:0] in_9,
  input  [31:0] in_10,
  input  [31:0] in_11,
  input  [31:0] in_12,
  input  [31:0] in_13,
  input  [31:0] in_14,
  input  [31:0] in_15,
  input  [31:0] in_16,
  input  [31:0] in_17,
  input  [31:0] in_18,
  input  [31:0] in_19,
  input  [31:0] in_20,
  input  [31:0] in_21,
  input  [31:0] in_22,
  input  [31:0] in_23,
  input  [31:0] in_24,
  input  [31:0] in_25,
  input  [31:0] in_26,
  input  [31:0] in_27,
  input  [31:0] in_28,
  input  [31:0] in_29,
  input  [31:0] in_30,
  input  [31:0] in_31,
  input  [31:0] in_32,
  input  [31:0] in_33,
  input  [31:0] in_34,
  input  [31:0] in_35,
  input  [31:0] in_36,
  input  [31:0] in_37,
  input  [31:0] in_38,
  input  [31:0] in_39,
  input  [31:0] in_40,
  input  [31:0] in_41,
  input  [31:0] in_42,
  input  [31:0] in_43,
  input  [31:0] in_44,
  input  [31:0] in_45,
  input  [31:0] in_46,
  input  [31:0] in_47,
  input  [31:0] in_48,
  input  [31:0] in_49,
  input  [31:0] in_50,
  input  [31:0] in_51,
  input  [31:0] in_52,
  input  [31:0] in_53,
  input  [31:0] in_54,
  input  [31:0] in_55,
  input  [31:0] in_56,
  input  [31:0] in_57,
  input  [31:0] in_58,
  input  [31:0] in_59,
  input  [31:0] in_60,
  input  [31:0] in_61,
  input  [31:0] in_62,
  input  [31:0] in_63,
  input  [31:0] in_64,
  output out_65,
  output out_66
);

  wire comparator_2_eq;
  wire [31:0] and_1_out, and_2_out, and_3_out, and_4_out, and_5_out, and_6_out, and_7_out, and_8_out,
       and_9_out, and_10_out, and_11_out, and_12_out, and_13_out, and_14_out, and_15_out, and_16_out,
       and_17_out, and_18_out, and_19_out, and_20_out, and_21_out, and_22_out, and_23_out, and_24_out,
       and_25_out, and_26_out, and_27_out, and_28_out, and_29_out, and_30_out, and_31_out, and_32_out,
       or_1_out;

  assign and_1_out = in_1 & in_2;  // AND_Gate and_1, 32 bits wide
  assign and_2_out = in_3 & in_4;  // AND_Gate and_2, 32 bits wide
  assign and_3_out = in_5 & in_6;  // AND_Gate and_3, 32 bits wide
  assign and_4_out = in_7 & in_8;  // AND_Gate and_4, 32 bits wide
  assign and_5_out = in_9 & in_10;  // AND_Gate and_5, 32 bits wide
  assign and_6_out = in_11 & in_12;  // AND_Gate and_6, 32 bits wide
  assign and_7_out = in_13 & in_14;  // AND_Gate and_7, 32 bits wide
  assign and_8_out = in_15 & in_16;  // AND_Gate and_8, 32 bits wide
  assign and_9_out = in_17 & in_18;  // AND_Gate and_9, 32 bits wide
  assign and_10_out = in_19 & in_20;  // AND_Gate and_10, 32 bits wide
  assign and_11_out = in_21 & in_22;  // AND_Gate and_11, 32 bits wide
  assign and_12_out = in_23 & in_24;  // AND_Gate and_12, 32 bits wide
  assign and_13_out = in_25 & in_26;  // AND_Gate and_13, 32 bits wide
  assign and_14_out = in_27 & in_28;  // AND_Gate and_14, 32 bits wide
  assign and_15_out = in_29 & in_30;  // AND_Gate and_15, 32 bits wide
  assign and_16_out = in_31 & in_32;  // AND_Gate and_16, 32 bits wide
  assign and_17_out = in_33 & in_34;  // AND_Gate and_17, 32 bits wide
  assign and_18_out = in_35 & in_36;  // AND_Gate and_18, 32 bits wide
  assign and_19_out = in_37 & in_38;  // AND_Gate and_19, 32 bits wide
  assign and_20_out = in_39 & in_40;  // AND_Gate and_20, 32 bits wide
  assign and_21_out = in_41 & in_42;  // AND_Gate and_21, 32 bits wide
  assign and_22_out = in_43 & in_44;  // AND_Gate and_22, 32 bits wide
  assign and_23_out = in_45 & in_46;  // AND_Gate and_23, 32 bits wide
  assign and_24_out = in_47 & in_48;  // AND_Gate and_24, 32 bits wide
  assign and_25_out = in_49 & in_50;  // AND_Gate and_25, 32 bits wide
  assign and_26_out = in_51 & in_52;  // AND_Gate and_26, 32 bits wide
  assign and_27_out = in_53 & in_54;  // AND_Gate and_27, 32 bits wide
  assign and_28_out = in_55 & in_56;  // AND_Gate and_28, 32 bits wide
  assign and_29_out = in_57 & in_58;  // AND_Gate and_29, 32 bits wide
  assign and_30_out = in_59 & in_60;  // AND_Gate and_30, 32 bits wide
  assign and_31_out = in_61 & in_62;  // AND_Gate and_31, 32 bits wide
  assign and_32_out = in_63 & in_64;  // AND_Gate and_32, 32 bits wide
  assign or_1_out = and_1_out | and_2_out | and_3_out | and_4_out | and_5_out | and_6_out | and_7_out | and_8_out | and_9_out | and_10_out | and_11_out | and_12_out | and_13_out | and_14_out | and_15_out | and_16_out | and_17_out | and_18_out | and_19_out | and_20_out | and_21_out | and_22_out | and_23_out | and_24_out | and_25_out | and_26_out | and_27_out | and_28_out | and_29_out | and_30_out | and_31_out | and_32_out;  // OR_Gate or_1, 32 bits wide
  Comparator #(.width(32)) comparator_1 (.a(and_29_out), .b({32{1'b0}}), .eq(out_66));  // open: gt, lt
  Comparator #(.width(32)) comparator_2 (.a(or_1_out), .b({32{1'b0}}), .eq(comparator_2_eq));  // open: gt, lt
  not not_1 (out_65, comparator_2_eq);
endmodule

module \коллизии_ямы  (
  input  [31:0] in_1,
  input  [31:0] in_2,
  output stop
);

  wire comparator_1_eq;
  wire [31:0] and_1_out;

  assign and_1_out = in_1 & in_2;  // AND_Gate and_1, 32 bits wide
  not not_1 (stop, comparator_1_eq);
  Comparator #(.width(32)) comparator_1 (.a(and_1_out), .b({32{1'b0}}), .eq(comparator_1_eq));  // open: gt, lt
endmodule
module \вверхняя_часть_карты  (
  input  clock,
  input  game_over,
  output [31:0] out_3,
  output [31:0] out_4,
  output [31:0] out_5,
  output [31:0] out_6,
  output [31:0] out_7,
  output [31:0] out_8,
  output [31:0] out_9,
  output [31:0] out_10,
  output [31:0] out_11,
  output [31:0] out_12,
  output [31:0] out_13,
  output [31:0] out_14,
  output [31:0] out_15,
  output [31:0] out_16,
  output [31:0] out_17
);

  wire and_1_out;
  wire [10:0] counter_1_q;
  wire [14:0] rom_1_data;

  Counter #(.width(11), .max('h7ff)) counter_1 (
    .count(1'b1), .Q(counter_1_q), .clk(and_1_out), .clr(game_over));  // open: load, D, carry
  and and_1 (and_1_out, clock, ~game_over);  // AND_Gate
  ROM #(.addrWidth(11), .dataWidth(15)) rom_1 (.addr(counter_1_q), .data(rom_1_data));  // open: sel
  DotMatrix #(.inputtype("row"), .matrixcols(32), .matrixrows(15)) dotmatrix_1 (
    .row0(out_3), .row1(out_4), .row2(out_5), .row3(out_6), .row4(out_7), .row5(out_8), .row6(out_9),
    .row7(out_10), .row8(out_11), .row9(out_12), .row10(out_13), .row11(out_14), .row12(out_15),
    .row13(out_16), .row14(out_17));
  \сдвиг_озу  \u_сдвиг_озу_1  (
    .in_1(rom_1_data[14]), .clock(and_1_out), .game_over(game_over), .out_5(out_3));  // open: out_4
  \сдвиг_озу  \u_сдвиг_озу_2  (
    .in_1(rom_1_data[13]), .clock(and_1_out), .game_over(game_over), .out_5(out_4));  // open: out_4
  \сдвиг_озу  \u_сдвиг_озу_3  (
    .in_1(rom_1_data[12]), .clock(and_1_out), .game_over(game_over), .out_5(out_5));  // open: out_4
  \сдвиг_озу  \u_сдвиг_озу_4  (
    .in_1(rom_1_data[11]), .clock(and_1_out), .game_over(game_over), .out_5(out_6));  // open: out_4
  \сдвиг_озу  \u_сдвиг_озу_5  (
    .in_1(rom_1_data[10]), .clock(and_1_out), .game_over(game_over), .out_5(out_7));  // open: out_4
  \сдвиг_озу  \u_сдвиг_озу_6  (
    .in_1(rom_1_data[9]), .clock(and_1_out), .game_over(game_over), .out_5(out_8));  // open: out_4
  \сдвиг_озу  \u_сдвиг_озу_7  (
    .in_1(rom_1_data[8]), .clock(and_1_out), .game_over(game_over), .out_5(out_9));  // open: out_4
  \сдвиг_озу  \u_сдвиг_озу_8  (
    .in_1(rom_1_data[7]), .clock(and_1_out), .game_over(game_over), .out_5(out_10));  // open: out_4
  \сдвиг_озу  \u_сдвиг_озу_9  (
    .in_1(rom_1_data[6]), .clock(and_1_out), .game_over(game_over), .out_5(out_11));  // open: out_4
  \сдвиг_озу  \u_сдвиг_озу_10  (
    .in_1(rom_1_data[5]), .clock(and_1_out), .game_over(game_over), .out_5(out_12));  // open: out_4
  \сдвиг_озу  \u_сдвиг_озу_11  (
    .in_1(rom_1_data[4]), .clock(and_1_out), .game_over(game_over), .out_5(out_13));  // open: out_4
  \сдвиг_озу  \u_сдвиг_озу_12  (
    .in_1(rom_1_data[3]), .clock(and_1_out), .game_over(game_over), .out_5(out_14));  // open: out_4
  \сдвиг_озу  \u_сдвиг_озу_13  (
    .in_1(rom_1_data[2]), .clock(and_1_out), .game_over(game_over), .out_5(out_15));  // open: out_4
  \сдвиг_озу  \u_сдвиг_озу_14  (
    .in_1(rom_1_data[1]), .clock(and_1_out), .game_over(game_over), .out_5(out_16));  // open: out_4
  \сдвиг_озу  \u_сдвиг_озу_15  (
    .in_1(rom_1_data[0]), .clock(and_1_out), .game_over(game_over), .out_5(out_17));  // open: out_4

  // Other names for the same wires on the sheet: _0[31:0] = out_17; _1[31:0] = out_16; _2[31:0] = out_15;
  //   _3[31:0] = out_14; _4[31:0] = out_13; _5[31:0] = out_12; _6[31:0] = out_11; _7[31:0] = out_10; _8[31:0] = out_9;
  //   _9[31:0] = out_8; _10[31:0] = out_7; _11[31:0] = out_6; _12[31:0] = out_5; _13[31:0] = out_4; _14[31:0] = out_3

  // Notes on the sheet:
  //   contents of rom_1 (hex, n*v repeats v):
  //   52*0 a a 1a 1e 4 c 1c 1e 3f 3f 37 5 4 4 4 583*0 4 c 14 3e 3 7f 1f f 7 5 5 4 583*0 4 c 14 3e 3 7f 1f
  //   f 7 5 5 4
endmodule

module \сдвиг_озу  (
  input  in_1,
  input  clock,
  input  game_over,
  output out_4,
  output [31:0] out_5
);

  Shift_Register #(.length(32)) shift_register_1 (
    .shift(1'b1), .in(in_1), .clk(clock), .out(out_4), .clr(game_over), .q0(out_5[0]), .q1(out_5[1]),
    .q2(out_5[2]), .q3(out_5[3]), .q4(out_5[4]), .q5(out_5[5]), .q6(out_5[6]), .q7(out_5[7]), .q8(out_5[8]),
    .q9(out_5[9]), .q10(out_5[10]), .q11(out_5[11]), .q12(out_5[12]), .q13(out_5[13]), .q14(out_5[14]),
    .q15(out_5[15]), .q16(out_5[16]), .q17(out_5[17]), .q18(out_5[18]), .q19(out_5[19]), .q20(out_5[20]),
    .q21(out_5[21]), .q22(out_5[22]), .q23(out_5[23]), .q24(out_5[24]), .q25(out_5[25]), .q26(out_5[26]),
    .q27(out_5[27]), .q28(out_5[28]), .q29(out_5[29]), .q30(out_5[30]), .q31(out_5[31]));  // open: load, d0, d1, d2, d3, d4, d5, d6, d7, d8, d9, d10, d11, d12, d13, d14, d15, d16, d17, d18, d19, d20, d21, d22, d23, d24, d25, d26, d27, d28, d29, d30, d31

  // Other names for the same wires on the sheet: _0 = out_5[0]; _1 = out_5[1]; _2 = out_5[2]; _3 = out_5[3];
  //   _4 = out_5[4]; _5 = out_5[5]; _6 = out_5[6]; _7 = out_5[7]; _8 = out_5[8]; _9 = out_5[9]; _10 = out_5[10];
  //   _11 = out_5[11]; _12 = out_5[12]; _13 = out_5[13]; _14 = out_5[14]; _15 = out_5[15]; _16 = out_5[16];
  //   _17 = out_5[17]; _18 = out_5[18]; _19 = out_5[19]; _20 = out_5[20]; _21 = out_5[21]; _22 = out_5[22];
  //   _23 = out_5[23]; _24 = out_5[24]; _25 = out_5[25]; _26 = out_5[26]; _27 = out_5[27]; _28 = out_5[28];
  //   _29 = out_5[29]; _30 = out_5[30]; _31 = out_5[31]
endmodule

module \нижняя_часть_карты  (
  input  clock,
  input  game_over,
  output [31:0] out_3,
  output [31:0] out_4,
  output [31:0] out_5,
  output [31:0] out_6,
  output [31:0] out_7,
  output [31:0] out_8,
  output [31:0] out_9,
  output [31:0] out_10,
  output [31:0] out_11,
  output [31:0] out_12
);

  wire and_1_out;
  wire [7:0] counter_1_q;
  wire [9:0] rom_1_data;

  Counter counter_1 (.count(1'b1), .Q(counter_1_q), .clk(and_1_out), .clr(game_over));  // open: load, D, carry
  and and_1 (and_1_out, clock, ~game_over);  // AND_Gate
  ROM #(.dataWidth(10)) rom_1 (.addr(counter_1_q), .data(rom_1_data));  // open: sel
  DotMatrix #(.inputtype("row"), .matrixcols(32), .matrixrows(10)) dotmatrix_1 (
    .row0(out_3), .row1(out_4), .row2(out_5), .row3(out_6), .row4(out_7), .row5(out_8), .row6(out_9),
    .row7(out_10), .row8(out_11), .row9(out_12));
  \сдвиг_озу  \u_сдвиг_озу_1  (
    .in_1(rom_1_data[9]), .clock(and_1_out), .game_over(game_over), .out_5(out_3));  // open: out_4
  \сдвиг_озу  \u_сдвиг_озу_2  (
    .in_1(rom_1_data[8]), .clock(and_1_out), .game_over(game_over), .out_5(out_4));  // open: out_4
  \сдвиг_озу  \u_сдвиг_озу_3  (
    .in_1(rom_1_data[7]), .clock(and_1_out), .game_over(game_over), .out_5(out_5));  // open: out_4
  \сдвиг_озу  \u_сдвиг_озу_4  (
    .in_1(rom_1_data[6]), .clock(and_1_out), .game_over(game_over), .out_5(out_6));  // open: out_4
  \сдвиг_озу  \u_сдвиг_озу_5  (
    .in_1(rom_1_data[5]), .clock(and_1_out), .game_over(game_over), .out_5(out_7));  // open: out_4
  \сдвиг_озу  \u_сдвиг_озу_6  (
    .in_1(rom_1_data[4]), .clock(and_1_out), .game_over(game_over), .out_5(out_8));  // open: out_4
  \сдвиг_озу  \u_сдвиг_озу_7  (
    .in_1(rom_1_data[3]), .clock(and_1_out), .game_over(game_over), .out_5(out_9));  // open: out_4
  \сдвиг_озу  \u_сдвиг_озу_8  (
    .in_1(rom_1_data[2]), .clock(and_1_out), .game_over(game_over), .out_5(out_10));  // open: out_4
  \сдвиг_озу  \u_сдвиг_озу_9  (
    .in_1(rom_1_data[1]), .clock(and_1_out), .game_over(game_over), .out_5(out_11));  // open: out_4
  \сдвиг_озу  \u_сдвиг_озу_10  (
    .in_1(rom_1_data[0]), .clock(and_1_out), .game_over(game_over), .out_5(out_12));  // open: out_4

  // Other names for the same wires on the sheet: _0[31:0] = out_12; _1[31:0] = out_11; _2[31:0] = out_10;
  //   _3[31:0] = out_9; _4[31:0] = out_8; _5[31:0] = out_7; _6[31:0] = out_6; _7[31:0] = out_5; _8[31:0] = out_4;
  //   _9[31:0] = out_3

  // Notes on the sheet:
  //   contents of rom_1 (hex, n*v repeats v):
  //   1c0 40 3f8 40 1c0 33*0 6*7 55*0 1c0 40 3f8 40 1c0 20 f8 20 60
endmodule

module \жизни  (
  input  [1:0] in_1,
  output [7:0] live1,
  output [7:0] live2,
  output [7:0] live3,
  output [7:0] live4,
  output [7:0] live5,
  output [7:0] live6,
  output [7:0] live7,
  output [7:0] live8,
  output [7:0] live9,
  output [7:0] live10,
  output [7:0] live11,
  output [7:0] live12,
  output [7:0] live13,
  output [7:0] live14,
  output [7:0] live15,
  output [7:0] live16,
  output [7:0] live17,
  output [7:0] live18,
  output [7:0] live19,
  output [7:0] live20,
  output [7:0] live21,
  output [7:0] live22,
  output [7:0] live23,
  output [7:0] live24,
  output [7:0] live25
);

  wire comparator_1_eq, comparator_2_gt, comparator_3_gt;

  Comparator #(.width(2), .mode("unsigned")) comparator_1 (.a(in_1), .b(2'b11), .eq(comparator_1_eq));  // open: gt, lt
  Comparator #(.width(2), .mode("unsigned")) comparator_2 (.a(in_1), .b(2'b01), .gt(comparator_2_gt));  // open: eq, lt
  Comparator #(.width(2), .mode("unsigned")) comparator_3 (.a(in_1), .b(2'b00), .gt(comparator_3_gt));  // open: eq, lt
  Multiplexer #(.width(8)) multiplexer_1 (
    .in0({8{1'b0}}), .in1(8'h78), .out(live3), .sel(comparator_1_eq));  // open: en
  Multiplexer #(.width(8)) multiplexer_2 (
    .in0({8{1'b0}}), .in1(8'h30), .out(live2), .sel(comparator_1_eq));  // open: en
  Multiplexer #(.width(8)) multiplexer_3 (
    .in0({8{1'b0}}), .in1(8'h3e), .out(live5), .sel(comparator_1_eq));  // open: en
  Multiplexer #(.width(8)) multiplexer_4 (
    .in0({8{1'b0}}), .in1(8'h7c), .out(live4), .sel(comparator_1_eq));  // open: en
  Multiplexer #(.width(8)) multiplexer_5 (
    .in0({8{1'b0}}), .in1(8'h30), .out(live10), .sel(comparator_2_gt));  // open: en
  Multiplexer #(.width(8)) multiplexer_6 (
    .in0({8{1'b0}}), .in1(8'h7c), .out(live12), .sel(comparator_2_gt));  // open: en
  Multiplexer #(.width(8)) multiplexer_7 (
    .in0({8{1'b0}}), .in1(8'h78), .out(live11), .sel(comparator_2_gt));  // open: en
  Multiplexer #(.width(8)) multiplexer_8 (
    .in0({8{1'b0}}), .in1(8'h3e), .out(live13), .sel(comparator_2_gt));  // open: en
  Multiplexer #(.width(8)) multiplexer_9 (
    .in0({8{1'b0}}), .in1(8'h30), .out(live18), .sel(comparator_3_gt));  // open: en
  Multiplexer #(.width(8)) multiplexer_10 (
    .in0({8{1'b0}}), .in1(8'h78), .out(live19), .sel(comparator_3_gt));  // open: en
  Multiplexer #(.width(8)) multiplexer_11 (
    .in0({8{1'b0}}), .in1(8'h3e), .out(live21), .sel(comparator_3_gt));  // open: en
  Multiplexer #(.width(8)) multiplexer_12 (
    .in0({8{1'b0}}), .in1(8'h7c), .out(live20), .sel(comparator_3_gt));  // open: en

  assign live1 = {8{1'b0}};
  assign live6 = live4;
  assign live7 = live3;
  assign live8 = live2;
  assign live9 = {8{1'b0}};
  assign live14 = live12;
  assign live15 = live11;
  assign live16 = live10;
  assign live17 = {8{1'b0}};
  assign live22 = live20;
  assign live23 = live19;
  assign live24 = live18;
  assign live25 = {8{1'b0}};
endmodule

module \подсчет_жизней  (
  input  clock_dino,
  input  stop1,
  input  stop2,
  input  rest,
  output [1:0] lcount,
  output game_over
);

  wire clock_1_out, comparator_1_eq, comparator_2_eq, comparator_3_eq, comparator_4_eq, or_1_out,
       register_1_q;
  wire [1:0] multiplexer_1_out, register_3_q;
  wire [7:0] counter_1_q;

  Clock clock_1 (.out(clock_1_out));
  or or_1 (or_1_out, stop1, stop2);
  Register #(.width(1)) register_1 (
    .D(or_1_out), .en(clock_dino), .Q(register_1_q), .clk(clock_dino), .clr(comparator_1_eq));
  Comparator #(.width(1)) comparator_1 (.a(register_1_q), .b(1'b1), .eq(comparator_1_eq));  // open: gt, lt
  Comparator #(.width(2)) comparator_2 (.a(lcount), .b(2'b00), .eq(comparator_2_eq));  // open: gt, lt
  Counter #(.max('h61)) counter_1 (
    .Q(counter_1_q), .clk(comparator_1_eq), .clr(comparator_3_eq));  // open: load, D, count, carry
  Comparator comparator_3 (.a(counter_1_q), .b(8'h60), .eq(comparator_3_eq));  // open: gt, lt
  Register #(.width(1)) register_2 (.D(comparator_2_eq), .en(1'b1), .Q(game_over), .clk(clock_dino), .clr(rest));
  Register #(.width(2)) register_3 (
    .D(multiplexer_1_out), .en(comparator_3_eq), .Q(register_3_q), .clk(comparator_3_eq), .clr(rest));
  Comparator #(.width(2)) comparator_4 (.a(register_3_q), .b(2'b00), .eq(comparator_4_eq));  // open: gt, lt
  Subtractor #(.width(2)) subtractor_1 (.a(register_3_q), .b(2'b01), .out(lcount));  // open: bin, bout
  Multiplexer #(.width(2)) multiplexer_1 (
    .in0(lcount), .in1(2'b11), .out(multiplexer_1_out), .sel(comparator_4_eq));  // open: en

  // Other names for the same wires on the sheet: clock = clock_dino
endmodule

module \game_over_фон  (
  input  clock,
  input  game_over,
  input  [31:0] in_3,
  input  [31:0] in_4,
  input  [31:0] in_5,
  input  [31:0] in_6,
  input  [31:0] in_7,
  input  [31:0] in_8,
  input  [31:0] in_9,
  input  [31:0] in_10,
  input  [31:0] in_11,
  input  [31:0] in_12,
  input  [31:0] in_13,
  input  [31:0] in_14,
  input  [31:0] in_15,
  input  [31:0] in_16,
  input  [31:0] in_17,
  input  [31:0] in_18,
  input  [31:0] in_19,
  input  [31:0] in_20,
  input  [31:0] in_21,
  input  [31:0] in_22,
  input  [31:0] in_23,
  input  [31:0] in_24,
  input  [31:0] in_25,
  input  [31:0] in_26,
  input  [31:0] in_27,
  input  [31:0] in_28,
  input  [31:0] in_29,
  input  [31:0] in_30,
  input  [31:0] in_31,
  input  [31:0] in_32,
  input  [31:0] in_33,
  input  [31:0] in_34,
  input  [31:0] in_35,
  input  [31:0] in_36,
  input  [31:0] in_37,
  output [31:0] out_38,
  output [31:0] out_39,
  output [31:0] out_40,
  output [31:0] out_41,
  output [31:0] out_42,
  output [31:0] out_43,
  output [31:0] out_44,
  output [31:0] out_45,
  output [31:0] out_46,
  output [31:0] out_47,
  output [31:0] out_48,
  output [31:0] out_49,
  output [31:0] out_50,
  output [31:0] out_51,
  output [31:0] out_52,
  output [31:0] out_53,
  output [31:0] out_54,
  output [31:0] out_55,
  output [31:0] out_56,
  output [31:0] out_57,
  output [31:0] out_58,
  output [31:0] out_59,
  output [31:0] out_60,
  output [31:0] out_61,
  output [31:0] out_62,
  output [31:0] out_63,
  output [31:0] out_64,
  output [31:0] out_65,
  output [31:0] out_66,
  output [31:0] out_67,
  output [31:0] out_68,
  output [31:0] out_69,
  output [31:0] out_70,
  output [31:0] out_71,
  output [31:0] out_72
);

  wire and_1_out, not_1_out;
  wire [31:0] _1, _2, _3, _4, _5, _6, _7, _8, _9, _10, _11, _12, _13, _14, _15;

  Multiplexer #(.width(32)) multiplexer_1 (.in0(in_3), .in1({32{1'b0}}), .out(out_38), .sel(game_over), .en(1'b1));
  Multiplexer #(.width(32)) multiplexer_2 (.in0(in_4), .in1({32{1'b0}}), .out(out_39), .sel(game_over), .en(1'b1));
  Multiplexer #(.width(32)) multiplexer_3 (.in0(in_5), .in1(_1), .out(out_40), .sel(game_over), .en(1'b1));
  Multiplexer #(.width(32)) multiplexer_4 (.in0(in_6), .in1(_2), .out(out_41), .sel(game_over), .en(1'b1));
  Multiplexer #(.width(32)) multiplexer_5 (.in0(in_7), .in1(_3), .out(out_42), .sel(game_over), .en(1'b1));
  Multiplexer #(.width(32)) multiplexer_6 (.in0(in_8), .in1(_4), .out(out_43), .sel(game_over), .en(1'b1));
  Multiplexer #(.width(32)) multiplexer_7 (.in0(in_9), .in1(_5), .out(out_44), .sel(game_over), .en(1'b1));
  Multiplexer #(.width(32)) multiplexer_8 (.in0(in_10), .in1(_6), .out(out_45), .sel(game_over), .en(1'b1));
  Multiplexer #(.width(32)) multiplexer_9 (.in0(in_11), .in1(_7), .out(out_46), .sel(game_over), .en(1'b1));
  Multiplexer #(.width(32)) multiplexer_10 (.in0(in_12), .in1({32{1'b0}}), .out(out_47), .sel(game_over), .en(1'b1));
  Multiplexer #(.width(32)) multiplexer_11 (.in0(in_13), .in1({32{1'b0}}), .out(out_48), .sel(game_over), .en(1'b1));
  Multiplexer #(.width(32)) multiplexer_12 (.in0(in_14), .in1({32{1'b0}}), .out(out_49), .sel(game_over), .en(1'b1));
  Multiplexer #(.width(32)) multiplexer_13 (.in0(in_15), .in1({32{1'b0}}), .out(out_50), .sel(game_over), .en(1'b1));
  Multiplexer #(.width(32)) multiplexer_14 (.in0(in_16), .in1({32{1'b0}}), .out(out_51), .sel(game_over), .en(1'b1));
  Multiplexer #(.width(32)) multiplexer_15 (.in0(in_17), .in1({32{1'b0}}), .out(out_52), .sel(game_over), .en(1'b1));
  Multiplexer #(.width(32)) multiplexer_16 (.in0(in_18), .in1({32{1'b0}}), .out(out_53), .sel(game_over), .en(1'b1));
  Multiplexer #(.width(32)) multiplexer_17 (.in0(in_19), .in1({32{1'b0}}), .out(out_54), .sel(game_over), .en(1'b1));
  Multiplexer #(.width(32)) multiplexer_18 (.in0(in_20), .in1({32{1'b0}}), .out(out_55), .sel(game_over), .en(1'b1));
  Multiplexer #(.width(32)) multiplexer_19 (.in0(in_21), .in1({32{1'b0}}), .out(out_56), .sel(game_over), .en(1'b1));
  Multiplexer #(.width(32)) multiplexer_20 (.in0(in_22), .in1({32{1'b0}}), .out(out_57), .sel(game_over), .en(1'b1));
  Multiplexer #(.width(32)) multiplexer_21 (.in0(in_23), .in1({32{1'b0}}), .out(out_58), .sel(game_over), .en(1'b1));
  Multiplexer #(.width(32)) multiplexer_22 (.in0(in_24), .in1({32{1'b0}}), .out(out_59), .sel(game_over), .en(1'b1));
  Multiplexer #(.width(32)) multiplexer_23 (.in0(in_25), .in1({32{1'b0}}), .out(out_60), .sel(game_over), .en(1'b1));
  Multiplexer #(.width(32)) multiplexer_24 (.in0(in_26), .in1({32{1'b0}}), .out(out_61), .sel(game_over), .en(1'b1));
  Multiplexer #(.width(32)) multiplexer_25 (.in0(in_27), .in1({32{1'b0}}), .out(out_62), .sel(game_over), .en(1'b1));
  Multiplexer #(.width(32)) multiplexer_26 (.in0(in_28), .in1({32{1'b0}}), .out(out_63), .sel(game_over), .en(1'b1));
  Multiplexer #(.width(32)) multiplexer_27 (.in0(in_29), .in1({32{1'b0}}), .out(out_64), .sel(game_over), .en(1'b1));
  Multiplexer #(.width(32)) multiplexer_28 (.in0(in_30), .in1({32{1'b0}}), .out(out_65), .sel(game_over), .en(1'b1));
  Multiplexer #(.width(32)) multiplexer_29 (.in0(in_31), .in1({32{1'b0}}), .out(out_66), .sel(game_over), .en(1'b1));
  Multiplexer #(.width(32)) multiplexer_30 (.in0(in_32), .in1({32{1'b0}}), .out(out_67), .sel(game_over), .en(1'b1));
  Multiplexer #(.width(32)) multiplexer_31 (.in0(in_33), .in1({32{1'b0}}), .out(out_68), .sel(game_over), .en(1'b1));
  Multiplexer #(.width(32)) multiplexer_32 (.in0(in_34), .in1({32{1'b0}}), .out(out_69), .sel(game_over), .en(1'b1));
  Multiplexer #(.width(32)) multiplexer_33 (.in0(in_35), .in1({32{1'b0}}), .out(out_70), .sel(game_over), .en(1'b1));
  Multiplexer #(.width(32)) multiplexer_34 (.in0(in_36), .in1({32{1'b0}}), .out(out_71), .sel(game_over), .en(1'b1));
  Multiplexer #(.width(32)) multiplexer_35 (.in0(in_37), .in1({32{1'b0}}), .out(out_72), .sel(game_over), .en(1'b1));
  and and_1 (and_1_out, clock, game_over);
  not not_1 (not_1_out, game_over);
  \game_over_надпись  \game_over_надпись_1  (
    .clock(and_1_out), .not_game_over(not_1_out), .out_3(_1), .out_4(_2), .out_5(_3), .out_6(_4), .out_7(_5),
    .out_8(_6), .out_9(_7), .out_10(_8), .out_11(_9), .out_12(_10), .out_13(_11), .out_14(_12), .out_15(_13),
    .out_16(_14), .out_17(_15));
endmodule

module \game_over_надпись  (
  input  clock,
  input  not_game_over,
  output [31:0] out_3,
  output [31:0] out_4,
  output [31:0] out_5,
  output [31:0] out_6,
  output [31:0] out_7,
  output [31:0] out_8,
  output [31:0] out_9,
  output [31:0] out_10,
  output [31:0] out_11,
  output [31:0] out_12,
  output [31:0] out_13,
  output [31:0] out_14,
  output [31:0] out_15,
  output [31:0] out_16,
  output [31:0] out_17
);

  wire [5:0] counter_1_q;
  wire [14:0] rom_1_data;

  Counter #(.width(6), .max('h3f)) counter_1 (
    .count(1'b1), .Q(counter_1_q), .clk(clock), .clr(not_game_over));  // open: load, D, carry
  ROM #(.addrWidth(6), .dataWidth(15)) rom_1 (.addr(counter_1_q), .data(rom_1_data));  // open: sel
  DotMatrix #(.inputtype("row"), .matrixcols(32), .matrixrows(15)) dotmatrix_1 (
    .row0(out_3), .row1(out_4), .row2(out_5), .row3(out_6), .row4(out_7), .row5(out_8), .row6(out_9),
    .row7(out_10), .row8(out_11), .row9(out_12), .row10(out_13), .row11(out_14), .row12(out_15),
    .row13(out_16), .row14(out_17));
  \сдвиг_озу  \u_сдвиг_озу_1  (
    .in_1(rom_1_data[14]), .clock(clock), .game_over(not_game_over), .out_5(out_3));  // open: out_4
  \сдвиг_озу  \u_сдвиг_озу_2  (
    .in_1(rom_1_data[13]), .clock(clock), .game_over(not_game_over), .out_5(out_4));  // open: out_4
  \сдвиг_озу  \u_сдвиг_озу_3  (
    .in_1(rom_1_data[12]), .clock(clock), .game_over(not_game_over), .out_5(out_5));  // open: out_4
  \сдвиг_озу  \u_сдвиг_озу_4  (
    .in_1(rom_1_data[11]), .clock(clock), .game_over(not_game_over), .out_5(out_6));  // open: out_4
  \сдвиг_озу  \u_сдвиг_озу_5  (
    .in_1(rom_1_data[10]), .clock(clock), .game_over(not_game_over), .out_5(out_7));  // open: out_4
  \сдвиг_озу  \u_сдвиг_озу_6  (
    .in_1(rom_1_data[9]), .clock(clock), .game_over(not_game_over), .out_5(out_8));  // open: out_4
  \сдвиг_озу  \u_сдвиг_озу_7  (
    .in_1(rom_1_data[8]), .clock(clock), .game_over(not_game_over), .out_5(out_9));  // open: out_4
  \сдвиг_озу  \u_сдвиг_озу_8  (
    .in_1(rom_1_data[7]), .clock(clock), .game_over(not_game_over), .out_5(out_10));  // open: out_4
  \сдвиг_озу  \u_сдвиг_озу_9  (
    .in_1(rom_1_data[6]), .clock(clock), .game_over(not_game_over), .out_5(out_11));  // open: out_4
  \сдвиг_озу  \u_сдвиг_озу_10  (
    .in_1(rom_1_data[5]), .clock(clock), .game_over(not_game_over), .out_5(out_12));  // open: out_4
  \сдвиг_озу  \u_сдвиг_озу_11  (
    .in_1(rom_1_data[4]), .clock(clock), .game_over(not_game_over), .out_5(out_13));  // open: out_4
  \сдвиг_озу  \u_сдвиг_озу_12  (
    .in_1(rom_1_data[3]), .clock(clock), .game_over(not_game_over), .out_5(out_14));  // open: out_4
  \сдвиг_озу  \u_сдвиг_озу_13  (
    .in_1(rom_1_data[2]), .clock(clock), .game_over(not_game_over), .out_5(out_15));  // open: out_4
  \сдвиг_озу  \u_сдвиг_озу_14  (
    .in_1(rom_1_data[1]), .clock(clock), .game_over(not_game_over), .out_5(out_16));  // open: out_4
  \сдвиг_озу  \u_сдвиг_озу_15  (
    .in_1(rom_1_data[0]), .clock(clock), .game_over(not_game_over), .out_5(out_17));  // open: out_4

  // Other names for the same wires on the sheet: _0[31:0] = out_17; _1[31:0] = out_16; _2[31:0] = out_15;
  //   _3[31:0] = out_14; _4[31:0] = out_13; _5[31:0] = out_12; _6[31:0] = out_11; _7[31:0] = out_10; _8[31:0] = out_9;
  //   _9[31:0] = out_8; _10[31:0] = out_7; _11[31:0] = out_6; _12[31:0] = out_5; _13[31:0] = out_4; _14[31:0] = out_3

  // Notes on the sheet:
  //   contents of rom_1 (hex, n*v repeats v):
  //   3e00 4100 4900 4900 2600 0 3f00 4800 4800 4800 3f00 0 7f00 2000 1f00 2000 7f00 0 7f00 4900 4900 4800
  //   6*0 3e00 4100 4100 4000 3e00 0 7c00 200 100 200 7c00 0 7f00 4900 4900 4900 0 7f00 5800 5400 7700
endmodule

module \удаление_препятствий  (
  input  clock,
  input  game_over,
  input  [31:0] in_3,
  input  [31:0] in_4,
  input  [31:0] in_5,
  input  [31:0] in_6,
  input  [31:0] in_7,
  input  [31:0] in_8,
  input  [31:0] in_9,
  input  [31:0] in_10,
  input  [31:0] in_11,
  input  [31:0] in_12,
  input  [31:0] in_13,
  input  [31:0] in_14,
  input  [31:0] in_15,
  input  [31:0] in_16,
  input  [31:0] in_17,
  input  [31:0] in_18,
  input  [31:0] in_19,
  input  [31:0] in_20,
  input  [31:0] in_21,
  input  [31:0] in_22,
  input  [31:0] in_23,
  input  [31:0] in_24,
  input  [31:0] in_25,
  input  [31:0] in_26,
  input  [31:0] in_27,
  input  [31:0] in_28,
  input  [31:0] in_29,
  input  [31:0] in_30,
  input  [31:0] in_31,
  input  [31:0] in_32,
  input  [31:0] in_33,
  input  [31:0] in_34,
  input  [31:0] in_35,
  input  [31:0] in_36,
  input  [31:0] in_37,
  output [31:0] out_38,
  output [31:0] out_39,
  output [31:0] out_40,
  output [31:0] out_41,
  output [31:0] out_42,
  output [31:0] out_43,
  output [31:0] out_44,
  output [31:0] out_45,
  output [31:0] out_46,
  output [31:0] out_47,
  output [31:0] out_48,
  output [31:0] out_49,
  output [31:0] out_50,
  output [31:0] out_51,
  output [31:0] out_52,
  output [31:0] out_53,
  output [31:0] out_54,
  output [31:0] out_55,
  output [31:0] out_56,
  output [31:0] out_57,
  output [31:0] out_58,
  output [31:0] out_59,
  output [31:0] out_60,
  output [31:0] out_61,
  output [31:0] out_62,
  output [31:0] out_63,
  output [31:0] out_64,
  output [31:0] out_65,
  output [31:0] out_66,
  output [31:0] out_67,
  output [31:0] out_68,
  output [31:0] out_69,
  output [31:0] out_70,
  output [31:0] out_71,
  output [31:0] out_72
);

  wire counter_1_carry, game_over_t, register_1_q, register_2_q;

  Register #(.width(1)) register_1 (
    .D(register_2_q), .Q(register_1_q), .clk(clock), .clr(counter_1_carry));  // open: en
  Register #(.width(1)) register_2 (.D(game_over), .Q(register_2_q), .clk(clock));  // open: en, clr
  Multiplexer #(.width(32)) multiplexer_1 (.in0(in_3), .in1({32{1'b0}}), .out(out_38), .sel(game_over_t), .en(1'b1));
  Multiplexer #(.width(32)) multiplexer_2 (.in0(in_4), .in1({32{1'b0}}), .out(out_39), .sel(game_over_t), .en(1'b1));
  Multiplexer #(.width(32)) multiplexer_3 (.in0(in_5), .in1({32{1'b0}}), .out(out_40), .sel(game_over_t), .en(1'b1));
  Multiplexer #(.width(32)) multiplexer_4 (.in0(in_6), .in1({32{1'b0}}), .out(out_41), .sel(game_over_t), .en(1'b1));
  Multiplexer #(.width(32)) multiplexer_5 (.in0(in_7), .in1({32{1'b0}}), .out(out_42), .sel(game_over_t), .en(1'b1));
  Multiplexer #(.width(32)) multiplexer_6 (.in0(in_8), .in1({32{1'b0}}), .out(out_43), .sel(game_over_t), .en(1'b1));
  Multiplexer #(.width(32)) multiplexer_7 (.in0(in_9), .in1({32{1'b0}}), .out(out_44), .sel(game_over_t), .en(1'b1));
  Multiplexer #(.width(32)) multiplexer_8 (.in0(in_10), .in1({32{1'b0}}), .out(out_45), .sel(game_over_t), .en(1'b1));
  Multiplexer #(.width(32)) multiplexer_9 (.in0(in_11), .in1({32{1'b0}}), .out(out_46), .sel(game_over_t), .en(1'b1));
  Multiplexer #(.width(32)) multiplexer_10 (.in0(in_12), .in1({32{1'b0}}), .out(out_47), .sel(game_over_t), .en(1'b1));
  Multiplexer #(.width(32)) multiplexer_11 (.in0(in_13), .in1({32{1'b0}}), .out(out_48), .sel(game_over_t), .en(1'b1));
  Multiplexer #(.width(32)) multiplexer_12 (.in0(in_14), .in1({32{1'b0}}), .out(out_49), .sel(game_over_t), .en(1'b1));
  Multiplexer #(.width(32)) multiplexer_13 (.in0(in_15), .in1({32{1'b0}}), .out(out_50), .sel(game_over_t), .en(1'b1));
  Multiplexer #(.width(32)) multiplexer_14 (.in0(in_16), .in1({32{1'b0}}), .out(out_51), .sel(game_over_t), .en(1'b1));
  Multiplexer #(.width(32)) multiplexer_15 (.in0(in_17), .in1({32{1'b0}}), .out(out_52), .sel(game_over_t), .en(1'b1));
  Multiplexer #(.width(32)) multiplexer_16 (.in0(in_18), .in1({32{1'b0}}), .out(out_53), .sel(game_over_t), .en(1'b1));
  Multiplexer #(.width(32)) multiplexer_17 (.in0(in_19), .in1({32{1'b0}}), .out(out_54), .sel(game_over_t), .en(1'b1));
  Multiplexer #(.width(32)) multiplexer_18 (.in0(in_20), .in1({32{1'b0}}), .out(out_55), .sel(game_over_t), .en(1'b1));
  Multiplexer #(.width(32)) multiplexer_19 (.in0(in_21), .in1({32{1'b0}}), .out(out_56), .sel(game_over_t), .en(1'b1));
  Multiplexer #(.width(32)) multiplexer_20 (.in0(in_22), .in1({32{1'b0}}), .out(out_57), .sel(game_over_t), .en(1'b1));
  Multiplexer #(.width(32)) multiplexer_21 (.in0(in_23), .in1({32{1'b0}}), .out(out_58), .sel(game_over_t), .en(1'b1));
  Multiplexer #(.width(32)) multiplexer_22 (.in0(in_24), .in1({32{1'b0}}), .out(out_59), .sel(game_over_t), .en(1'b1));
  Multiplexer #(.width(32)) multiplexer_23 (.in0(in_25), .in1({32{1'b0}}), .out(out_60), .sel(game_over_t), .en(1'b1));
  Multiplexer #(.width(32)) multiplexer_24 (.in0(in_26), .in1({32{1'b0}}), .out(out_61), .sel(game_over_t), .en(1'b1));
  Multiplexer #(.width(32)) multiplexer_25 (.in0(in_27), .in1({32{1'b0}}), .out(out_62), .sel(game_over_t), .en(1'b1));
  Multiplexer #(.width(32)) multiplexer_26 (.in0(in_28), .in1({32{1'b0}}), .out(out_63), .sel(game_over_t), .en(1'b1));
  Multiplexer #(.width(32)) multiplexer_27 (.in0(in_29), .in1({32{1'b0}}), .out(out_64), .sel(game_over_t), .en(1'b1));
  Multiplexer #(.width(32)) multiplexer_28 (.in0(in_30), .in1({32{1'b0}}), .out(out_65), .sel(game_over_t), .en(1'b1));
  Multiplexer #(.width(32)) multiplexer_29 (.in0(in_31), .in1({32{1'b0}}), .out(out_66), .sel(game_over_t), .en(1'b1));
  Multiplexer #(.width(32)) multiplexer_30 (.in0(in_32), .in1({32{1'b0}}), .out(out_67), .sel(game_over_t), .en(1'b1));
  Multiplexer #(.width(32)) multiplexer_31 (.in0(in_33), .in1({32{1'b0}}), .out(out_68), .sel(game_over_t), .en(1'b1));
  Multiplexer #(.width(32)) multiplexer_32 (.in0(in_34), .in1({32{1'b0}}), .out(out_69), .sel(game_over_t), .en(1'b1));
  Multiplexer #(.width(32)) multiplexer_33 (.in0(in_35), .in1({32{1'b0}}), .out(out_70), .sel(game_over_t), .en(1'b1));
  Multiplexer #(.width(32)) multiplexer_34 (.in0(in_36), .in1({32{1'b0}}), .out(out_71), .sel(game_over_t), .en(1'b1));
  Multiplexer #(.width(32)) multiplexer_35 (.in0(in_37), .in1({32{1'b0}}), .out(out_72), .sel(game_over_t), .en(1'b1));
  S_R_Flip_Flop s_r_ff_1 (
    .clk(clock), .Q(game_over_t), .preset(register_1_q), .reset(counter_1_carry), .en(1'b1));  // open: S, R, Qn
  Counter #(.max('h9)) counter_1 (
    .count(game_over_t), .carry(counter_1_carry), .clk(clock), .clr(counter_1_carry));  // open: load, D, Q

  // Other names for the same wires on the sheet: strop = game_over
endmodule

module cdm_8 (
  input  IRQ,
  input  [2:0] vector,
  input  [7:0] in_3,
  input  [7:0] in_4,
  input  [7:0] in_5,
  input  [7:0] in_6,
  input  in_7,
  input  in_8,
  output lAck,
  output in_out,
  output [3:0] I_Oadr,
  output I_Osel,
  output [7:0] I_Odat
);

  wire and_1_out, and_4_out, cdm_8_mark5_1_p5, cdm_8_mark5_1_p6, cdm_8_mark5_1_p8, cdm_8_mark5_1_p9,
       cdm_8_mark5_1_p10, cdm_8_mark5_1_p11, cdm_8_mark5_1_p12, cdm_8_mark5_1_p13, clock, clock_1_out,
       clock_2, code, comparator_2_eq, counter_1_carry, counter_clock, data, data_2, keyboard_1_avail, ld,
       mem, name, not_1_out, not_3_out, not_5_out, player, str;
  wire [1:0] counter_2_q;
  wire [6:0] keyboard_1_data;
  wire [7:0] adder_1_out, addr_2, bit_extender_1_out, cdm_8_mark5_1_p17, cdm_8_mark5_1_p18, counter,
       counter_1_q, d_2, multiplexer_2_out, register_1_q;
  wire [7:4] addr_1;

  Keyboard keyboard_1 (.clk(clock_1_out), .re(1'b1), .avail(keyboard_1_avail), .data(keyboard_1_data));  // open: clr
  Clock clock_1 (.out(clock_1_out));
  Clock u_clock_2 (.out(clock));
  // Probe on cdm_8_mark5_1_p5
  // Probe on cdm_8_mark5_1_p6
  // Probe on cdm_8_mark5_1_p8
  // Probe on cdm_8_mark5_1_p9
  and and_1 (and_1_out, clock, ~clock_2);  // AND_Gate
  or or_1 (data_2, clock_2, data);
  // Probe on cdm_8_mark5_1_p10
  // Probe on cdm_8_mark5_1_p11
  // Probe on cdm_8_mark5_1_p12
  // CdM_8_mark5 cdm_8_mark5_1: pin names not known; wires that end beside it: clock_2, IRQ, vector, lAck, cdm_8_mark5_1_p5, cdm_8_mark5_1_p6, and_1_out, cdm_8_mark5_1_p8, cdm_8_mark5_1_p9, cdm_8_mark5_1_p10, cdm_8_mark5_1_p11, cdm_8_mark5_1_p12, cdm_8_mark5_1_p13, mem, in_out, {addr_1, I_Oadr}, cdm_8_mark5_1_p17, cdm_8_mark5_1_p18
  D_Flip_Flop d_ff_1 (.clk(clock_1_out), .D(1'b1));  // open: Q, Qn, preset, en, reset
  Decoder decoder_1 (.out0(code), .out1(data), .sel(cdm_8_mark5_1_p13), .en(mem));
  assign I_Odat = not_1_out ? cdm_8_mark5_1_p17 : 8'bz;  // Controlled_Buffer controlled_buffer_1
  not not_1 (not_1_out, in_out);
  assign cdm_8_mark5_1_p18 = in_out ? I_Odat : 8'bz;  // Controlled_Buffer controlled_buffer_2
  Counter #(.max('hd)) counter_1 (
    .count(1'b1), .Q(counter_1_q), .carry(counter_1_carry), .clk(counter_clock));  // open: load, D, clr
  not not_2 (player, counter_1_carry);
  and and_2 (ld, ~clock_2, in_out);  // AND_Gate
  Pull_Resistor pull_resistor_1 (.node(code));
  Pull_Resistor pull_resistor_2 (.node(data));
  and and_3 (I_Osel, and_4_out, clock, data);
  Adder adder_1 (.a({8{1'b0}}), .b(counter_1_q), .out(adder_1_out));  // open: cin, cout
  and and_4 (and_4_out, addr_1[4], addr_1[5], addr_1[6], addr_1[7]);
  or or_2 (str, clock_2, not_3_out);
  not not_3 (not_3_out, in_out);
  Comparator comparator_1 (.a(8'h9), .b(counter_1_q), .gt(name));  // open: eq, lt
  ROM rom_1 (.addr({addr_1, I_Oadr}), .data(I_Odat), .sel(code));
  RAM #(.bus("separate")) ram_1 (
    .addr(addr_2), .din(d_2), .data(I_Odat), .str(str), .sel(data_2), .clk(clock), .ld(ld));  // open: clr
  Multiplexer #(.width(8)) multiplexer_1 (
    .in0({addr_1, I_Oadr}), .in1(adder_1_out), .out(addr_2), .sel(clock_2), .en(1'b1));
  assign bit_extender_1_out = {{1{keyboard_1_data[6]}}, keyboard_1_data};  // Bit_Extender bit_extender_1
  not not_4 (counter_clock, comparator_2_eq);
  Comparator #(.width(7)) comparator_2 (.a(keyboard_1_data), .b({7{1'b0}}), .eq(comparator_2_eq));  // open: gt, lt
  Register register_1 (.D(bit_extender_1_out), .en(in_7), .Q(register_1_q), .clk(counter_clock));  // open: clr
  ROM rom_2 ();  // open: addr, data, sel
  Counter #(.width(2), .max('h3), .ongoal("stay")) counter_2 (
    .count(not_5_out), .Q(counter_2_q), .clk(counter_clock));  // open: load, D, carry, clr
  not not_5 (not_5_out, name);
  Multiplexer #(.width(8)) multiplexer_2 (
    .in0(counter), .in1(register_1_q), .out(multiplexer_2_out), .sel(name), .en(1'b1));
  Multiplexer #(.select(2), .width(8)) multiplexer_3 (
    .in0(in_3), .in1(in_4), .in2(in_5), .in3(in_6), .out(counter), .sel(counter_2_q), .en(1'b1));
  and and_5 (clock_2, in_8, player);
  Multiplexer #(.width(8)) multiplexer_4 (.in0(I_Odat), .in1(multiplexer_2_out), .out(d_2), .sel(clock_2), .en(1'b1));

  // Other names for the same wires on the sheet: addr_1[3:0] = I_Oadr; d_1[7:0] = I_Odat; rd_wr = in_out

  // Notes on the sheet:
  //   contents of rom_1 (hex, n*v repeats v):
  //   d0 b4 c0 d6 28 d1 d8 d0 f0 b0 74 e0 16 d2 f4 19 c1 d6 9f c5 ee 7 d0 e4 d1 f0 b5 d2 c a0 e0 27 b3 a7
  //   8c 8d 8a ee 1d d4 c9 1 b5 b5 d0 e4 b0 71 ed 36 ee 7f ee 7e 71 e1 7c d0 e5 b0 c9 1 b5 8d b5 71 ed 48
  //   ee 7f ee 7a 71 e1 78 c9 1 b5 d0 2 11 b5 d0 e6 b0 71 ed 5c ee 7f ee 76 71 e1 74 c9 1 b5 d0 3 11 b5 d0
  //   e7 b0 71 ed 70 ee 7f ee 72 ee 86 ee 76 ee 86 ee 7a ee 86 ee 7e ee 86 d7 c8 1 b0 d1 f0 a4 d7 c9 1 b5
  //   d0 cc 74 e1 97 d1 f0 d0 d8 a4 cc 1 ee 9d d0 c 11 c1 d6 28 c4 d7 c8 1 b0 d2 c 1 19 d2 c a e0 b2 b3 a7
  //   8c 8d 8a ee a8 d7
  //   contents of rom_2 (hex, n*v repeats v):
  //   d0 b4 c0 d6 28 d1 d8 d0 f0 b0 74 e0 16 d2 f4 19 c1 d6 9f c5 ee 7 d0 e4 d1 f0 b5 d2 c a0 e0 27 b3 a7
  //   8c 8d 8a ee 1d d4 c9 1 b5 b5 d0 e4 b0 71 ed 36 ee 7f ee 7e 71 e1 7c d0 e5 b0 c9 1 b5 8d b5 71 ed 48
  //   ee 7f ee 7a 71 e1 78 c9 1 b5 d0 2 11 b5 d0 e6 b0 71 ed 5c ee 7f ee 76 71 e1 74 c9 1 b5 d0 3 11 b5 d0
  //   e7 b0 71 ed 70 ee 7f ee 72 ee 86 ee 76 ee 86 ee 7a ee 86 ee 7e ee 86 d7 c8 1 b0 d1 f0 a4 d7 c9 1 b5
  //   d0 cc 74 e1 97 d1 f0 d0 d8 a4 cc 1 ee 9d d0 c 11 c1 d6 28 c4 d7 c8 1 b0 d2 c 1 19 d2 c a e0 b2 b3 a7
  //   8c 8d 8a ee a8 d7
endmodule

module \дино_выбор  (
  input  choose,
  output [31:0] d1,
  output [31:0] d2,
  output [31:0] d3,
  output [31:0] d4,
  output [31:0] d5,
  output [31:0] d6,
  output [31:0] d7,
  output [31:0] d8,
  output [31:0] d9
);

  Multiplexer #(.width(32)) multiplexer_1 (.in0(32'hd800000), .in1(32'hc800000), .out(d1), .sel(choose));  // open: en
  Multiplexer #(.width(32)) multiplexer_2 (.in0(32'h9000000), .in1(32'h49800000), .out(d2), .sel(choose));  // open: en
  Multiplexer #(.width(32)) multiplexer_3 (.in0(32'hf000000), .in1(32'h2f000000), .out(d3), .sel(choose));  // open: en
  Multiplexer #(.width(32)) multiplexer_4 (.in0(32'h1f400000), .in1(32'h1f000000), .out(d4), .sel(choose));  // open: en
  Multiplexer #(.width(32)) multiplexer_5 (.in0(32'h2fc00000), .in1(32'h3000000), .out(d5), .sel(choose));  // open: en
  Multiplexer #(.width(32)) multiplexer_6 (.in0(32'h47000000), .in1(32'h7c00000), .out(d6), .sel(choose));  // open: en
  Multiplexer #(.width(32)) multiplexer_7 (.in0(32'h3c00000), .in1(32'h7000000), .out(d7), .sel(choose));  // open: en
  Multiplexer #(.width(32)) multiplexer_8 (.in0(32'h3000000), .in1(32'h6c00000), .out(d8), .sel(choose));  // open: en
  Multiplexer #(.width(32)) multiplexer_9 (.in0(32'h3c00000), .in1(32'h3800000), .out(d9), .sel(choose));  // open: en
endmodule

module write_memory (
  input  [7:0] in_1,
  input  in_2,
  input  [15:0] top1,
  input  [15:0] top2,
  input  [15:0] top3,
  input  [15:0] recent,
  output [7:0] out_7
);

  wire addrptr, and_1_out, defineByte1, defineByte2, defineByte3, defineByteRct, demultiplexer_1_out5,
       demultiplexer_1_out7, demultiplexer_1_out9, demultiplexer_1_out11, enable1, enable2, enable3,
       enablerct, recentptr, top1ptr, top2ptr, top3ptr;
  wire [7:0] bitselector_1_out, bitselector_2_out, bitselector_3_out, bitselector_4_out, register_1_q,
       register_2_q, register_3_q, register_4_q;

  Demultiplexer #(.select(4), .enable("false")) demultiplexer_1 (
    .out4(defineByte1), .out5(demultiplexer_1_out5), .out6(defineByte2), .out7(demultiplexer_1_out7),
    .out8(defineByte3), .out9(demultiplexer_1_out9), .out10(defineByteRct), .out11(demultiplexer_1_out11),
    .in(1'b1), .sel(in_1[3:0]));  // open: out0, out1, out2, out3, out12, out13, out14, out15
  or or_1 (top1ptr, defineByte1, demultiplexer_1_out5);
  and and_1 (and_1_out, in_1[7], in_1[6], in_1[5], in_1[4]);
  and and_2 (addrptr, and_1_out, in_2);
  or or_2 (top2ptr, defineByte2, demultiplexer_1_out7);
  or or_3 (top3ptr, defineByte3, demultiplexer_1_out9);
  or or_4 (recentptr, defineByteRct, demultiplexer_1_out11);
  and and_3 (enable1, top1ptr, in_2);
  and and_4 (enable2, top2ptr, in_2);
  BitSelector #(.width(16), .group(8)) bitselector_1 (.in(top1), .out(bitselector_1_out), .sel(defineByte1));
  BitSelector #(.width(16), .group(8)) bitselector_2 (.in(top2), .out(bitselector_2_out), .sel(defineByte2));
  BitSelector #(.width(16), .group(8)) bitselector_3 (.in(top3), .out(bitselector_3_out), .sel(defineByte3));
  BitSelector #(.width(16), .group(8)) bitselector_4 (.in(recent), .out(bitselector_4_out), .sel(defineByteRct));
  Register register_1 (.D(bitselector_1_out), .Q(register_1_q), .clk(enable1));  // open: en, clr
  assign out_7 = enable1 ? register_1_q : 8'bz;  // Controlled_Buffer controlled_buffer_1
  assign out_7 = enable2 ? register_2_q : 8'bz;  // Controlled_Buffer controlled_buffer_2
  Register register_2 (.D(bitselector_2_out), .Q(register_2_q), .clk(enable2));  // open: en, clr
  Register register_3 (.D(bitselector_3_out), .Q(register_3_q), .clk(enable3));  // open: en, clr
  assign out_7 = enable3 ? register_3_q : 8'bz;  // Controlled_Buffer controlled_buffer_3
  assign out_7 = enablerct ? register_4_q : 8'bz;  // Controlled_Buffer controlled_buffer_4
  Register register_4 (.D(bitselector_4_out), .Q(register_4_q), .clk(enablerct));  // open: en, clr
  and and_5 (enable3, top3ptr, in_2);
  and and_6 (enablerct, recentptr, in_2);

  // Other names for the same wires on the sheet: address[7:0] = in_1; write = in_2
endmodule

module HexDec (
  input  [15:0] in_1,
  output [3:0] num0,
  output [3:0] num1,
  output [3:0] num2,
  output [3:0] num3,
  output [3:0] num4
);

  wire [15:0] divider_1_out, divider_1_rem, divider_2_out, divider_2_rem, divider_3_out, divider_3_rem,
       divider_4_out, divider_4_rem, divider_5_rem;

  Divider #(.width(16)) divider_1 (.a(in_1), .b(16'ha), .out(divider_1_out), .rem(divider_1_rem));  // open: upper
  Divider #(.width(16)) divider_2 (
    .a(divider_1_out), .b(16'ha), .out(divider_2_out), .rem(divider_2_rem));  // open: upper
  Bit_Extender #(.in_width(16), .out_width(4)) bit_extender_1 (.in(divider_1_rem), .out(num0));
  Divider #(.width(16)) divider_3 (
    .a(divider_2_out), .b(16'ha), .out(divider_3_out), .rem(divider_3_rem));  // open: upper
  Bit_Extender #(.in_width(16), .out_width(4)) bit_extender_2 (.in(divider_2_rem), .out(num1));
  Divider #(.width(16)) divider_4 (
    .a(divider_3_out), .b(16'ha), .out(divider_4_out), .rem(divider_4_rem));  // open: upper
  Bit_Extender #(.in_width(16), .out_width(4)) bit_extender_3 (.in(divider_3_rem), .out(num2));
  Divider #(.width(16)) divider_5 (.a(divider_4_out), .b(16'ha), .rem(divider_5_rem));  // open: out, upper
  Bit_Extender #(.in_width(16), .out_width(4)) bit_extender_4 (.in(divider_4_rem), .out(num3));
  Bit_Extender #(.in_width(16), .out_width(4)) bit_extender_5 (.in(divider_5_rem), .out(num4));
endmodule

module \лидеры  (
  input  [7:0] in_1,
  input  [7:0] in_2,
  input  in_3,
  output [15:0] out_4,
  output [3:0] out_5,
  output [3:0] out_6,
  output [3:0] out_7,
  output [3:0] out_8,
  output [3:0] out_9,
  output [15:0] out_10,
  output [3:0] out_11,
  output [3:0] out_12,
  output [3:0] out_13,
  output [3:0] out_14,
  output [3:0] out_15,
  output [15:0] out_16,
  output [3:0] out_17,
  output [3:0] out_18,
  output [3:0] out_19,
  output [3:0] out_20,
  output [3:0] out_21
);

  wire addrptr, and_1_out, enable1_0, enable1_1, enable2_0, enable2_1, enable3_0, enable3_1;
  wire [7:0] multiplexer_1_out, multiplexer_2_out, multiplexer_3_out, multiplexer_4_out, multiplexer_5_out,
       multiplexer_6_out, score1_0, score1_1, score2_0, score2_1, score3_0, score3_1;
  wire [15:0] adder_1_out, adder_2_out, adder_3_out, register_1_q, register_2_q, register_3_q, register_4_q,
       register_5_q, register_6_q, register_7_q, register_8_q, register_9_q, register_10_q, register_11_q,
       register_12_q, score1_0ext, score1_1ext, score2_0ext, score2_1ext, score3_0ext, score3_1ext,
       shifter_1_out, shifter_2_out, shifter_3_out, shifter_4_out, shifter_5_out, shifter_6_out;

  and and_1 (and_1_out, in_2[4], in_2[5], in_2[6], in_2[7]);
  and and_2 (addrptr, in_3, and_1_out);
  Demultiplexer #(.select(4), .width(8)) demultiplexer_1 (
    .out4(score1_0), .out5(score1_1), .out6(score2_0), .out7(score2_1), .out8(score3_0), .out9(score3_1),
    .in(in_1), .sel(in_2[3:0]), .en(in_3));  // open: out0, out1, out2, out3, out10, out11, out12, out13, out14, out15
  Demultiplexer #(.select(4)) demultiplexer_2 (
    .out4(enable1_0), .out5(enable1_1), .out6(enable2_0), .out7(enable2_1), .out8(enable3_0),
    .out9(enable3_1), .in(1'b1), .sel(in_2[3:0]), .en(in_3));  // open: out0, out1, out2, out3, out10, out11, out12, out13, out14, out15
  // Probe on score1_0
  // Probe on score1_1
  // Probe on score2_0
  // Probe on score2_1
  // Probe on score3_0
  // Probe on score3_1
  Multiplexer #(.width(8), .enable("false")) multiplexer_1 (
    .in0({8{1'b0}}), .in1(score1_0), .out(multiplexer_1_out), .sel(enable1_0));
  assign score1_0ext = {{8{1'b0}}, multiplexer_1_out};  // Bit_Extender bit_extender_1
  Multiplexer #(.width(8), .enable("false")) multiplexer_2 (
    .in0({8{1'b0}}), .in1(score1_1), .out(multiplexer_2_out), .sel(enable1_1));
  assign score1_1ext = {{8{1'b0}}, multiplexer_2_out};  // Bit_Extender bit_extender_2
  assign score2_0ext = {{8{1'b0}}, multiplexer_3_out};  // Bit_Extender bit_extender_3
  Multiplexer #(.width(8), .enable("false")) multiplexer_3 (
    .in0({8{1'b0}}), .in1(score2_0), .out(multiplexer_3_out), .sel(enable2_0));
  assign score2_1ext = {{8{1'b0}}, multiplexer_4_out};  // Bit_Extender bit_extender_4
  Multiplexer #(.width(8), .enable("false")) multiplexer_4 (
    .in0({8{1'b0}}), .in1(score2_1), .out(multiplexer_4_out), .sel(enable2_1));
  assign score3_0ext = {{8{1'b0}}, multiplexer_5_out};  // Bit_Extender bit_extender_5
  Multiplexer #(.width(8), .enable("false")) multiplexer_5 (
    .in0({8{1'b0}}), .in1(score3_0), .out(multiplexer_5_out), .sel(enable3_0));
  assign score3_1ext = {{8{1'b0}}, multiplexer_6_out};  // Bit_Extender bit_extender_6
  Multiplexer #(.width(8), .enable("false")) multiplexer_6 (
    .in0({8{1'b0}}), .in1(score3_1), .out(multiplexer_6_out), .sel(enable3_1));
  Shifter #(.width(16)) shifter_1 (.in(score1_0ext), .\dist (4'b0111), .out(shifter_1_out));
  Shifter #(.width(16)) shifter_2 (.in(score2_0ext), .\dist (4'b0111), .out(shifter_2_out));
  Shifter #(.width(16)) shifter_3 (.in(score3_0ext), .\dist (4'b0111), .out(shifter_3_out));
  Register #(.width(16), .trigger("high")) register_1 (
    .D(shifter_1_out), .Q(register_1_q), .clk(enable1_0));  // open: en, clr
  Adder #(.width(16)) adder_1 (.a(register_1_q), .b(register_2_q), .out(adder_1_out));  // open: cin, cout
  Register #(.width(16), .trigger("high")) register_2 (
    .D(score1_1ext), .Q(register_2_q), .clk(enable1_1));  // open: en, clr
  Register #(.width(16), .trigger("high")) register_3 (
    .D(shifter_2_out), .Q(register_3_q), .clk(enable2_0));  // open: en, clr
  Adder #(.width(16)) adder_2 (.a(register_3_q), .b(register_4_q), .out(adder_2_out));  // open: cin, cout
  Register #(.width(16), .trigger("high")) register_4 (
    .D(score2_1ext), .Q(register_4_q), .clk(enable2_1));  // open: en, clr
  Register #(.width(16), .trigger("high")) register_5 (
    .D(shifter_3_out), .Q(register_5_q), .clk(enable3_0));  // open: en, clr
  Adder #(.width(16)) adder_3 (.a(register_5_q), .b(register_6_q), .out(adder_3_out));  // open: cin, cout
  Register #(.width(16), .trigger("high")) register_6 (
    .D(score3_1ext), .Q(register_6_q), .clk(enable3_1));  // open: en, clr
  HexDec hexdec_1 (.in_1(adder_1_out), .num0(out_5), .num1(out_6), .num2(out_7), .num3(out_8), .num4(out_9));
  HexDec hexdec_2 (.in_1(adder_2_out), .num0(out_11), .num1(out_12), .num2(out_13), .num3(out_14), .num4(out_15));
  HexDec hexdec_3 (.in_1(adder_3_out), .num0(out_17), .num1(out_18), .num2(out_19), .num3(out_20), .num4(out_21));
  Shifter #(.width(16)) shifter_4 (.in(score1_0ext), .\dist (4'b1000), .out(shifter_4_out));
  Shifter #(.width(16)) shifter_5 (.in(score2_0ext), .\dist (4'b1000), .out(shifter_5_out));
  Shifter #(.width(16)) shifter_6 (.in(score3_0ext), .\dist (4'b1000), .out(shifter_6_out));
  Register #(.width(16), .trigger("high")) register_7 (
    .D(shifter_4_out), .Q(register_7_q), .clk(enable1_0));  // open: en, clr
  Register #(.width(16), .trigger("high")) register_8 (
    .D(score1_1ext), .Q(register_8_q), .clk(enable1_1));  // open: en, clr
  Register #(.width(16), .trigger("high")) register_9 (
    .D(shifter_5_out), .Q(register_9_q), .clk(enable2_0));  // open: en, clr
  Register #(.width(16), .trigger("high")) register_10 (
    .D(score2_1ext), .Q(register_10_q), .clk(enable2_1));  // open: en, clr
  Register #(.width(16), .trigger("high")) register_11 (
    .D(shifter_6_out), .Q(register_11_q), .clk(enable3_0));  // open: en, clr
  Register #(.width(16), .trigger("high")) register_12 (
    .D(score3_1ext), .Q(register_12_q), .clk(enable3_1));  // open: en, clr
  Adder #(.width(16)) adder_4 (.a(register_7_q), .b(register_8_q), .out(out_4));  // open: cin, cout
  Adder #(.width(16)) adder_5 (.a(register_9_q), .b(register_10_q), .out(out_10));  // open: cin, cout
  Adder #(.width(16)) adder_6 (.a(register_11_q), .b(register_12_q), .out(out_16));  // open: cin, cout

  // Other names for the same wires on the sheet: address[7:0] = in_2; read = in_3; score[7:0] = in_1
endmodule

module \лидеры_cdm_8  (
  input  [13:0] recent_result,
  input  losesignal,
  input  tact,
  output [3:0] out_4,
  output [3:0] out_5,
  output [3:0] out_6,
  output [3:0] out_7,
  output [3:0] out_8,
  output [3:0] out_9,
  output [3:0] out_10,
  output [3:0] out_11,
  output [3:0] out_12,
  output [3:0] out_13,
  output [3:0] out_14,
  output [3:0] out_15,
  output [3:0] out_16,
  output [3:0] out_17,
  output [3:0] out_18,
  output [3:0] out_19,
  output [3:0] out_20,
  output [3:0] out_21,
  output [3:0] out_22,
  output [3:0] out_23
);

  wire and_2_out, and_3_out, cdm_8_mark5_1_p1, cdm_8_mark5_1_p3, cdm_8_mark5_1_p4, cdm_8_mark5_1_p6,
       cdm_8_mark5_1_p7, cdm_8_mark5_1_p9, cdm_8_mark5_1_p10, cdm_8_mark5_1_p11, cdm_8_mark5_1_p12, Cl,
       decoder_2_out0, decoder_2_out1, I_Osel, not_1_out, not_2_out, or_1_out, read, read_write, seloutput,
       write;
  wire [3:0] addr1hex, I_Oaddress;
  wire [7:0] cdm_8_mark5_1_p15, cdm_8_mark5_1_p16, controlled_buffer_4_out, I_Odata, \output , PCanchor,
       write_memory_1_out_7;
  wire [15:0] bit_extender_1_out, bit_extender_2_out, bit_extender_3_out, rct16, shifter_1_out,
       \лидеры_1_out_4 , \лидеры_1_out_10 , \лидеры_1_out_16 ;

  // Probe on cdm_8_mark5_1_p3
  // Probe on cdm_8_mark5_1_p6
  // Probe on cdm_8_mark5_1_p4
  and and_1 (I_Osel, seloutput, decoder_2_out1);
  // Probe on cdm_8_mark5_1_p7
  // Probe on PCanchor
  // Probe on cdm_8_mark5_1_p10
  // Probe on cdm_8_mark5_1_p9
  // CdM_8_mark5 cdm_8_mark5_1: pin names not known; wires that end beside it: cdm_8_mark5_1_p1, cdm_8_mark5_1_p1, cdm_8_mark5_1_p3, cdm_8_mark5_1_p4, Cl, cdm_8_mark5_1_p6, cdm_8_mark5_1_p7, PCanchor, cdm_8_mark5_1_p9, cdm_8_mark5_1_p10, cdm_8_mark5_1_p11, cdm_8_mark5_1_p12, read_write, {addr1hex, I_Oaddress}, cdm_8_mark5_1_p15, cdm_8_mark5_1_p16
  Decoder decoder_1 (.out0(read), .out1(write), .sel(read_write), .en(I_Osel));
  Pull_Resistor pull_resistor_1 (.node(read));
  Pull_Resistor pull_resistor_2 (.node(write));
  Decoder decoder_2 (.out0(decoder_2_out0), .out1(decoder_2_out1), .sel(cdm_8_mark5_1_p11), .en(cdm_8_mark5_1_p12));
  not not_1 (not_1_out, read_write);
  assign I_Odata = not_1_out ? cdm_8_mark5_1_p15 : 8'bz;  // Controlled_Buffer controlled_buffer_1
  assign cdm_8_mark5_1_p16 = read_write ? I_Odata : 8'bz;  // Controlled_Buffer controlled_buffer_2
  Demultiplexer #(.select(4), .enable("false")) demultiplexer_1 (
    .out15(seloutput), .in(1'b1), .sel(addr1hex));  // open: out0, out1, out2, out3, out4, out5, out6, out7, out8, out9, out10, out11, out12, out13, out14
  assign bit_extender_1_out = {{8{1'b0}}, {1'b0, recent_result[6:0]}};  // Bit_Extender bit_extender_1
  assign bit_extender_2_out = {{8{1'b0}}, {1'b0, recent_result[13:7]}};  // Bit_Extender bit_extender_2
  Shifter #(.width(16)) shifter_1 (.in(bit_extender_2_out), .\dist (4'b1000), .out(shifter_1_out));
  assign Cl = or_1_out ? tact : 1'bz;  // Controlled_Buffer controlled_buffer_3
  Adder #(.width(16)) adder_1 (.a(bit_extender_1_out), .b(shifter_1_out), .out(rct16));  // open: cin, cout
  and and_2 (and_2_out, decoder_2_out1, I_Osel);
  or or_1 (or_1_out, ~and_3_out, losesignal);  // OR_Gate
  not not_2 (not_2_out, Cl);
  and and_3 (and_3_out, PCanchor[0], ~PCanchor[1], ~PCanchor[2], ~PCanchor[3], ~PCanchor[4], ~PCanchor[5], ~PCanchor[6], ~PCanchor[7]);  // AND_Gate
  ROM rom_1 (.addr({addr1hex, I_Oaddress}), .data(I_Odata), .sel(decoder_2_out0));
  RAM #(.bus("separate")) ram_1 (
    .addr({addr1hex, I_Oaddress}), .din(\output ), .data(I_Odata), .str(write), .sel(and_2_out),
    .clk(not_2_out), .ld(read_write));  // open: clr
  assign bit_extender_3_out = {{2{1'b0}}, recent_result};  // Bit_Extender bit_extender_3
  // Probe on {addr1hex, I_Oaddress}
  // Probe on I_Odata
  assign controlled_buffer_4_out = read ? I_Odata : 8'bz;  // Controlled_Buffer controlled_buffer_4
  // Probe on out_4
  // Probe on out_5
  // Probe on out_9
  // Probe on out_10
  // Probe on out_15
  // Probe on out_14
  HexDec hexdec_1 (
    .in_1(bit_extender_3_out), .num0(out_19), .num1(out_20), .num2(out_21), .num3(out_22), .num4(out_23));
  // Probe on out_6
  // Probe on out_11
  // Probe on out_16
  \лидеры  \u_лидеры_1  (
    .in_1(controlled_buffer_4_out), .in_2({addr1hex, I_Oaddress}), .in_3(read), .out_4(\лидеры_1_out_4 ),
    .out_10(\лидеры_1_out_10 ), .out_16(\лидеры_1_out_16 ), .out_5(out_4), .out_11(out_9), .out_17(out_14),
    .out_6(out_5), .out_12(out_10), .out_18(out_15), .out_7(out_6), .out_13(out_11), .out_19(out_16),
    .out_8(out_7), .out_14(out_12), .out_20(out_17), .out_9(out_8), .out_15(out_13), .out_21(out_18));
  // Probe on out_7
  // Probe on out_8
  // Probe on out_12
  // Probe on out_13
  // Probe on out_18
  // Probe on out_17
  assign \output  = write ? write_memory_1_out_7 : 8'bz;  // Controlled_Buffer controlled_buffer_5
  write_memory write_memory_1 (
    .in_1({addr1hex, I_Oaddress}), .in_2(write), .top1(\лидеры_1_out_4 ), .top2(\лидеры_1_out_10 ),
    .top3(\лидеры_1_out_16 ), .recent(rct16), .out_7(write_memory_1_out_7));

  // Other names for the same wires on the sheet: rct14[13:0] = recent_result; I_Oaddress[7:4] = addr1hex;
  //   sendrct = losesignal

  // Notes on the sheet:
  //   contents of rom_1 (hex, n*v repeats v):
  //   c3 c7 d0 fa b0 a0 d0 fb b0 a0 d0 f4 b0 a0 d0 f5 b0 a0 d0 f6 b0 a0 d0 f7 b0 a0 d0 f8 b0 a0 d0 f9 b0
  //   a0 d6 24 c7 d0 f4 b0 d2 f5 ba d1 fa b5 71 e5 35 d6 a1 ee 4f 71 e1 4d d1 fb b5 79 e5 42 d6 a1 ee 4b
  //   79 e1 49 d6 1 ee 4b d6 4f ee 4f d6 4f c7 d0 f6 b0 d2 f7 ba d1 fa b5 71 e5 60 d6 c8 ee 7a 71 e1 78 d1
  //   fb b5 79 e5 6d d6 c8 ee 76 79 e1 74 d6 1 ee 76 d6 7a ee 7a d6 7a c7 d0 f8 b0 d2 f9 ba d1 fa b5 71 e5
  //   8b d6 e3 ee a1 71 e1 9f d1 fb b5 79 e5 98 d6 e3 ee 9d 79 e1 9d d6 1 ee a1 d6 1 c7 d0 f6 b0 d1 f8 a4
  //   d0 f7 b0 d1 f9 a4 d0 f4 b0 d1 f6 a4 d0 f5 b0 d1 f7 a4 d0 fa b0 d1 f4 a4 d0 fb b0 d1 f5 a4 d6 1 c7 d0
  //   f6 b0 d1 f8 a4 d0 f7 b0 d1 f9 a4 d0 fa b0 d1 f6 a4 d0 fb b0 d1 f7 a4 d6 1 c7 d0 fa b0 d1 f8 a4 d0 fb
  //   b0 d1 f9 a4 d6 1 d6 1
endmodule

module \клавиатура  (
  input  [6:0] sumbol,
  input  start,
  input  [3:0] count_3,
  input  [3:0] count_4,
  output clock,
  output [1:0] lcount,
  output [31:0] _1,
  output out_8,
  output out_9,
  output out_10,
  output out_11,
  output [31:0] _2,
  output [31:0] _3,
  output [31:0] out_14,
  output [31:0] out_15,
  output [31:0] out_16,
  output [31:0] out_17,
  output [31:0] out_18,
  output [31:0] out_19,
  output [31:0] out_20,
  output [31:0] out_21,
  output [31:0] out_22,
  output [31:0] out_23,
  output [31:0] out_24,
  output [31:0] out_25,
  output [31:0] out_26,
  output [31:0] out_27,
  output [31:0] out_28,
  output [31:0] out_29,
  output [31:0] out_30,
  output [31:0] out_31,
  output [31:0] out_32,
  output [31:0] out_33,
  output [31:0] out_34,
  output [31:0] out_35,
  output [31:0] out_36,
  output [31:0] out_37,
  output [31:0] out_38,
  output [31:0] out_39,
  output [31:0] out_40,
  output [31:0] out_41,
  output [31:0] out_42,
  output [31:0] out_43,
  output [31:0] out_44,
  output [31:0] _1_2,
  output [31:0] _35,
  output [31:0] out_47,
  output [31:0] out_48,
  output [31:0] out_49,
  output [31:0] out_50,
  output [31:0] out_51,
  output [31:0] out_52,
  output [31:0] out_53,
  output [31:0] out_54,
  output [31:0] out_55,
  output [31:0] out_56,
  output [31:0] out_57,
  output [31:0] out_58,
  output [31:0] out_59,
  output [31:0] out_60,
  output [31:0] out_61,
  output [31:0] out_62,
  output [31:0] out_63,
  output [31:0] out_64,
  output [31:0] out_65,
  output [31:0] out_66,
  output [31:0] out_67,
  output [31:0] out_68,
  output [31:0] out_69,
  output [31:0] out_70,
  output [31:0] out_71,
  output [31:0] out_72,
  output [31:0] out_73,
  output [31:0] out_74,
  output [31:0] out_75,
  output [31:0] out_76,
  output [31:0] out_77,
  output [31:0] out_78,
  output [31:0] out_79,
  output [31:0] out_80,
  output [31:0] out_81,
  output [31:0] out_82,
  output [31:0] out_83,
  output [31:0] out_84,
  output [31:0] out_85,
  output [31:0] out_86,
  output [31:0] out_87,
  output [31:0] out_88,
  output [31:0] out_89,
  output [31:0] out_90,
  output [31:0] out_91,
  output [31:0] out_92,
  output [31:0] out_93,
  output [31:0] out_94,
  output [31:0] out_95,
  output [31:0] out_96,
  output [31:0] out_97,
  output [31:0] out_98,
  output [31:0] out_99,
  output [31:0] out_100,
  output [31:0] out_101,
  output [31:0] out_102,
  output [31:0] out_103,
  output [31:0] out_104,
  output [31:0] out_105,
  output [31:0] out_106,
  output [31:0] out_107,
  output [31:0] out_108,
  output [31:0] out_109,
  output [31:0] out_110,
  output [31:0] out_111,
  output [31:0] out_112,
  output [31:0] out_113,
  output [31:0] out_114,
  output [31:0] out_115
);

  wire and_2_out, and_4_out, choose, clear, clear_rest, clock_3, clock_t, comparator_1_eq, comparator_2_eq,
       comparator_3_eq, comparator_4_eq, comparator_5_eq, comparator_6_eq, comparator_7_eq, comparator_8_eq,
       counter_3_carry, d_ff_1_q, jump, jump_out, or_1_out, or_2_out, sit_down, stop1, stop2,
       \или32_1_out_98 , \подсчет_жизней_1_game_over ;
  wire [4:0] counter_2_q, vec_adr;
  wire [7:0] counter_1_q;
  wire [13:0] c;
  wire [31:0] \вверхняя_часть_карты_1_out_3 , \вверхняя_часть_карты_1_out_4 , \вверхняя_часть_карты_1_out_5 ,
       \вверхняя_часть_карты_1_out_6 , \вверхняя_часть_карты_1_out_7 , \вверхняя_часть_карты_1_out_8 ,
       \вверхняя_часть_карты_1_out_9 , \вверхняя_часть_карты_1_out_10 , \вверхняя_часть_карты_1_out_11 ,
       \вверхняя_часть_карты_1_out_12 , \вверхняя_часть_карты_1_out_13 , \вверхняя_часть_карты_1_out_14 ,
       \вверхняя_часть_карты_1_out_15 , \вверхняя_часть_карты_1_out_16 , \вверхняя_часть_карты_1_out_17 ,
       \дино_1_out_6 , \дино_1_out_7 , \дино_1_out_8 , \дино_1_out_9 , \дино_1_out_10 , \дино_1_out_11 ,
       \дино_1_out_12 , \дино_1_out_13 , \дино_1_out_14 , \дино_1_out_15 , \дино_1_out_16 , \дино_1_out_17 ,
       \дино_1_out_18 , \дино_1_out_20 , \дино_1_out_21 , \дино_1_out_22 , \дино_1_out_23 , \дино_1_out_24 ,
       \дино_1_out_25 , \дино_1_out_26 , \дино_1_out_27 , \дино_1_out_28 , \дино_1_out_29 , \дино_1_out_30 ,
       \дино_1_out_31 , \дино_1_out_32 , \дино_1_out_33 , \дино_1_out_34 , \дино_1_out_35 , \дино_1_out_36 ,
       \дино_1_out_37 , \дино_1_out_38 , \нижняя_часть_карты_1_out_3 , \нижняя_часть_карты_1_out_4 ,
       \нижняя_часть_карты_1_out_5 , \нижняя_часть_карты_1_out_6 , \нижняя_часть_карты_1_out_7 ,
       \нижняя_часть_карты_1_out_8 , \нижняя_часть_карты_1_out_9 , \нижняя_часть_карты_1_out_10 ,
       \нижняя_часть_карты_1_out_11 , \нижняя_часть_карты_1_out_12 , \сдвиг_карты_2_out_43 ,
       \сдвиг_карты_2_out_44 , \сдвиг_карты_2_out_45 , \сдвиг_карты_2_out_46 , \сдвиг_карты_2_out_47 ,
       \сдвиг_карты_2_out_48 , \сдвиг_карты_2_out_49 , \сдвиг_карты_2_out_50 , \сдвиг_карты_2_out_51 ,
       \сдвиг_карты_2_out_52 , \сдвиг_карты_2_out_53 , \сдвиг_карты_2_out_54 , \сдвиг_карты_2_out_55 ,
       \сдвиг_карты_2_out_56 , \сдвиг_карты_2_out_57 , \сдвиг_карты_2_out_58 , \сдвиг_карты_2_out_59 ,
       \сдвиг_карты_2_out_60 , \сдвиг_карты_2_out_61 , \сдвиг_карты_2_out_62 , \сдвиг_карты_2_out_63 ,
       \сдвиг_карты_2_out_64 , \сдвиг_карты_2_out_65 , \сдвиг_карты_2_out_66 , \сдвиг_карты_2_out_67 ,
       \сдвиг_карты_2_out_68 , \сдвиг_карты_2_out_69 , \сдвиг_карты_2_out_70 , \сдвиг_карты_2_out_71 ,
       \сдвиг_карты_2_out_72 , \сдвиг_карты_2_out_73 , \сдвиг_карты_2_out_74 , \сдвиг_карты_2_out_75 ,
       \сдвиг_карты_2_out_76 , \сдвиг_карты_2_out_77 , \удаление_препятствий_1_out_38 ,
       \удаление_препятствий_1_out_39 , \удаление_препятствий_1_out_40 , \удаление_препятствий_1_out_41 ,
       \удаление_препятствий_1_out_42 , \удаление_препятствий_1_out_43 , \удаление_препятствий_1_out_44 ,
       \удаление_препятствий_1_out_45 , \удаление_препятствий_1_out_46 , \удаление_препятствий_1_out_47 ,
       \удаление_препятствий_1_out_48 , \удаление_препятствий_1_out_49 , \удаление_препятствий_1_out_50 ,
       \удаление_препятствий_1_out_51 , \удаление_препятствий_1_out_52 , \удаление_препятствий_1_out_53 ,
       \удаление_препятствий_1_out_54 , \удаление_препятствий_1_out_55 , \удаление_препятствий_1_out_56 ,
       \удаление_препятствий_1_out_57 , \удаление_препятствий_1_out_58 , \удаление_препятствий_1_out_59 ,
       \удаление_препятствий_1_out_60 , \удаление_препятствий_1_out_61 , \удаление_препятствий_1_out_62 ,
       \удаление_препятствий_1_out_63 , \удаление_препятствий_1_out_64 , \удаление_препятствий_1_out_65 ,
       \удаление_препятствий_1_out_66 , \удаление_препятствий_1_out_67 , \удаление_препятствий_1_out_68 ,
       \удаление_препятствий_1_out_69 ;

  \вверхняя_часть_карты  \u_вверхняя_часть_карты_1  (
    .clock(clock_t), .out_3(\вверхняя_часть_карты_1_out_3 ), .out_4(\вверхняя_часть_карты_1_out_4 ),
    .out_5(\вверхняя_часть_карты_1_out_5 ), .out_6(\вверхняя_часть_карты_1_out_6 ),
    .out_7(\вверхняя_часть_карты_1_out_7 ), .out_8(\вверхняя_часть_карты_1_out_8 ),
    .out_9(\вверхняя_часть_карты_1_out_9 ), .out_10(\вверхняя_часть_карты_1_out_10 ),
    .out_11(\вверхняя_часть_карты_1_out_11 ), .out_12(\вверхняя_часть_карты_1_out_12 ),
    .out_13(\вверхняя_часть_карты_1_out_13 ), .out_14(\вверхняя_часть_карты_1_out_14 ),
    .out_15(\вверхняя_часть_карты_1_out_15 ), .out_16(\вверхняя_часть_карты_1_out_16 ),
    .out_17(\вверхняя_часть_карты_1_out_17 ), .game_over(out_8));
  \нижняя_часть_карты  \u_нижняя_часть_карты_1  (
    .clock(out_9), .out_3(\нижняя_часть_карты_1_out_3 ), .out_4(\нижняя_часть_карты_1_out_4 ),
    .out_5(\нижняя_часть_карты_1_out_5 ), .out_6(\нижняя_часть_карты_1_out_6 ),
    .out_7(\нижняя_часть_карты_1_out_7 ), .out_8(\нижняя_часть_карты_1_out_8 ),
    .out_9(\нижняя_часть_карты_1_out_9 ), .out_10(\нижняя_часть_карты_1_out_10 ),
    .out_11(\нижняя_часть_карты_1_out_11 ), .out_12(\нижняя_часть_карты_1_out_12 ), .game_over(out_8));
  D_Flip_Flop d_ff_1 (.clk(clock_t), .D(out_10), .Q(d_ff_1_q), .en(1'b1));  // open: Qn, preset, reset
  \game_over_фон  \game_over_фон_1  (
    .clock(clock_t), .game_over(out_10), .in_3({32{1'b0}}), .out_38(_1), .in_4({32{1'b0}}), .out_39(_2),
    .in_5({32{1'b0}}), .out_40(_3), .in_6({32{1'b0}}), .out_41(out_14), .in_7({32{1'b0}}), .out_42(out_15),
    .in_8({32{1'b0}}), .out_43(out_16), .in_9({32{1'b0}}), .out_44(out_17), .in_10({32{1'b0}}),
    .out_45(out_18), .in_11({32{1'b0}}), .out_46(out_19), .in_12({32{1'b0}}), .out_47(out_20),
    .in_13(\вверхняя_часть_карты_1_out_3 ), .out_48(out_21), .in_14(\вверхняя_часть_карты_1_out_4 ),
    .out_49(out_22), .in_15(\вверхняя_часть_карты_1_out_5 ), .out_50(out_23),
    .in_16(\вверхняя_часть_карты_1_out_6 ), .out_51(out_24), .in_17(\вверхняя_часть_карты_1_out_7 ),
    .out_52(out_25), .in_18(\вверхняя_часть_карты_1_out_8 ), .out_53(out_26),
    .in_19(\вверхняя_часть_карты_1_out_9 ), .out_54(out_27), .in_20(\вверхняя_часть_карты_1_out_10 ),
    .out_55(out_28), .in_21(\вверхняя_часть_карты_1_out_11 ), .out_56(out_29),
    .in_22(\вверхняя_часть_карты_1_out_12 ), .out_57(out_30), .in_23(\вверхняя_часть_карты_1_out_13 ),
    .out_58(out_31), .in_24(\вверхняя_часть_карты_1_out_14 ), .out_59(out_32),
    .in_25(\вверхняя_часть_карты_1_out_15 ), .out_60(out_33), .in_26(\вверхняя_часть_карты_1_out_16 ),
    .out_61(out_34), .in_27(\вверхняя_часть_карты_1_out_17 ), .out_62(out_35),
    .in_28(\нижняя_часть_карты_1_out_3 ), .out_63(out_36), .in_29(\нижняя_часть_карты_1_out_4 ),
    .out_64(out_37), .in_30(\нижняя_часть_карты_1_out_5 ), .out_65(out_38),
    .in_31(\нижняя_часть_карты_1_out_6 ), .out_66(out_39), .in_32(\нижняя_часть_карты_1_out_7 ),
    .out_67(out_40), .in_33(\нижняя_часть_карты_1_out_8 ), .out_68(out_41),
    .in_34(\нижняя_часть_карты_1_out_9 ), .out_69(out_42), .in_35(\нижняя_часть_карты_1_out_10 ),
    .out_70(out_43), .in_36(\нижняя_часть_карты_1_out_11 ), .out_71(out_44),
    .in_37(\нижняя_часть_карты_1_out_12 ), .out_72(_35));
  and and_1 (clear, out_10, ~d_ff_1_q);  // AND_Gate
  Comparator #(.width(7)) comparator_1 (.a(sumbol), .b(7'b0100000), .eq(comparator_1_eq));  // open: gt, lt
  Comparator #(.width(7)) comparator_2 (.a(sumbol), .b(7'b1110011), .eq(comparator_2_eq));  // open: gt, lt
  Comparator #(.width(7)) comparator_3 (.a(sumbol), .b(7'b1100011), .eq(comparator_3_eq));  // open: gt, lt
  Comparator #(.width(7)) comparator_4 (.a(sumbol), .b(7'b1111000), .eq(comparator_4_eq));  // open: gt, lt
  Comparator #(.width(7)) comparator_5 (.a(sumbol), .b(7'b1110010), .eq(comparator_5_eq));  // open: gt, lt
  \сдвиг_карты  \u_сдвиг_карты_1  (
    .in_3(_1), .in_4(out_18), .in_5(out_25), .in_6(out_32), .in_7(out_39), .in_8(_2), .in_9(out_19),
    .in_10(out_26), .in_11(out_33), .in_12(out_40), .in_13(_3), .in_14(out_20), .in_15(out_27),
    .in_16(out_34), .in_17(out_41), .in_18(out_14), .in_19(out_21), .in_20(out_28), .in_21(out_35),
    .in_22(out_42), .in_23(out_15), .in_24(out_22), .in_25(out_29), .in_26(out_36), .in_27(out_43),
    .in_28(out_16), .in_29(out_23), .in_30(out_30), .in_31(out_37), .in_32(out_44), .in_33(out_17),
    .in_34(out_24), .in_35(out_31), .in_36(out_38), .in_37(_35), .in_38(clock_t), .in_41(clock_t),
    .in_39(clock_t), .in_40(clock_t), .in_42(out_9), .out_43(_1_2), .out_44(out_53), .out_45(out_60),
    .out_46(out_67), .out_47(out_74), .out_48(out_47), .out_49(out_54), .out_50(out_61), .out_51(out_68),
    .out_52(out_75), .out_53(out_48), .out_54(out_55), .out_55(out_62), .out_56(out_69), .out_57(out_76),
    .out_58(out_49), .out_59(out_56), .out_60(out_63), .out_61(out_70), .out_62(out_77), .out_63(out_50),
    .out_64(out_57), .out_65(out_64), .out_66(out_71), .out_67(out_78), .out_68(out_51), .out_69(out_58),
    .out_70(out_65), .out_71(out_72), .out_72(out_79), .out_73(out_52), .out_74(out_59), .out_75(out_66),
    .out_76(out_73), .out_77(out_80), .in_1(out_10), .in_2(clear_rest));
  D_Flip_Flop d_ff_2 (.clk(start), .D(1'b1), .Q(jump), .en(comparator_1_eq), .reset(jump_out));  // open: Qn, preset
  D_Flip_Flop d_ff_3 (.clk(start), .D(1'b1), .Q(sit_down), .en(comparator_2_eq), .reset(jump_out));  // open: Qn, preset
  D_Flip_Flop d_ff_4 (
    .clk(start), .D(1'b1), .Q(choose), .en(comparator_3_eq), .reset(comparator_4_eq));  // open: Qn, preset
  D_Flip_Flop d_ff_5 (.clk(start), .D(1'b1), .Q(out_8), .en(comparator_5_eq), .reset(clear_rest));  // open: Qn, preset
  or or_1 (or_1_out, stop2, stop1);
  \сдвиг_карты  \u_сдвиг_карты_2  (
    .in_3(_1_2), .in_4(out_53), .in_5(out_60), .in_6(out_67), .in_7(out_74), .in_8(out_47), .in_9(out_54),
    .in_10(out_61), .in_11(out_68), .in_12(out_75), .in_13(out_48), .in_14(out_55), .in_15(out_62),
    .in_16(out_69), .in_17(out_76), .in_18(out_49), .in_19(out_56), .in_20(out_63), .in_21(out_70),
    .in_22(out_77), .in_23(out_50), .in_24(out_57), .in_25(out_64), .in_26(out_71), .in_27(out_78),
    .in_28(out_51), .in_29(out_58), .in_30(out_65), .in_31(out_72), .in_32(out_79), .in_33(out_52),
    .in_34(out_59), .in_35(out_66), .in_36(out_73), .in_37(out_80), .in_38(clock_t), .in_41(clock_t),
    .in_39(clock_t), .in_40(clock_t), .in_42(out_9), .out_43(\сдвиг_карты_2_out_43 ),
    .out_44(\сдвиг_карты_2_out_44 ), .out_45(\сдвиг_карты_2_out_45 ), .out_46(\сдвиг_карты_2_out_46 ),
    .out_47(\сдвиг_карты_2_out_47 ), .out_48(\сдвиг_карты_2_out_48 ), .out_49(\сдвиг_карты_2_out_49 ),
    .out_50(\сдвиг_карты_2_out_50 ), .out_51(\сдвиг_карты_2_out_51 ), .out_52(\сдвиг_карты_2_out_52 ),
    .out_53(\сдвиг_карты_2_out_53 ), .out_54(\сдвиг_карты_2_out_54 ), .out_55(\сдвиг_карты_2_out_55 ),
    .out_56(\сдвиг_карты_2_out_56 ), .out_57(\сдвиг_карты_2_out_57 ), .out_58(\сдвиг_карты_2_out_58 ),
    .out_59(\сдвиг_карты_2_out_59 ), .out_60(\сдвиг_карты_2_out_60 ), .out_61(\сдвиг_карты_2_out_61 ),
    .out_62(\сдвиг_карты_2_out_62 ), .out_63(\сдвиг_карты_2_out_63 ), .out_64(\сдвиг_карты_2_out_64 ),
    .out_65(\сдвиг_карты_2_out_65 ), .out_66(\сдвиг_карты_2_out_66 ), .out_67(\сдвиг_карты_2_out_67 ),
    .out_68(\сдвиг_карты_2_out_68 ), .out_69(\сдвиг_карты_2_out_69 ), .out_70(\сдвиг_карты_2_out_70 ),
    .out_71(\сдвиг_карты_2_out_71 ), .out_72(\сдвиг_карты_2_out_72 ), .out_73(\сдвиг_карты_2_out_73 ),
    .out_74(\сдвиг_карты_2_out_74 ), .out_75(\сдвиг_карты_2_out_75 ), .out_76(\сдвиг_карты_2_out_76 ),
    .out_77(\сдвиг_карты_2_out_77 ), .in_1(out_10), .in_2(clear_rest));
  \дино  \u_дино_1  (
    .jump(jump), .Game_Over(out_10), .clock(out_11), .out_6(\дино_1_out_6 ), .sit_down(sit_down),
    .out_7(\дино_1_out_7 ), .choose(choose), .out_8(\дино_1_out_8 ), .out_9(\дино_1_out_9 ),
    .out_10(\дино_1_out_10 ), .out_11(\дино_1_out_11 ), .out_12(\дино_1_out_12 ), .out_13(\дино_1_out_13 ),
    .out_14(\дино_1_out_14 ), .out_15(\дино_1_out_15 ), .out_16(\дино_1_out_16 ), .out_17(\дино_1_out_17 ),
    .out_18(\дино_1_out_18 ), .out_20(\дино_1_out_20 ), .out_21(\дино_1_out_21 ), .out_22(\дино_1_out_22 ),
    .out_23(\дино_1_out_23 ), .out_24(\дино_1_out_24 ), .out_25(\дино_1_out_25 ), .out_26(\дино_1_out_26 ),
    .out_27(\дино_1_out_27 ), .out_28(\дино_1_out_28 ), .out_29(\дино_1_out_29 ), .out_30(\дино_1_out_30 ),
    .out_31(\дино_1_out_31 ), .out_32(\дино_1_out_32 ), .out_33(\дино_1_out_33 ), .out_34(\дино_1_out_34 ),
    .out_35(\дино_1_out_35 ), .out_36(\дино_1_out_36 ), .out_37(\дино_1_out_37 ), .out_38(\дино_1_out_38 ),
    .jump_out(jump_out));
  \удаление_препятствий  \u_удаление_препятствий_1  (
    .clock(clock_3), .game_over(or_1_out), .in_3(\сдвиг_карты_2_out_43 ),
    .out_38(\удаление_препятствий_1_out_38 ), .in_4(\сдвиг_карты_2_out_48 ),
    .out_39(\удаление_препятствий_1_out_39 ), .in_5(\сдвиг_карты_2_out_53 ),
    .out_40(\удаление_препятствий_1_out_40 ), .in_6(\сдвиг_карты_2_out_58 ),
    .out_41(\удаление_препятствий_1_out_41 ), .in_7(\сдвиг_карты_2_out_63 ),
    .out_42(\удаление_препятствий_1_out_42 ), .in_8(\сдвиг_карты_2_out_68 ),
    .out_43(\удаление_препятствий_1_out_43 ), .in_9(\сдвиг_карты_2_out_73 ),
    .out_44(\удаление_препятствий_1_out_44 ), .in_10(\сдвиг_карты_2_out_44 ),
    .out_45(\удаление_препятствий_1_out_45 ), .in_11(\сдвиг_карты_2_out_49 ),
    .out_46(\удаление_препятствий_1_out_46 ), .in_12(\сдвиг_карты_2_out_54 ),
    .out_47(\удаление_препятствий_1_out_47 ), .in_13(\сдвиг_карты_2_out_59 ),
    .out_48(\удаление_препятствий_1_out_48 ), .in_14(\сдвиг_карты_2_out_64 ),
    .out_49(\удаление_препятствий_1_out_49 ), .in_15(\сдвиг_карты_2_out_69 ),
    .out_50(\удаление_препятствий_1_out_50 ), .in_16(\сдвиг_карты_2_out_74 ),
    .out_51(\удаление_препятствий_1_out_51 ), .in_17(\сдвиг_карты_2_out_45 ),
    .out_52(\удаление_препятствий_1_out_52 ), .in_18(\сдвиг_карты_2_out_50 ),
    .out_53(\удаление_препятствий_1_out_53 ), .in_19(\сдвиг_карты_2_out_55 ),
    .out_54(\удаление_препятствий_1_out_54 ), .in_20(\сдвиг_карты_2_out_60 ),
    .out_55(\удаление_препятствий_1_out_55 ), .in_21(\сдвиг_карты_2_out_65 ),
    .out_56(\удаление_препятствий_1_out_56 ), .in_22(\сдвиг_карты_2_out_70 ),
    .out_57(\удаление_препятствий_1_out_57 ), .in_23(\сдвиг_карты_2_out_75 ),
    .out_58(\удаление_препятствий_1_out_58 ), .in_24(\сдвиг_карты_2_out_46 ),
    .out_59(\удаление_препятствий_1_out_59 ), .in_25(\сдвиг_карты_2_out_51 ),
    .out_60(\удаление_препятствий_1_out_60 ), .in_26(\сдвиг_карты_2_out_56 ),
    .out_61(\удаление_препятствий_1_out_61 ), .in_27(\сдвиг_карты_2_out_61 ),
    .out_62(\удаление_препятствий_1_out_62 ), .in_28(\сдвиг_карты_2_out_66 ),
    .out_63(\удаление_препятствий_1_out_63 ), .in_29(\сдвиг_карты_2_out_71 ),
    .out_64(\удаление_препятствий_1_out_64 ), .in_30(\сдвиг_карты_2_out_76 ),
    .out_65(\удаление_препятствий_1_out_65 ), .in_31(\сдвиг_карты_2_out_47 ),
    .out_66(\удаление_препятствий_1_out_66 ), .in_32(\сдвиг_карты_2_out_52 ),
    .out_67(\удаление_препятствий_1_out_67 ), .in_33(\сдвиг_карты_2_out_57 ),
    .out_68(\удаление_препятствий_1_out_68 ), .in_34(\сдвиг_карты_2_out_62 ),
    .out_69(\удаление_препятствий_1_out_69 ), .in_35(\сдвиг_карты_2_out_67 ), .out_70(out_113),
    .in_36(\сдвиг_карты_2_out_72 ), .out_71(out_114), .in_37(\сдвиг_карты_2_out_77 ), .out_72(out_115));
  \скорость2  \u_скорость2_1  (.clock(start), .del(5'b00001), .out_3(out_11));
  \скорость2  \u_скорость2_2  (.clock(start), .del(vec_adr), .out_3(clock_t));
  Comparator #(.width(4)) comparator_6 (.a(count_3), .b(4'b0000), .eq(comparator_6_eq));  // open: gt, lt
  Comparator #(.width(4)) comparator_7 (.a(count_3), .b(4'b0101), .eq(comparator_7_eq));  // open: gt, lt
  Comparator #(.width(4)) comparator_8 (.a(count_4), .b(4'b0000), .eq(comparator_8_eq));  // open: gt, lt
  \или32  \u_или32_1  (
    .in_1(\дино_1_out_6 ), .in_2(\дино_1_out_7 ), .in_3(\дино_1_out_8 ), .in_4(\дино_1_out_9 ),
    .in_5(\дино_1_out_10 ), .in_6(\дино_1_out_11 ), .in_7(\дино_1_out_12 ), .in_8(\дино_1_out_13 ),
    .in_9(\дино_1_out_14 ), .in_10(\дино_1_out_15 ), .in_11(\дино_1_out_16 ), .in_12(\дино_1_out_17 ),
    .in_13(\дино_1_out_18 ), .in_14(\дино_1_out_20 ), .in_15(\дино_1_out_21 ), .in_16(\дино_1_out_22 ),
    .in_17(\дино_1_out_23 ), .in_18(\дино_1_out_24 ), .in_19(\дино_1_out_25 ), .in_20(\дино_1_out_26 ),
    .in_21(\дино_1_out_27 ), .in_22(\дино_1_out_28 ), .in_23(\дино_1_out_29 ), .in_24(\дино_1_out_30 ),
    .in_25(\дино_1_out_31 ), .in_26(\дино_1_out_32 ), .in_27(\дино_1_out_33 ), .in_28(\дино_1_out_34 ),
    .in_29(\дино_1_out_35 ), .in_30(\дино_1_out_36 ), .in_31(\дино_1_out_37 ), .in_32(\дино_1_out_38 ),
    .in_33(\удаление_препятствий_1_out_38 ), .in_34(\удаление_препятствий_1_out_39 ),
    .in_35(\удаление_препятствий_1_out_40 ), .in_36(\удаление_препятствий_1_out_41 ),
    .in_37(\удаление_препятствий_1_out_42 ), .in_38(\удаление_препятствий_1_out_43 ),
    .in_39(\удаление_препятствий_1_out_44 ), .in_40(\удаление_препятствий_1_out_45 ),
    .in_41(\удаление_препятствий_1_out_46 ), .in_42(\удаление_препятствий_1_out_47 ),
    .in_43(\удаление_препятствий_1_out_48 ), .in_44(\удаление_препятствий_1_out_49 ),
    .in_45(\удаление_препятствий_1_out_50 ), .in_46(\удаление_препятствий_1_out_51 ),
    .in_47(\удаление_препятствий_1_out_52 ), .in_48(\удаление_препятствий_1_out_53 ),
    .in_49(\удаление_препятствий_1_out_54 ), .in_50(\удаление_препятствий_1_out_55 ),
    .in_51(\удаление_препятствий_1_out_56 ), .in_52(\удаление_препятствий_1_out_57 ),
    .in_53(\удаление_препятствий_1_out_58 ), .in_54(\удаление_препятствий_1_out_59 ),
    .in_55(\удаление_препятствий_1_out_60 ), .in_56(\удаление_препятствий_1_out_61 ),
    .in_57(\удаление_препятствий_1_out_62 ), .in_58(\удаление_препятствий_1_out_63 ),
    .in_59(\удаление_препятствий_1_out_64 ), .in_60(\удаление_препятствий_1_out_65 ),
    .in_61(\удаление_препятствий_1_out_66 ), .in_62(\удаление_препятствий_1_out_67 ),
    .in_63(\удаление_препятствий_1_out_68 ), .in_64(\удаление_препятствий_1_out_69 ), .out_65(out_81),
    .out_66(out_82), .out_67(out_83), .out_68(out_84), .out_69(out_85), .out_71(out_86), .out_72(out_87),
    .out_73(out_88), .out_74(out_89), .out_75(out_90), .out_76(out_91), .out_77(out_92), .out_78(out_93),
    .out_79(out_94), .out_80(out_95), .out_81(out_96), .out_82(out_97), .out_83(out_98), .out_84(out_99),
    .out_85(out_100), .out_86(out_101), .out_87(out_102), .out_88(out_103), .out_89(out_104),
    .out_90(out_105), .out_91(out_106), .out_92(out_107), .out_93(out_108), .out_94(out_109),
    .out_95(out_110), .out_96(out_111), .out_97(out_112), .stop(stop1), .out_98(\или32_1_out_98 ));
  or or_2 (or_2_out, comparator_6_eq, comparator_7_eq);
  Counter #(.max('h4), .trigger("falling")) counter_1 (
    .Q(counter_1_q), .clk(clock_t), .clr(out_9));  // open: load, D, count, carry
  and and_2 (and_2_out, or_2_out, comparator_8_eq);
  Comparator comparator_9 (.a(counter_1_q), .b(8'h3), .eq(out_9));  // open: gt, lt
  \коллизии_ямы  \u_коллизии_ямы_1  (.in_1(\дино_1_out_38 ), .in_2(out_113), .stop(stop2));
  Multiplexer multiplexer_1 (.in0(clock_t), .in1(out_9), .out(clock_3), .sel(\или32_1_out_98 ), .en(1'b1));
  Counter #(.width(5), .max('hf), .ongoal("stay")) counter_2 (
    .count(1'b1), .Q(counter_2_q), .clk(and_2_out), .clr(out_8));  // open: load, D, carry
  \подсчет_жизней  \u_подсчет_жизней_1  (
    .clock_dino(start), .stop1(stop1), .stop2(stop2), .rest(out_8), .lcount(lcount),
    .game_over(\подсчет_жизней_1_game_over ));
  Subtractor #(.width(5)) subtractor_1 (.a(5'b10000), .b(counter_2_q), .out(vec_adr));  // open: bin, bout
  or or_3 (out_10, \подсчет_жизней_1_game_over , \подсчет_жизней_1_game_over );
  Counter #(.width(2), .max('h3)) counter_3 (
    .count(1'b1), .carry(counter_3_carry), .clk(start));  // open: load, D, Q, clr
  and and_3 (clear_rest, out_8, counter_3_carry);
  Counter #(.width(14), .max('h3fff)) counter_4 (.count(1'b1), .Q(c), .clk(and_4_out));  // open: load, D, carry, clr
  and and_4 (and_4_out, out_9, ~out_10);  // AND_Gate

  assign clock = start;

  // Other names for the same wires on the sheet: clock_2 = out_9; clock_dino = out_11; game_over = out_10;
  //   m1_0[31:0] = _1; m1_1[31:0] = _2; m1_2[31:0] = _3; m1_3[31:0] = out_14; m1_4[31:0] = out_15;
  //   m1_5[31:0] = out_17; m1_6[31:0] = out_18; m1_7[31:0] = out_19; m1_8[31:0] = out_20; m1_9[31:0] = out_21;
  //   m1_10[31:0] = out_22; m1_11[31:0] = out_23; m1_12[31:0] = out_24; m1_13[31:0] = out_25; m1_14[31:0] = out_26;
  //   m1_15[31:0] = out_27; m1_16[31:0] = out_28; m1_17[31:0] = out_29; m1_18[31:0] = out_30; m1_19[31:0] = out_31;
  //   m1_20[31:0] = out_32; m1_21[31:0] = out_33; m1_22[31:0] = out_34; m1_23[31:0] = out_35; m1_55[31:0] = out_16;
  //   m1_c0[31:0] = out_42; m1_c1[31:0] = out_41; m1_c2[31:0] = out_40; m1_c3[31:0] = out_39; m1_c4[31:0] = out_38;
  //   m1_c5[31:0] = out_37; m1_c6[31:0] = out_36; m1_r0[31:0] = _35; m1_r1[31:0] = out_44; m1_r2[31:0] = out_43;
  //   m2_0[31:0] = _1_2; m2_1[31:0] = out_47; m2_2[31:0] = out_48; m2_3[31:0] = out_49; m2_4[31:0] = out_50;
  //   m2_5[31:0] = out_52; m2_6[31:0] = out_53; m2_7[31:0] = out_54; m2_8[31:0] = out_55; m2_9[31:0] = out_56;
  //   m2_10[31:0] = out_57; m2_11[31:0] = out_58; m2_12[31:0] = out_59; m2_13[31:0] = out_60; m2_14[31:0] = out_61;
  //   m2_15[31:0] = out_62; m2_16[31:0] = out_63; m2_17[31:0] = out_64; m2_18[31:0] = out_65; m2_19[31:0] = out_66;
  //   m2_20[31:0] = out_67; m2_21[31:0] = out_68; m2_22[31:0] = out_69; m2_23[31:0] = out_70; m2_55[31:0] = out_51;
  //   m2_c0[31:0] = out_77; m2_c1[31:0] = out_76; m2_c2[31:0] = out_75; m2_c3[31:0] = out_74; m2_c4[31:0] = out_73;
  //   m2_c5[31:0] = out_72; m2_c6[31:0] = out_71; m2_r0[31:0] = out_80; m2_r1[31:0] = out_79; m2_r2[31:0] = out_78;
  //   m3_0[31:0] = out_81; m3_1[31:0] = out_82; m3_2[31:0] = out_83; m3_3[31:0] = out_84; m3_4[31:0] = out_85;
  //   m3_5[31:0] = out_87; m3_6[31:0] = out_88; m3_7[31:0] = out_89; m3_8[31:0] = out_90; m3_9[31:0] = out_91;
  //   m3_10[31:0] = out_92; m3_11[31:0] = out_93; m3_12[31:0] = out_94; m3_13[31:0] = out_95; m3_14[31:0] = out_96;
  //   m3_15[31:0] = out_97; m3_16[31:0] = out_98; m3_17[31:0] = out_99; m3_18[31:0] = out_100; m3_19[31:0] = out_101;
  //   m3_20[31:0] = out_102; m3_21[31:0] = out_103; m3_22[31:0] = out_104; m3_23[31:0] = out_105;
  //   m3_55[31:0] = out_86; m3_c0[31:0] = out_112; m3_c1[31:0] = out_111; m3_c2[31:0] = out_110;
  //   m3_c3[31:0] = out_109; m3_c4[31:0] = out_108; m3_c5[31:0] = out_107; m3_c6[31:0] = out_106;
  //   m3_r0[31:0] = out_115; m3_r1[31:0] = out_114; m3_r2[31:0] = out_113; rest = out_8

  // Notes on the sheet:
  //   клавиатура
  //   картинка
  //   скорость
  //   жизни/конец_игры/рестарт
endmodule
module \черновик  (
  input  in_1,
  input  in_2
);

  wire and_1_out, clock, clock_1_out, clock_dino, clock_img, comparator_1_eq, comparator_2_eq,
       comparator_3_eq, comparator_4_eq, counter_2_carry, d_ff_1_q, game_over, init, jmpuls, register_1_q,
       rest, signal, t_ff_1_q, \клавиатура_1_clock ;
  wire [1:0] \клавиатура_1_lcount ;
  wire [2:0] counter_2_q;
  wire [3:0] count1, count2, count3, count4, \лидеры_cdm_8_1_out_4 , \лидеры_cdm_8_1_out_5 ,
       \лидеры_cdm_8_1_out_6 , \лидеры_cdm_8_1_out_7 , \лидеры_cdm_8_1_out_8 , \лидеры_cdm_8_1_out_9 ,
       \лидеры_cdm_8_1_out_10 , \лидеры_cdm_8_1_out_11 , \лидеры_cdm_8_1_out_12 , \лидеры_cdm_8_1_out_13 ,
       \лидеры_cdm_8_1_out_14 , \лидеры_cdm_8_1_out_15 , \лидеры_cdm_8_1_out_16 , \лидеры_cdm_8_1_out_17 ,
       \лидеры_cdm_8_1_out_18 , \лидеры_cdm_8_1_out_19 , \лидеры_cdm_8_1_out_20 , \лидеры_cdm_8_1_out_21 ,
       \лидеры_cdm_8_1_out_22 , \лидеры_cdm_8_1_out_23 ;
  wire [6:0] keyboard_1_data;
  wire [7:0] \жизни_1_live1 , \жизни_1_live2 , \жизни_1_live3 , \жизни_1_live4 , \жизни_1_live5 ,
       \жизни_1_live6 , \жизни_1_live7 , \жизни_1_live8 , \жизни_1_live9 , \жизни_1_live10 ,
       \жизни_1_live11 , \жизни_1_live12 , \жизни_1_live13 , \жизни_1_live14 , \жизни_1_live15 ,
       \жизни_1_live16 , \жизни_1_live17 , \жизни_1_live18 , \жизни_1_live19 , \жизни_1_live20 ,
       \жизни_1_live21 , \жизни_1_live22 , \жизни_1_live23 , \жизни_1_live24 , \жизни_1_live25 ;
  wire [9:0] counter_1_q;
  wire [13:0] data, multiplexer_1_out, multiplexer_3_out, \очки_1_out_4 ;
  wire [31:0] \клавиатура_1__1 , \клавиатура_1__1_2 , \клавиатура_1__2 , \клавиатура_1__3 ,
       \клавиатура_1__35 , \клавиатура_1_out_14 , \клавиатура_1_out_15 , \клавиатура_1_out_16 ,
       \клавиатура_1_out_17 , \клавиатура_1_out_18 , \клавиатура_1_out_19 , \клавиатура_1_out_20 ,
       \клавиатура_1_out_21 , \клавиатура_1_out_22 , \клавиатура_1_out_23 , \клавиатура_1_out_24 ,
       \клавиатура_1_out_25 , \клавиатура_1_out_26 , \клавиатура_1_out_27 , \клавиатура_1_out_28 ,
       \клавиатура_1_out_29 , \клавиатура_1_out_30 , \клавиатура_1_out_31 , \клавиатура_1_out_32 ,
       \клавиатура_1_out_33 , \клавиатура_1_out_34 , \клавиатура_1_out_35 , \клавиатура_1_out_36 ,
       \клавиатура_1_out_37 , \клавиатура_1_out_38 , \клавиатура_1_out_39 , \клавиатура_1_out_40 ,
       \клавиатура_1_out_41 , \клавиатура_1_out_42 , \клавиатура_1_out_43 , \клавиатура_1_out_44 ,
       \клавиатура_1_out_47 , \клавиатура_1_out_48 , \клавиатура_1_out_49 , \клавиатура_1_out_50 ,
       \клавиатура_1_out_51 , \клавиатура_1_out_52 , \клавиатура_1_out_53 , \клавиатура_1_out_54 ,
       \клавиатура_1_out_55 , \клавиатура_1_out_56 , \клавиатура_1_out_57 , \клавиатура_1_out_58 ,
       \клавиатура_1_out_59 , \клавиатура_1_out_60 , \клавиатура_1_out_61 , \клавиатура_1_out_62 ,
       \клавиатура_1_out_63 , \клавиатура_1_out_64 , \клавиатура_1_out_65 , \клавиатура_1_out_66 ,
       \клавиатура_1_out_67 , \клавиатура_1_out_68 , \клавиатура_1_out_69 , \клавиатура_1_out_70 ,
       \клавиатура_1_out_71 , \клавиатура_1_out_72 , \клавиатура_1_out_73 , \клавиатура_1_out_74 ,
       \клавиатура_1_out_75 , \клавиатура_1_out_76 , \клавиатура_1_out_77 , \клавиатура_1_out_78 ,
       \клавиатура_1_out_79 , \клавиатура_1_out_80 , \клавиатура_1_out_81 , \клавиатура_1_out_82 ,
       \клавиатура_1_out_83 , \клавиатура_1_out_84 , \клавиатура_1_out_85 , \клавиатура_1_out_86 ,
       \клавиатура_1_out_87 , \клавиатура_1_out_88 , \клавиатура_1_out_89 , \клавиатура_1_out_90 ,
       \клавиатура_1_out_91 , \клавиатура_1_out_92 , \клавиатура_1_out_93 , \клавиатура_1_out_94 ,
       \клавиатура_1_out_95 , \клавиатура_1_out_96 , \клавиатура_1_out_97 , \клавиатура_1_out_98 ,
       \клавиатура_1_out_99 , \клавиатура_1_out_100 , \клавиатура_1_out_101 , \клавиатура_1_out_102 ,
       \клавиатура_1_out_103 , \клавиатура_1_out_104 , \клавиатура_1_out_105 , \клавиатура_1_out_106 ,
       \клавиатура_1_out_107 , \клавиатура_1_out_108 , \клавиатура_1_out_109 , \клавиатура_1_out_110 ,
       \клавиатура_1_out_111 , \клавиатура_1_out_112 , \клавиатура_1_out_113 , \клавиатура_1_out_114 ,
       \клавиатура_1_out_115 , \рекорды_1_the_1_st_line_of_the_picture ,
       \рекорды_1_the_1_st_line_of_the_picture_2 , \рекорды_1_the_2_nd_line_of_the_picture ,
       \рекорды_1_the_2_nd_line_of_the_picture_2 , \рекорды_1_the_3_rd_line_of_the_picture ,
       \рекорды_1_the_3_rd_line_of_the_picture_2 , \рекорды_1_the_4_th_line_of_the_picture ,
       \рекорды_1_the_4_th_line_of_the_picture_2 , \рекорды_1_the_5_th_line_of_the_picture ,
       \рекорды_1_the_5_th_line_of_the_picture_2 , \рекорды_1_the_6_th_line_of_the_picture ,
       \рекорды_1_the_6_th_line_of_the_picture_2 , \рекорды_1_the_7_th_line_of_the_picture ,
       \рекорды_1_the_7_th_line_of_the_picture_2 , \рекорды_1_the_8_th_line_of_the_picture ,
       \рекорды_1_the_8_th_line_of_the_picture_2 , \рекорды_1_the_9_th_line_of_the_picture ,
       \рекорды_1_the_9_th_line_of_the_picture_2 , \рекорды_1_the_10_th_line_of_the_picture ,
       \рекорды_1_the_10_th_line_of_the_picture_2 , \рекорды_1_the_11_th_line_of_the_picture ,
       \рекорды_1_the_11_th_line_of_the_picture_2 , \рекорды_1_the_12_th_line_of_the_picture ,
       \рекорды_1_the_12_th_line_of_the_picture_2 , \рекорды_1_the_13_th_line_of_the_picture ,
       \рекорды_1_the_13_th_line_of_the_picture_2 , \рекорды_1_the_14_th_line_of_the_picture ,
       \рекорды_1_the_14_th_line_of_the_picture_2 , \рекорды_1_the_15_th_line_of_the_picture ,
       \рекорды_1_the_15_th_line_of_the_picture_2 , \рекорды_1_the_16_th_line_of_the_picture ,
       \рекорды_1_the_16_th_line_of_the_picture_2 , \рекорды_1_the_17_th_line_of_the_picture ,
       \рекорды_1_the_17_th_line_of_the_picture_2 , \рекорды_1_the_18_th_line_of_the_picture ,
       \рекорды_1_the_18_th_line_of_the_picture_2 , \рекорды_1_the_19_th_line_of_the_picture ,
       \рекорды_1_the_19_th_line_of_the_picture_2 , \рекорды_1_the_20_th_line_of_the_picture ,
       \рекорды_1_the_20_th_line_of_the_picture_2 , \рекорды_1_the_21_st_line_of_the_picture ,
       \рекорды_1_the_21_st_line_of_the_picture_2 , \рекорды_1_the_22_nd_line_of_the_picture ,
       \рекорды_1_the_22_nd_line_of_the_picture_2 , \рекорды_1_the_23_rd_line_of_the_picture ,
       \рекорды_1_the_23_rd_line_of_the_picture_2 , \рекорды_1_the_24_th_line_of_the_picture ,
       \рекорды_1_the_24_th_line_of_the_picture_2 , \рекорды_1_the_25_th_line_of_the_picture ,
       \рекорды_1_the_25_th_line_of_the_picture_2 , \рекорды_1_the_26_th_line_of_the_picture ,
       \рекорды_1_the_26_th_line_of_the_picture_2 , \рекорды_1_the_27_th_line_of_the_picture ,
       \рекорды_1_the_27_th_line_of_the_picture_2 , \рекорды_1_the_28_th_line_of_the_picture ,
       \рекорды_1_the_28_th_line_of_the_picture_2 , \рекорды_1_the_29_th_line_of_the_picture ,
       \рекорды_1_the_29_th_line_of_the_picture_2 , \рекорды_1_the_30_th_line_of_the_picture_2 ,
       \рекорды_1_the_31_st_line_of_the_picture_2 , \рекорды_1_the_32_nd_line_of_the_picture ,
       \рекорды_1_the_32_nd_line_of_the_picture_2 , \текущие_очки_1_the_1_st_line_of_the_picture ,
       \текущие_очки_1_the_1_st_line_of_the_picture_2 , \текущие_очки_1_the_2_nd_line_of_the_picture ,
       \текущие_очки_1_the_2_nd_line_of_the_picture_2 , \текущие_очки_1_the_3_rd_line_of_the_picture ,
       \текущие_очки_1_the_3_rd_line_of_the_picture_2 , \текущие_очки_1_the_4_th_line_of_the_picture ,
       \текущие_очки_1_the_4_th_line_of_the_picture_2 , \текущие_очки_1_the_5_th_line_of_the_picture ,
       \текущие_очки_1_the_5_th_line_of_the_picture_2 , \текущие_очки_1_the_6_th_line_of_the_picture ,
       \текущие_очки_1_the_6_th_line_of_the_picture_2 , \текущие_очки_1_the_7_th_line_of_the_picture ,
       \текущие_очки_1_the_7_th_line_of_the_picture_2 , \текущие_очки_1_the_8_th_line_of_the_picture ,
       \текущие_очки_1_the_8_th_line_of_the_picture_2 , \текущие_очки_1_the_9_th_line_of_the_picture ,
       \текущие_очки_1_the_9_th_line_of_the_picture_2 , \текущие_очки_1_the_10_th_line_of_the_picture ,
       \текущие_очки_1_the_10_th_line_of_the_picture_2 , \текущие_очки_1_the_11_th_line_of_the_picture ,
       \текущие_очки_1_the_11_th_line_of_the_picture_2 , \текущие_очки_1_the_12_th_line_of_the_picture ,
       \текущие_очки_1_the_12_th_line_of_the_picture_2 , \текущие_очки_1_the_13_th_line_of_the_picture ,
       \текущие_очки_1_the_13_th_line_of_the_picture_2 , \текущие_очки_1_the_14_th_line_of_the_picture ,
       \текущие_очки_1_the_14_th_line_of_the_picture_2 , \текущие_очки_1_the_15_th_line_of_the_picture ,
       \текущие_очки_1_the_15_th_line_of_the_picture_2 , \текущие_очки_1_the_16_th_line_of_the_picture ,
       \текущие_очки_1_the_16_th_line_of_the_picture_2 , \текущие_очки_1_the_17_th_line_of_the_picture ,
       \текущие_очки_1_the_17_th_line_of_the_picture_2 , \текущие_очки_1_the_18_th_line_of_the_picture ,
       \текущие_очки_1_the_18_th_line_of_the_picture_2 , \текущие_очки_1_the_19_th_line_of_the_picture ,
       \текущие_очки_1_the_19_th_line_of_the_picture_2 , \текущие_очки_1_the_20_th_line_of_the_picture ,
       \текущие_очки_1_the_20_th_line_of_the_picture_2 , \текущие_очки_1_the_21_st_line_of_the_picture ,
       \текущие_очки_1_the_21_st_line_of_the_picture_2 , \текущие_очки_1_the_22_nd_line_of_the_picture ,
       \текущие_очки_1_the_22_nd_line_of_the_picture_2 , \текущие_очки_1_the_23_rd_line_of_the_picture ,
       \текущие_очки_1_the_23_rd_line_of_the_picture_2 , \текущие_очки_1_the_24_th_line_of_the_picture ,
       \текущие_очки_1_the_24_th_line_of_the_picture_2 , \текущие_очки_1_the_25_th_line_of_the_picture ,
       \текущие_очки_1_the_25_th_line_of_the_picture_2 , \текущие_очки_1_the_26_th_line_of_the_picture ,
       \текущие_очки_1_the_26_th_line_of_the_picture_2 , \текущие_очки_1_the_27_th_line_of_the_picture ,
       \текущие_очки_1_the_27_th_line_of_the_picture_2 , \текущие_очки_1_the_28_th_line_of_the_picture ,
       \текущие_очки_1_the_28_th_line_of_the_picture_2 , \текущие_очки_1_the_29_th_line_of_the_picture ,
       \текущие_очки_1_the_29_th_line_of_the_picture_2 , \текущие_очки_1_the_30_th_line_of_the_picture ,
       \текущие_очки_1_the_30_th_line_of_the_picture_2 , \текущие_очки_1_the_31_st_line_of_the_picture ,
       \текущие_очки_1_the_31_st_line_of_the_picture_2 ;

  Keyboard keyboard_1 (.clk(\клавиатура_1_clock ), .re(1'b1), .data(keyboard_1_data));  // open: clr, avail
  Clock clock_1 (.out(clock_1_out));
  Register #(.width(1)) register_1 (.D(1'b1), .Q(register_1_q), .clk(counter_2_carry));  // open: en, clr
  Counter #(.width(10), .max('h3ff)) counter_1 (
    .D(counter_1_q), .count(1'b1), .Q(counter_1_q), .clk(clock_1_out), .clr(d_ff_1_q));  // open: load, carry
  \клавиатура  \u_клавиатура_1  (
    .sumbol(keyboard_1_data), .count_3(count3), .count_4(count4), .clock(\клавиатура_1_clock ),
    ._1(\клавиатура_1__1 ), ._2(\клавиатура_1__2 ), ._3(\клавиатура_1__3 ), .out_14(\клавиатура_1_out_14 ),
    .out_15(\клавиатура_1_out_15 ), .out_16(\клавиатура_1_out_16 ), .out_17(\клавиатура_1_out_17 ),
    .out_18(\клавиатура_1_out_18 ), .out_19(\клавиатура_1_out_19 ), .out_20(\клавиатура_1_out_20 ),
    .out_21(\клавиатура_1_out_21 ), .out_22(\клавиатура_1_out_22 ), .out_23(\клавиатура_1_out_23 ),
    .out_24(\клавиатура_1_out_24 ), .out_25(\клавиатура_1_out_25 ), .out_26(\клавиатура_1_out_26 ),
    .out_27(\клавиатура_1_out_27 ), .out_28(\клавиатура_1_out_28 ), .out_29(\клавиатура_1_out_29 ),
    .out_30(\клавиатура_1_out_30 ), .out_31(\клавиатура_1_out_31 ), .out_32(\клавиатура_1_out_32 ),
    .out_33(\клавиатура_1_out_33 ), .out_34(\клавиатура_1_out_34 ), .out_35(\клавиатура_1_out_35 ),
    .out_36(\клавиатура_1_out_36 ), .out_37(\клавиатура_1_out_37 ), .out_38(\клавиатура_1_out_38 ),
    .out_39(\клавиатура_1_out_39 ), .out_40(\клавиатура_1_out_40 ), .out_41(\клавиатура_1_out_41 ),
    .out_42(\клавиатура_1_out_42 ), .out_43(\клавиатура_1_out_43 ), .out_44(\клавиатура_1_out_44 ),
    ._1_2(\клавиатура_1__1_2 ), ._35(\клавиатура_1__35 ), .out_47(\клавиатура_1_out_47 ),
    .out_48(\клавиатура_1_out_48 ), .out_49(\клавиатура_1_out_49 ), .out_50(\клавиатура_1_out_50 ),
    .out_51(\клавиатура_1_out_51 ), .out_52(\клавиатура_1_out_52 ), .out_53(\клавиатура_1_out_53 ),
    .out_54(\клавиатура_1_out_54 ), .out_55(\клавиатура_1_out_55 ), .out_56(\клавиатура_1_out_56 ),
    .out_57(\клавиатура_1_out_57 ), .out_58(\клавиатура_1_out_58 ), .out_59(\клавиатура_1_out_59 ),
    .out_60(\клавиатура_1_out_60 ), .out_61(\клавиатура_1_out_61 ), .out_62(\клавиатура_1_out_62 ),
    .out_63(\клавиатура_1_out_63 ), .out_64(\клавиатура_1_out_64 ), .out_65(\клавиатура_1_out_65 ),
    .out_66(\клавиатура_1_out_66 ), .out_67(\клавиатура_1_out_67 ), .out_68(\клавиатура_1_out_68 ),
    .out_69(\клавиатура_1_out_69 ), .out_70(\клавиатура_1_out_70 ), .out_71(\клавиатура_1_out_71 ),
    .out_72(\клавиатура_1_out_72 ), .out_73(\клавиатура_1_out_73 ), .out_74(\клавиатура_1_out_74 ),
    .out_75(\клавиатура_1_out_75 ), .out_76(\клавиатура_1_out_76 ), .out_77(\клавиатура_1_out_77 ),
    .out_78(\клавиатура_1_out_78 ), .out_79(\клавиатура_1_out_79 ), .out_80(\клавиатура_1_out_80 ),
    .out_81(\клавиатура_1_out_81 ), .out_82(\клавиатура_1_out_82 ), .out_83(\клавиатура_1_out_83 ),
    .out_84(\клавиатура_1_out_84 ), .out_85(\клавиатура_1_out_85 ), .out_86(\клавиатура_1_out_86 ),
    .out_87(\клавиатура_1_out_87 ), .out_88(\клавиатура_1_out_88 ), .out_89(\клавиатура_1_out_89 ),
    .out_90(\клавиатура_1_out_90 ), .out_91(\клавиатура_1_out_91 ), .out_92(\клавиатура_1_out_92 ),
    .out_93(\клавиатура_1_out_93 ), .out_94(\клавиатура_1_out_94 ), .out_95(\клавиатура_1_out_95 ),
    .out_96(\клавиатура_1_out_96 ), .out_97(\клавиатура_1_out_97 ), .out_98(\клавиатура_1_out_98 ),
    .out_99(\клавиатура_1_out_99 ), .out_100(\клавиатура_1_out_100 ), .out_101(\клавиатура_1_out_101 ),
    .out_102(\клавиатура_1_out_102 ), .out_103(\клавиатура_1_out_103 ), .out_104(\клавиатура_1_out_104 ),
    .out_105(\клавиатура_1_out_105 ), .out_106(\клавиатура_1_out_106 ), .out_107(\клавиатура_1_out_107 ),
    .out_108(\клавиатура_1_out_108 ), .out_109(\клавиатура_1_out_109 ), .out_110(\клавиатура_1_out_110 ),
    .out_111(\клавиатура_1_out_111 ), .out_112(\клавиатура_1_out_112 ), .out_113(\клавиатура_1_out_113 ),
    .out_114(\клавиатура_1_out_114 ), .out_115(\клавиатура_1_out_115 ), .lcount(\клавиатура_1_lcount ),
    .out_9(clock), .out_10(game_over), .out_11(clock_dino), .out_8(rest), .start(clock_img));
  DotMatrix #(.inputtype("row"), .matrixcols(32), .matrixrows(31)) dotmatrix_1 (
    .row0(\рекорды_1_the_1_st_line_of_the_picture ), .row1(\рекорды_1_the_2_nd_line_of_the_picture ),
    .row2(\рекорды_1_the_3_rd_line_of_the_picture ), .row3(\рекорды_1_the_4_th_line_of_the_picture ),
    .row4(\рекорды_1_the_5_th_line_of_the_picture ), .row5(\рекорды_1_the_6_th_line_of_the_picture ),
    .row6(\рекорды_1_the_7_th_line_of_the_picture ), .row7(\рекорды_1_the_8_th_line_of_the_picture ),
    .row8(\рекорды_1_the_9_th_line_of_the_picture ), .row9(\рекорды_1_the_10_th_line_of_the_picture ),
    .row10(\рекорды_1_the_11_th_line_of_the_picture ), .row11(\рекорды_1_the_12_th_line_of_the_picture ),
    .row12(\рекорды_1_the_13_th_line_of_the_picture ), .row13(\рекорды_1_the_14_th_line_of_the_picture ),
    .row14(\рекорды_1_the_15_th_line_of_the_picture ), .row15(\рекорды_1_the_16_th_line_of_the_picture ),
    .row16(\рекорды_1_the_17_th_line_of_the_picture ), .row17(\рекорды_1_the_18_th_line_of_the_picture ),
    .row18(\рекорды_1_the_19_th_line_of_the_picture ), .row19(\рекорды_1_the_20_th_line_of_the_picture ),
    .row20(\рекорды_1_the_21_st_line_of_the_picture ), .row21(\рекорды_1_the_22_nd_line_of_the_picture ),
    .row22(\рекорды_1_the_23_rd_line_of_the_picture ), .row23(\рекорды_1_the_24_th_line_of_the_picture ),
    .row24(\рекорды_1_the_25_th_line_of_the_picture ), .row25(\рекорды_1_the_26_th_line_of_the_picture ),
    .row26(\рекорды_1_the_27_th_line_of_the_picture ), .row27(\рекорды_1_the_28_th_line_of_the_picture ),
    .row28(\рекорды_1_the_29_th_line_of_the_picture ), .row29(\рекорды_1_the_32_nd_line_of_the_picture ),
    .row30(\рекорды_1_the_1_st_line_of_the_picture_2 ));
  \рекорды  \u_рекорды_1  (
    .the_1_st_line_of_the_picture(\рекорды_1_the_1_st_line_of_the_picture ),
    .the_2_nd_line_of_the_picture(\рекорды_1_the_2_nd_line_of_the_picture ),
    .the_3_rd_line_of_the_picture(\рекорды_1_the_3_rd_line_of_the_picture ),
    .the_4_th_line_of_the_picture(\рекорды_1_the_4_th_line_of_the_picture ),
    .the_5_th_line_of_the_picture(\рекорды_1_the_5_th_line_of_the_picture ),
    .the_6_th_line_of_the_picture(\рекорды_1_the_6_th_line_of_the_picture ),
    .the_7_th_line_of_the_picture(\рекорды_1_the_7_th_line_of_the_picture ),
    .the_8_th_line_of_the_picture(\рекорды_1_the_8_th_line_of_the_picture ),
    .the_9_th_line_of_the_picture(\рекорды_1_the_9_th_line_of_the_picture ),
    .the_10_th_line_of_the_picture(\рекорды_1_the_10_th_line_of_the_picture ),
    .the_11_th_line_of_the_picture(\рекорды_1_the_11_th_line_of_the_picture ),
    .the_12_th_line_of_the_picture(\рекорды_1_the_12_th_line_of_the_picture ),
    .the_13_th_line_of_the_picture(\рекорды_1_the_13_th_line_of_the_picture ),
    .the_14_th_line_of_the_picture(\рекорды_1_the_14_th_line_of_the_picture ),
    .the_15_th_line_of_the_picture(\рекорды_1_the_15_th_line_of_the_picture ),
    .the_16_th_line_of_the_picture(\рекорды_1_the_16_th_line_of_the_picture ),
    .the_17_th_line_of_the_picture(\рекорды_1_the_17_th_line_of_the_picture ),
    .the_18_th_line_of_the_picture(\рекорды_1_the_18_th_line_of_the_picture ),
    .the_19_th_line_of_the_picture(\рекорды_1_the_19_th_line_of_the_picture ),
    .the_20_th_line_of_the_picture(\рекорды_1_the_20_th_line_of_the_picture ),
    .the_21_st_line_of_the_picture(\рекорды_1_the_21_st_line_of_the_picture ),
    .the_22_nd_line_of_the_picture(\рекорды_1_the_22_nd_line_of_the_picture ),
    .the_23_rd_line_of_the_picture(\рекорды_1_the_23_rd_line_of_the_picture ),
    .the_24_th_line_of_the_picture(\рекорды_1_the_24_th_line_of_the_picture ),
    .the_25_th_line_of_the_picture(\рекорды_1_the_25_th_line_of_the_picture ),
    .the_26_th_line_of_the_picture(\рекорды_1_the_26_th_line_of_the_picture ),
    .the_27_th_line_of_the_picture(\рекорды_1_the_27_th_line_of_the_picture ),
    .the_28_th_line_of_the_picture(\рекорды_1_the_28_th_line_of_the_picture ),
    .the_29_th_line_of_the_picture(\рекорды_1_the_29_th_line_of_the_picture ),
    .the_30_th_line_of_the_picture(\рекорды_1_the_28_th_line_of_the_picture ),
    .the_31_st_line_of_the_picture(\рекорды_1_the_29_th_line_of_the_picture ),
    .the_32_nd_line_of_the_picture(\рекорды_1_the_32_nd_line_of_the_picture ),
    .the_1_st_line_of_the_picture_2(\рекорды_1_the_1_st_line_of_the_picture_2 ),
    .the_2_nd_line_of_the_picture_2(\рекорды_1_the_2_nd_line_of_the_picture_2 ),
    .the_3_rd_line_of_the_picture_2(\рекорды_1_the_3_rd_line_of_the_picture_2 ),
    .the_4_th_line_of_the_picture_2(\рекорды_1_the_4_th_line_of_the_picture_2 ),
    .the_5_th_line_of_the_picture_2(\рекорды_1_the_5_th_line_of_the_picture_2 ),
    .the_6_th_line_of_the_picture_2(\рекорды_1_the_6_th_line_of_the_picture_2 ),
    .the_7_th_line_of_the_picture_2(\рекорды_1_the_7_th_line_of_the_picture_2 ),
    .the_8_th_line_of_the_picture_2(\рекорды_1_the_8_th_line_of_the_picture_2 ),
    .the_9_th_line_of_the_picture_2(\рекорды_1_the_9_th_line_of_the_picture_2 ),
    .the_10_th_line_of_the_picture_2(\рекорды_1_the_10_th_line_of_the_picture_2 ),
    .the_11_th_line_of_the_picture_2(\рекорды_1_the_11_th_line_of_the_picture_2 ),
    .the_12_th_line_of_the_picture_2(\рекорды_1_the_12_th_line_of_the_picture_2 ),
    .the_13_th_line_of_the_picture_2(\рекорды_1_the_13_th_line_of_the_picture_2 ),
    .the_14_th_line_of_the_picture_2(\рекорды_1_the_14_th_line_of_the_picture_2 ),
    .the_15_th_line_of_the_picture_2(\рекорды_1_the_15_th_line_of_the_picture_2 ),
    .the_16_th_line_of_the_picture_2(\рекорды_1_the_16_th_line_of_the_picture_2 ),
    .the_17_th_line_of_the_picture_2(\рекорды_1_the_17_th_line_of_the_picture_2 ),
    .the_18_th_line_of_the_picture_2(\рекорды_1_the_18_th_line_of_the_picture_2 ),
    .the_19_th_line_of_the_picture_2(\рекорды_1_the_19_th_line_of_the_picture_2 ),
    .the_20_th_line_of_the_picture_2(\рекорды_1_the_20_th_line_of_the_picture_2 ),
    .the_21_st_line_of_the_picture_2(\рекорды_1_the_21_st_line_of_the_picture_2 ),
    .the_22_nd_line_of_the_picture_2(\рекорды_1_the_22_nd_line_of_the_picture_2 ),
    .the_23_rd_line_of_the_picture_2(\рекорды_1_the_23_rd_line_of_the_picture_2 ),
    .the_24_th_line_of_the_picture_2(\рекорды_1_the_24_th_line_of_the_picture_2 ),
    .the_25_th_line_of_the_picture_2(\рекорды_1_the_25_th_line_of_the_picture_2 ),
    .the_26_th_line_of_the_picture_2(\рекорды_1_the_26_th_line_of_the_picture_2 ),
    .the_27_th_line_of_the_picture_2(\рекорды_1_the_27_th_line_of_the_picture_2 ),
    .the_28_th_line_of_the_picture_2(\рекорды_1_the_28_th_line_of_the_picture_2 ),
    .the_29_th_line_of_the_picture_2(\рекорды_1_the_29_th_line_of_the_picture_2 ),
    .the_30_th_line_of_the_picture_2(\рекорды_1_the_30_th_line_of_the_picture_2 ),
    .the_31_st_line_of_the_picture_2(\рекорды_1_the_31_st_line_of_the_picture_2 ),
    .the_32_nd_line_of_the_picture_2(\рекорды_1_the_32_nd_line_of_the_picture_2 ));
  \лидеры_cdm_8  \u_лидеры_cdm_8_1  (
    .recent_result(data), .losesignal(signal), .out_4(\лидеры_cdm_8_1_out_4 ),
    .out_9(\лидеры_cdm_8_1_out_9 ), .out_14(\лидеры_cdm_8_1_out_14 ), .out_5(\лидеры_cdm_8_1_out_5 ),
    .out_10(\лидеры_cdm_8_1_out_10 ), .out_15(\лидеры_cdm_8_1_out_15 ), .out_6(\лидеры_cdm_8_1_out_6 ),
    .out_11(\лидеры_cdm_8_1_out_11 ), .out_16(\лидеры_cdm_8_1_out_16 ), .out_7(\лидеры_cdm_8_1_out_7 ),
    .out_12(\лидеры_cdm_8_1_out_12 ), .out_17(\лидеры_cdm_8_1_out_17 ), .out_8(\лидеры_cdm_8_1_out_8 ),
    .out_13(\лидеры_cdm_8_1_out_13 ), .out_18(\лидеры_cdm_8_1_out_18 ), .out_19(\лидеры_cdm_8_1_out_19 ),
    .out_20(\лидеры_cdm_8_1_out_20 ), .out_21(\лидеры_cdm_8_1_out_21 ), .out_22(\лидеры_cdm_8_1_out_22 ),
    .out_23(\лидеры_cdm_8_1_out_23 ), .tact(clock_1_out));
  not not_1 (init, register_1_q);
  D_Flip_Flop d_ff_1 (.clk(clock_1_out), .D(comparator_1_eq), .Q(d_ff_1_q), .en(1'b1));  // open: Qn, preset, reset
  Counter #(.width(3), .max('h6), .ongoal("stay")) counter_2 (
    .count(init), .Q(counter_2_q), .carry(counter_2_carry), .clk(t_ff_1_q));  // open: load, D, clr
  Comparator #(.width(10)) comparator_1 (.a(counter_1_q), .b(10'h63), .eq(comparator_1_eq));  // open: gt, lt
  \счетчик  \u_счетчик_1  (.clock(and_1_out), .count4(count4), .count3(count3), .count2(count2), .count1(count1));
  and and_1 (and_1_out, clock_dino, ~game_over);  // AND_Gate
  DotMatrix #(.inputtype("row"), .matrixcols(32), .matrixrows(32)) dotmatrix_2 (
    .row0(\клавиатура_1_out_81 ), .row1(\клавиатура_1_out_82 ), .row2(\клавиатура_1_out_83 ),
    .row3(\клавиатура_1_out_84 ), .row4(\клавиатура_1_out_85 ), .row5(\клавиатура_1_out_86 ),
    .row6(\клавиатура_1_out_87 ), .row7(\клавиатура_1_out_88 ), .row8(\клавиатура_1_out_89 ),
    .row9(\клавиатура_1_out_90 ), .row10(\клавиатура_1_out_91 ), .row11(\клавиатура_1_out_92 ),
    .row12(\клавиатура_1_out_93 ), .row13(\клавиатура_1_out_94 ), .row14(\клавиатура_1_out_95 ),
    .row15(\клавиатура_1_out_96 ), .row16(\клавиатура_1_out_97 ), .row17(\клавиатура_1_out_98 ),
    .row18(\клавиатура_1_out_99 ), .row19(\клавиатура_1_out_100 ), .row20(\клавиатура_1_out_101 ),
    .row21(\клавиатура_1_out_102 ), .row22(\клавиатура_1_out_103 ), .row23(\клавиатура_1_out_104 ),
    .row24(\клавиатура_1_out_105 ), .row25(\клавиатура_1_out_106 ), .row26(\клавиатура_1_out_107 ),
    .row27(\клавиатура_1_out_108 ), .row28(\клавиатура_1_out_109 ), .row29(\клавиатура_1_out_110 ),
    .row30(\клавиатура_1_out_111 ), .row31(\клавиатура_1_out_112 ));
  DotMatrix #(.inputtype("row"), .matrixcols(32), .matrixrows(3)) dotmatrix_3 (
    .row0(\клавиатура_1_out_113 ), .row1(\клавиатура_1_out_114 ), .row2(\клавиатура_1_out_115 ));
  Hex_Digit_Display hex_digit_display_1 (.value(\лидеры_cdm_8_1_out_8 ));  // open: dp
  Hex_Digit_Display hex_digit_display_2 (.value(\лидеры_cdm_8_1_out_13 ));  // open: dp
  Hex_Digit_Display hex_digit_display_3 (.value(\лидеры_cdm_8_1_out_18 ));  // open: dp
  and and_2 (clock_img, ~init, clock_1_out);  // AND_Gate
  or or_1 (signal, game_over, jmpuls);
  T_Flip_Flop t_ff_1 (.clk(comparator_1_eq), .T(1'b1), .Q(t_ff_1_q), .en(1'b1));  // open: Qn, preset, reset
  Hex_Digit_Display hex_digit_display_4 (.value(\лидеры_cdm_8_1_out_6 ));  // open: dp
  Hex_Digit_Display hex_digit_display_5 (.value(\лидеры_cdm_8_1_out_7 ));  // open: dp
  Hex_Digit_Display hex_digit_display_6 (.value(\лидеры_cdm_8_1_out_11 ));  // open: dp
  Hex_Digit_Display hex_digit_display_7 (.value(\лидеры_cdm_8_1_out_12 ));  // open: dp
  Hex_Digit_Display hex_digit_display_8 (.value(\лидеры_cdm_8_1_out_16 ));  // open: dp
  Hex_Digit_Display hex_digit_display_9 (.value(\лидеры_cdm_8_1_out_17 ));  // open: dp
  Comparator #(.width(3)) comparator_2 (.a(counter_2_q), .b(3'b001), .eq(comparator_2_eq));  // open: gt, lt
  Comparator #(.width(3)) comparator_3 (.a(counter_2_q), .b(3'b011), .eq(comparator_3_eq));  // open: gt, lt
  Comparator #(.width(3)) comparator_4 (.a(counter_2_q), .b(3'b101), .eq(comparator_4_eq));  // open: gt, lt
  DotMatrix #(.inputtype("row"), .matrixcols(32), .matrixrows(31)) dotmatrix_4 (
    .row0(\рекорды_1_the_2_nd_line_of_the_picture_2 ), .row1(\рекорды_1_the_3_rd_line_of_the_picture_2 ),
    .row2(\рекорды_1_the_4_th_line_of_the_picture_2 ), .row3(\рекорды_1_the_5_th_line_of_the_picture_2 ),
    .row4(\рекорды_1_the_6_th_line_of_the_picture_2 ), .row5(\рекорды_1_the_7_th_line_of_the_picture_2 ),
    .row6(\рекорды_1_the_8_th_line_of_the_picture_2 ), .row7(\рекорды_1_the_9_th_line_of_the_picture_2 ),
    .row8(\рекорды_1_the_10_th_line_of_the_picture_2 ), .row9(\рекорды_1_the_11_th_line_of_the_picture_2 ),
    .row10(\рекорды_1_the_12_th_line_of_the_picture_2 ), .row11(\рекорды_1_the_13_th_line_of_the_picture_2 ),
    .row12(\рекорды_1_the_14_th_line_of_the_picture_2 ), .row13(\рекорды_1_the_15_th_line_of_the_picture_2 ),
    .row14(\рекорды_1_the_16_th_line_of_the_picture_2 ), .row15(\рекорды_1_the_17_th_line_of_the_picture_2 ),
    .row16(\рекорды_1_the_18_th_line_of_the_picture_2 ), .row17(\рекорды_1_the_19_th_line_of_the_picture_2 ),
    .row18(\рекорды_1_the_20_th_line_of_the_picture_2 ), .row19(\рекорды_1_the_21_st_line_of_the_picture_2 ),
    .row20(\рекорды_1_the_22_nd_line_of_the_picture_2 ), .row21(\рекорды_1_the_23_rd_line_of_the_picture_2 ),
    .row22(\рекорды_1_the_24_th_line_of_the_picture_2 ), .row23(\рекорды_1_the_25_th_line_of_the_picture_2 ),
    .row24(\рекорды_1_the_26_th_line_of_the_picture_2 ), .row25(\рекорды_1_the_27_th_line_of_the_picture_2 ),
    .row26(\рекорды_1_the_28_th_line_of_the_picture_2 ), .row27(\рекорды_1_the_29_th_line_of_the_picture_2 ),
    .row28(\рекорды_1_the_30_th_line_of_the_picture_2 ), .row29(\рекорды_1_the_31_st_line_of_the_picture_2 ),
    .row30(\рекорды_1_the_32_nd_line_of_the_picture_2 ));
  Hex_Digit_Display hex_digit_display_10 (.value(\лидеры_cdm_8_1_out_5 ));  // open: dp
  Hex_Digit_Display hex_digit_display_11 (.value(\лидеры_cdm_8_1_out_10 ));  // open: dp
  Hex_Digit_Display hex_digit_display_12 (.value(\лидеры_cdm_8_1_out_15 ));  // open: dp
  or or_2 (jmpuls, comparator_2_eq, comparator_3_eq, comparator_4_eq);
  Hex_Digit_Display hex_digit_display_13 (.value(\лидеры_cdm_8_1_out_4 ));  // open: dp
  Hex_Digit_Display hex_digit_display_14 (.value(\лидеры_cdm_8_1_out_9 ));  // open: dp
  Hex_Digit_Display hex_digit_display_15 (.value(\лидеры_cdm_8_1_out_14 ));  // open: dp
  DotMatrix #(.inputtype("row"), .matrixcols(32), .matrixrows(32)) dotmatrix_5 (
    .row0(\клавиатура_1__1_2 ), .row1(\клавиатура_1_out_47 ), .row2(\клавиатура_1_out_48 ),
    .row3(\клавиатура_1_out_49 ), .row4(\клавиатура_1_out_50 ), .row5(\клавиатура_1_out_51 ),
    .row6(\клавиатура_1_out_52 ), .row7(\клавиатура_1_out_53 ), .row8(\клавиатура_1_out_54 ),
    .row9(\клавиатура_1_out_55 ), .row10(\клавиатура_1_out_56 ), .row11(\клавиатура_1_out_57 ),
    .row12(\клавиатура_1_out_58 ), .row13(\клавиатура_1_out_59 ), .row14(\клавиатура_1_out_60 ),
    .row15(\клавиатура_1_out_61 ), .row16(\клавиатура_1_out_62 ), .row17(\клавиатура_1_out_63 ),
    .row18(\клавиатура_1_out_64 ), .row19(\клавиатура_1_out_65 ), .row20(\клавиатура_1_out_66 ),
    .row21(\клавиатура_1_out_67 ), .row22(\клавиатура_1_out_68 ), .row23(\клавиатура_1_out_69 ),
    .row24(\клавиатура_1_out_70 ), .row25(\клавиатура_1_out_71 ), .row26(\клавиатура_1_out_72 ),
    .row27(\клавиатура_1_out_73 ), .row28(\клавиатура_1_out_74 ), .row29(\клавиатура_1_out_75 ),
    .row30(\клавиатура_1_out_76 ), .row31(\клавиатура_1_out_77 ));
  DotMatrix #(.inputtype("row"), .matrixcols(32), .matrixrows(3)) dotmatrix_6 (
    .row0(\клавиатура_1_out_78 ), .row1(\клавиатура_1_out_79 ), .row2(\клавиатура_1_out_80 ));
  \очки  \u_очки_1  (.clock(clock), .game_over(game_over), .rest(rest), .out_4(\очки_1_out_4 ));
  Multiplexer #(.width(14)) multiplexer_1 (
    .in0(14'h5), .in1(14'h1), .out(multiplexer_1_out), .sel(comparator_2_eq), .en(1'b1));
  Multiplexer #(.width(14)) multiplexer_2 (
    .in0(\очки_1_out_4 ), .in1(multiplexer_3_out), .out(data), .sel(init), .en(1'b1));
  Multiplexer #(.width(14)) multiplexer_3 (
    .in0(multiplexer_1_out), .in1(14'h7), .out(multiplexer_3_out), .sel(comparator_4_eq), .en(1'b1));
  DotMatrix #(.inputtype("row"), .matrixcols(32), .matrixrows(31)) dotmatrix_7 (
    .row0(\текущие_очки_1_the_1_st_line_of_the_picture ),
    .row1(\текущие_очки_1_the_2_nd_line_of_the_picture ),
    .row2(\текущие_очки_1_the_3_rd_line_of_the_picture ),
    .row3(\текущие_очки_1_the_4_th_line_of_the_picture ),
    .row4(\текущие_очки_1_the_5_th_line_of_the_picture ),
    .row5(\текущие_очки_1_the_6_th_line_of_the_picture ),
    .row6(\текущие_очки_1_the_7_th_line_of_the_picture ),
    .row7(\текущие_очки_1_the_8_th_line_of_the_picture ),
    .row8(\текущие_очки_1_the_9_th_line_of_the_picture ),
    .row9(\текущие_очки_1_the_10_th_line_of_the_picture ),
    .row10(\текущие_очки_1_the_11_th_line_of_the_picture ),
    .row11(\текущие_очки_1_the_12_th_line_of_the_picture ),
    .row12(\текущие_очки_1_the_13_th_line_of_the_picture ),
    .row13(\текущие_очки_1_the_14_th_line_of_the_picture ),
    .row14(\текущие_очки_1_the_15_th_line_of_the_picture ),
    .row15(\текущие_очки_1_the_16_th_line_of_the_picture ),
    .row16(\текущие_очки_1_the_17_th_line_of_the_picture ),
    .row17(\текущие_очки_1_the_18_th_line_of_the_picture ),
    .row18(\текущие_очки_1_the_19_th_line_of_the_picture ),
    .row19(\текущие_очки_1_the_20_th_line_of_the_picture ),
    .row20(\текущие_очки_1_the_21_st_line_of_the_picture ),
    .row21(\текущие_очки_1_the_22_nd_line_of_the_picture ),
    .row22(\текущие_очки_1_the_23_rd_line_of_the_picture ),
    .row23(\текущие_очки_1_the_24_th_line_of_the_picture ),
    .row24(\текущие_очки_1_the_25_th_line_of_the_picture ),
    .row25(\текущие_очки_1_the_26_th_line_of_the_picture ),
    .row26(\текущие_очки_1_the_27_th_line_of_the_picture ),
    .row27(\текущие_очки_1_the_28_th_line_of_the_picture ),
    .row28(\текущие_очки_1_the_29_th_line_of_the_picture ),
    .row29(\текущие_очки_1_the_30_th_line_of_the_picture ),
    .row30(\текущие_очки_1_the_31_st_line_of_the_picture ));
  \текущие_очки  \u_текущие_очки_1  (
    .the_1_st_line_of_the_picture(\текущие_очки_1_the_1_st_line_of_the_picture ),
    .the_2_nd_line_of_the_picture(\текущие_очки_1_the_2_nd_line_of_the_picture ),
    .the_3_rd_line_of_the_picture(\текущие_очки_1_the_3_rd_line_of_the_picture ),
    .the_4_th_line_of_the_picture(\текущие_очки_1_the_4_th_line_of_the_picture ),
    .the_5_th_line_of_the_picture(\текущие_очки_1_the_5_th_line_of_the_picture ),
    .the_6_th_line_of_the_picture(\текущие_очки_1_the_6_th_line_of_the_picture ),
    .the_7_th_line_of_the_picture(\текущие_очки_1_the_7_th_line_of_the_picture ),
    .the_8_th_line_of_the_picture(\текущие_очки_1_the_8_th_line_of_the_picture ),
    .the_9_th_line_of_the_picture(\текущие_очки_1_the_9_th_line_of_the_picture ),
    .the_10_th_line_of_the_picture(\текущие_очки_1_the_10_th_line_of_the_picture ),
    .the_11_th_line_of_the_picture(\текущие_очки_1_the_11_th_line_of_the_picture ),
    .the_12_th_line_of_the_picture(\текущие_очки_1_the_12_th_line_of_the_picture ),
    .the_13_th_line_of_the_picture(\текущие_очки_1_the_13_th_line_of_the_picture ),
    .the_14_th_line_of_the_picture(\текущие_очки_1_the_14_th_line_of_the_picture ),
    .the_15_th_line_of_the_picture(\текущие_очки_1_the_15_th_line_of_the_picture ),
    .the_16_th_line_of_the_picture(\текущие_очки_1_the_16_th_line_of_the_picture ),
    .the_17_th_line_of_the_picture(\текущие_очки_1_the_17_th_line_of_the_picture ),
    .the_18_th_line_of_the_picture(\текущие_очки_1_the_18_th_line_of_the_picture ),
    .the_19_th_line_of_the_picture(\текущие_очки_1_the_19_th_line_of_the_picture ),
    .the_20_th_line_of_the_picture(\текущие_очки_1_the_20_th_line_of_the_picture ),
    .the_21_st_line_of_the_picture(\текущие_очки_1_the_21_st_line_of_the_picture ),
    .the_22_nd_line_of_the_picture(\текущие_очки_1_the_22_nd_line_of_the_picture ),
    .the_23_rd_line_of_the_picture(\текущие_очки_1_the_23_rd_line_of_the_picture ),
    .the_24_th_line_of_the_picture(\текущие_очки_1_the_24_th_line_of_the_picture ),
    .the_25_th_line_of_the_picture(\текущие_очки_1_the_25_th_line_of_the_picture ),
    .the_26_th_line_of_the_picture(\текущие_очки_1_the_26_th_line_of_the_picture ),
    .the_27_th_line_of_the_picture(\текущие_очки_1_the_27_th_line_of_the_picture ),
    .the_28_th_line_of_the_picture(\текущие_очки_1_the_28_th_line_of_the_picture ),
    .the_29_th_line_of_the_picture(\текущие_очки_1_the_29_th_line_of_the_picture ),
    .the_30_th_line_of_the_picture(\текущие_очки_1_the_30_th_line_of_the_picture ),
    .the_31_st_line_of_the_picture(\текущие_очки_1_the_31_st_line_of_the_picture ),
    .the_1_st_line_of_the_picture_2(\текущие_очки_1_the_1_st_line_of_the_picture_2 ),
    .the_2_nd_line_of_the_picture_2(\текущие_очки_1_the_2_nd_line_of_the_picture_2 ),
    .the_3_rd_line_of_the_picture_2(\текущие_очки_1_the_3_rd_line_of_the_picture_2 ),
    .the_4_th_line_of_the_picture_2(\текущие_очки_1_the_4_th_line_of_the_picture_2 ),
    .the_5_th_line_of_the_picture_2(\текущие_очки_1_the_5_th_line_of_the_picture_2 ),
    .the_6_th_line_of_the_picture_2(\текущие_очки_1_the_6_th_line_of_the_picture_2 ),
    .the_7_th_line_of_the_picture_2(\текущие_очки_1_the_7_th_line_of_the_picture_2 ),
    .the_8_th_line_of_the_picture_2(\текущие_очки_1_the_8_th_line_of_the_picture_2 ),
    .the_9_th_line_of_the_picture_2(\текущие_очки_1_the_9_th_line_of_the_picture_2 ),
    .the_10_th_line_of_the_picture_2(\текущие_очки_1_the_10_th_line_of_the_picture_2 ),
    .the_11_th_line_of_the_picture_2(\текущие_очки_1_the_11_th_line_of_the_picture_2 ),
    .the_12_th_line_of_the_picture_2(\текущие_очки_1_the_12_th_line_of_the_picture_2 ),
    .the_13_th_line_of_the_picture_2(\текущие_очки_1_the_13_th_line_of_the_picture_2 ),
    .the_14_th_line_of_the_picture_2(\текущие_очки_1_the_14_th_line_of_the_picture_2 ),
    .the_15_th_line_of_the_picture_2(\текущие_очки_1_the_15_th_line_of_the_picture_2 ),
    .the_16_th_line_of_the_picture_2(\текущие_очки_1_the_16_th_line_of_the_picture_2 ),
    .the_17_th_line_of_the_picture_2(\текущие_очки_1_the_17_th_line_of_the_picture_2 ),
    .the_18_th_line_of_the_picture_2(\текущие_очки_1_the_18_th_line_of_the_picture_2 ),
    .the_19_th_line_of_the_picture_2(\текущие_очки_1_the_19_th_line_of_the_picture_2 ),
    .the_20_th_line_of_the_picture_2(\текущие_очки_1_the_20_th_line_of_the_picture_2 ),
    .the_21_st_line_of_the_picture_2(\текущие_очки_1_the_21_st_line_of_the_picture_2 ),
    .the_22_nd_line_of_the_picture_2(\текущие_очки_1_the_22_nd_line_of_the_picture_2 ),
    .the_23_rd_line_of_the_picture_2(\текущие_очки_1_the_23_rd_line_of_the_picture_2 ),
    .the_24_th_line_of_the_picture_2(\текущие_очки_1_the_24_th_line_of_the_picture_2 ),
    .the_25_th_line_of_the_picture_2(\текущие_очки_1_the_25_th_line_of_the_picture_2 ),
    .the_26_th_line_of_the_picture_2(\текущие_очки_1_the_26_th_line_of_the_picture_2 ),
    .the_27_th_line_of_the_picture_2(\текущие_очки_1_the_27_th_line_of_the_picture_2 ),
    .the_28_th_line_of_the_picture_2(\текущие_очки_1_the_28_th_line_of_the_picture_2 ),
    .the_29_th_line_of_the_picture_2(\текущие_очки_1_the_29_th_line_of_the_picture_2 ),
    .the_30_th_line_of_the_picture_2(\текущие_очки_1_the_30_th_line_of_the_picture_2 ),
    .the_31_st_line_of_the_picture_2(\текущие_очки_1_the_31_st_line_of_the_picture_2 ));
  DotMatrix #(.inputtype("row"), .matrixcols(32), .matrixrows(32)) dotmatrix_8 (
    .row0(\клавиатура_1__1 ), .row1(\клавиатура_1__2 ), .row2(\клавиатура_1__3 ),
    .row3(\клавиатура_1_out_14 ), .row4(\клавиатура_1_out_15 ), .row5(\клавиатура_1_out_16 ),
    .row6(\клавиатура_1_out_17 ), .row7(\клавиатура_1_out_18 ), .row8(\клавиатура_1_out_19 ),
    .row9(\клавиатура_1_out_20 ), .row10(\клавиатура_1_out_21 ), .row11(\клавиатура_1_out_22 ),
    .row12(\клавиатура_1_out_23 ), .row13(\клавиатура_1_out_24 ), .row14(\клавиатура_1_out_25 ),
    .row15(\клавиатура_1_out_26 ), .row16(\клавиатура_1_out_27 ), .row17(\клавиатура_1_out_28 ),
    .row18(\клавиатура_1_out_29 ), .row19(\клавиатура_1_out_30 ), .row20(\клавиатура_1_out_31 ),
    .row21(\клавиатура_1_out_32 ), .row22(\клавиатура_1_out_33 ), .row23(\клавиатура_1_out_34 ),
    .row24(\клавиатура_1_out_35 ), .row25(\клавиатура_1_out_36 ), .row26(\клавиатура_1_out_37 ),
    .row27(\клавиатура_1_out_38 ), .row28(\клавиатура_1_out_39 ), .row29(\клавиатура_1_out_40 ),
    .row30(\клавиатура_1_out_41 ), .row31(\клавиатура_1_out_42 ));
  DotMatrix #(.inputtype("row"), .matrixcols(32), .matrixrows(3)) dotmatrix_9 (
    .row0(\клавиатура_1_out_43 ), .row1(\клавиатура_1_out_44 ), .row2(\клавиатура_1__35 ));
  Hex_Digit_Display hex_digit_display_16 (.value(\лидеры_cdm_8_1_out_23 ));  // open: dp
  Hex_Digit_Display hex_digit_display_17 (.value(\лидеры_cdm_8_1_out_22 ));  // open: dp
  DotMatrix #(.matrixcols(25), .matrixrows(8)) dotmatrix_10 (
    .col0(\жизни_1_live1 ), .col1(\жизни_1_live2 ), .col2(\жизни_1_live3 ), .col3(\жизни_1_live4 ),
    .col4(\жизни_1_live5 ), .col5(\жизни_1_live6 ), .col6(\жизни_1_live7 ), .col7(\жизни_1_live8 ),
    .col8(\жизни_1_live9 ), .col9(\жизни_1_live10 ), .col10(\жизни_1_live11 ), .col11(\жизни_1_live12 ),
    .col12(\жизни_1_live13 ), .col13(\жизни_1_live14 ), .col14(\жизни_1_live15 ), .col15(\жизни_1_live16 ),
    .col16(\жизни_1_live17 ), .col17(\жизни_1_live18 ), .col18(\жизни_1_live19 ), .col19(\жизни_1_live20 ),
    .col20(\жизни_1_live21 ), .col21(\жизни_1_live22 ), .col22(\жизни_1_live23 ), .col23(\жизни_1_live24 ),
    .col24(\жизни_1_live25 ));
  \жизни  \u_жизни_1  (
    .in_1(\клавиатура_1_lcount ), .live1(\жизни_1_live1 ), .live2(\жизни_1_live2 ), .live3(\жизни_1_live3 ),
    .live4(\жизни_1_live4 ), .live5(\жизни_1_live5 ), .live6(\жизни_1_live6 ), .live7(\жизни_1_live7 ),
    .live8(\жизни_1_live8 ), .live9(\жизни_1_live9 ), .live10(\жизни_1_live10 ), .live11(\жизни_1_live11 ),
    .live12(\жизни_1_live12 ), .live13(\жизни_1_live13 ), .live14(\жизни_1_live14 ),
    .live15(\жизни_1_live15 ), .live16(\жизни_1_live16 ), .live17(\жизни_1_live17 ),
    .live18(\жизни_1_live18 ), .live19(\жизни_1_live19 ), .live20(\жизни_1_live20 ),
    .live21(\жизни_1_live21 ), .live22(\жизни_1_live22 ), .live23(\жизни_1_live23 ),
    .live24(\жизни_1_live24 ), .live25(\жизни_1_live25 ));
  DotMatrix #(.inputtype("row"), .matrixcols(32), .matrixrows(31)) dotmatrix_11 (
    .row0(\текущие_очки_1_the_1_st_line_of_the_picture_2 ),
    .row1(\текущие_очки_1_the_2_nd_line_of_the_picture_2 ),
    .row2(\текущие_очки_1_the_3_rd_line_of_the_picture_2 ),
    .row3(\текущие_очки_1_the_4_th_line_of_the_picture_2 ),
    .row4(\текущие_очки_1_the_5_th_line_of_the_picture_2 ),
    .row5(\текущие_очки_1_the_6_th_line_of_the_picture_2 ),
    .row6(\текущие_очки_1_the_7_th_line_of_the_picture_2 ),
    .row7(\текущие_очки_1_the_8_th_line_of_the_picture_2 ),
    .row8(\текущие_очки_1_the_9_th_line_of_the_picture_2 ),
    .row9(\текущие_очки_1_the_10_th_line_of_the_picture_2 ),
    .row10(\текущие_очки_1_the_11_th_line_of_the_picture_2 ),
    .row11(\текущие_очки_1_the_12_th_line_of_the_picture_2 ),
    .row12(\текущие_очки_1_the_13_th_line_of_the_picture_2 ),
    .row13(\текущие_очки_1_the_14_th_line_of_the_picture_2 ),
    .row14(\текущие_очки_1_the_15_th_line_of_the_picture_2 ),
    .row15(\текущие_очки_1_the_16_th_line_of_the_picture_2 ),
    .row16(\текущие_очки_1_the_17_th_line_of_the_picture_2 ),
    .row17(\текущие_очки_1_the_18_th_line_of_the_picture_2 ),
    .row18(\текущие_очки_1_the_19_th_line_of_the_picture_2 ),
    .row19(\текущие_очки_1_the_20_th_line_of_the_picture_2 ),
    .row20(\текущие_очки_1_the_21_st_line_of_the_picture_2 ),
    .row21(\текущие_очки_1_the_22_nd_line_of_the_picture_2 ),
    .row22(\текущие_очки_1_the_23_rd_line_of_the_picture_2 ),
    .row23(\текущие_очки_1_the_24_th_line_of_the_picture_2 ),
    .row24(\текущие_очки_1_the_25_th_line_of_the_picture_2 ),
    .row25(\текущие_очки_1_the_26_th_line_of_the_picture_2 ),
    .row26(\текущие_очки_1_the_27_th_line_of_the_picture_2 ),
    .row27(\текущие_очки_1_the_28_th_line_of_the_picture_2 ),
    .row28(\текущие_очки_1_the_29_th_line_of_the_picture_2 ),
    .row29(\текущие_очки_1_the_30_th_line_of_the_picture_2 ),
    .row30(\текущие_очки_1_the_31_st_line_of_the_picture_2 ));
  Hex_Digit_Display hex_digit_display_18 (.value(\лидеры_cdm_8_1_out_21 ));  // open: dp
  Hex_Digit_Display hex_digit_display_19 (.value(\лидеры_cdm_8_1_out_20 ));  // open: dp
  Hex_Digit_Display hex_digit_display_20 (.value(\лидеры_cdm_8_1_out_19 ));  // open: dp
endmodule

module \рекорды  (
  output [31:0] the_1_st_line_of_the_picture,
  output [31:0] the_2_nd_line_of_the_picture,
  output [31:0] the_3_rd_line_of_the_picture,
  output [31:0] the_4_th_line_of_the_picture,
  output [31:0] the_5_th_line_of_the_picture,
  output [31:0] the_6_th_line_of_the_picture,
  output [31:0] the_7_th_line_of_the_picture,
  output [31:0] the_8_th_line_of_the_picture,
  output [31:0] the_9_th_line_of_the_picture,
  output [31:0] the_10_th_line_of_the_picture,
  output [31:0] the_11_th_line_of_the_picture,
  output [31:0] the_12_th_line_of_the_picture,
  output [31:0] the_13_th_line_of_the_picture,
  output [31:0] the_14_th_line_of_the_picture,
  output [31:0] the_15_th_line_of_the_picture,
  output [31:0] the_16_th_line_of_the_picture,
  output [31:0] the_17_th_line_of_the_picture,
  output [31:0] the_18_th_line_of_the_picture,
  output [31:0] the_19_th_line_of_the_picture,
  output [31:0] the_20_th_line_of_the_picture,
  output [31:0] the_21_st_line_of_the_picture,
  output [31:0] the_22_nd_line_of_the_picture,
  output [31:0] the_23_rd_line_of_the_picture,
  output [31:0] the_24_th_line_of_the_picture,
  output [31:0] the_25_th_line_of_the_picture,
  output [31:0] the_26_th_line_of_the_picture,
  output [31:0] the_27_th_line_of_the_picture,
  output [31:0] the_28_th_line_of_the_picture,
  output [31:0] the_29_th_line_of_the_picture,
  output [31:0] the_30_th_line_of_the_picture,
  output [31:0] the_31_st_line_of_the_picture,
  output [31:0] the_32_nd_line_of_the_picture,
  output [31:0] the_1_st_line_of_the_picture_2,
  output [31:0] the_2_nd_line_of_the_picture_2,
  output [31:0] the_3_rd_line_of_the_picture_2,
  output [31:0] the_4_th_line_of_the_picture_2,
  output [31:0] the_5_th_line_of_the_picture_2,
  output [31:0] the_6_th_line_of_the_picture_2,
  output [31:0] the_7_th_line_of_the_picture_2,
  output [31:0] the_8_th_line_of_the_picture_2,
  output [31:0] the_9_th_line_of_the_picture_2,
  output [31:0] the_10_th_line_of_the_picture_2,
  output [31:0] the_11_th_line_of_the_picture_2,
  output [31:0] the_12_th_line_of_the_picture_2,
  output [31:0] the_13_th_line_of_the_picture_2,
  output [31:0] the_14_th_line_of_the_picture_2,
  output [31:0] the_15_th_line_of_the_picture_2,
  output [31:0] the_16_th_line_of_the_picture_2,
  output [31:0] the_17_th_line_of_the_picture_2,
  output [31:0] the_18_th_line_of_the_picture_2,
  output [31:0] the_19_th_line_of_the_picture_2,
  output [31:0] the_20_th_line_of_the_picture_2,
  output [31:0] the_21_st_line_of_the_picture_2,
  output [31:0] the_22_nd_line_of_the_picture_2,
  output [31:0] the_23_rd_line_of_the_picture_2,
  output [31:0] the_24_th_line_of_the_picture_2,
  output [31:0] the_25_th_line_of_the_picture_2,
  output [31:0] the_26_th_line_of_the_picture_2,
  output [31:0] the_27_th_line_of_the_picture_2,
  output [31:0] the_28_th_line_of_the_picture_2,
  output [31:0] the_29_th_line_of_the_picture_2,
  output [31:0] the_30_th_line_of_the_picture_2,
  output [31:0] the_31_st_line_of_the_picture_2,
  output [31:0] the_32_nd_line_of_the_picture_2
);

  DotMatrix #(.inputtype("row"), .matrixcols(32), .matrixrows(32)) dotmatrix_1 (
    .row0({32{1'b0}}), .row1(32'h3e07e1f0), .row2(32'h7f8ff1f0), .row3(32'h71dff3f8), .row4(32'h60dfe3b8),
    .row5(32'h60dc071c), .row6(32'h60dc070d), .row7(32'h719fee01), .row8(32'h7f1fce01), .row9(32'h7e1c070d),
    .row10(32'h7c1c071c), .row11(32'h6e1fe3b8), .row12(32'h6e5ff3f8), .row13(32'h679ff1f0),
    .row14(32'h630fe1f0), .row15({32{1'b0}}), .row16({32{1'b0}}), .row17(32'hf81f007), .row18(32'h1fc1f01f),
    .row19(32'h3fe3f83f), .row20(32'h38e3b87c), .row21(32'h3c671cf8), .row22(32'h1e270cf8),
    .row23(32'hf0e01f0), .row24(32'h78e01f0), .row25(32'h43c70cf8), .row26(32'h61e71cf8),
    .row27(32'h70e3b87c), .row28(32'h79e3f83f), .row29(32'h3fe1f01f), .row30(32'h1fc1f007), .row31({32{1'b0}}));
  DotMatrix #(.inputtype("row"), .matrixcols(32), .matrixrows(32)) dotmatrix_2 (
    .row0({32{1'b0}}), .row1(32'h1f03e1f0), .row2(32'h3f87f9f8), .row3(32'h7fc71d98), .row4(32'hffe60d8c),
    .row5(32'hf1e60d8c), .row6(32'he0f60d86), .row7(32'hc0771986), .row8(32'hc077f186), .row9(32'he0f7e186),
    .row10(32'hf1e7c18c), .row11(32'hffe6e18c), .row12(32'h7fc6e598), .row13(32'h3f8679f8),
    .row14(32'h1f0631f0), .row15({32{1'b0}}), .row16({32{1'b0}}), .row17(32'he01f81fc), .row18(32'hf83fe3fe),
    .row19(32'hfc3c77fe), .row20(32'h3e3837fc), .row21(32'h1f383780), .row22(32'h1f383780),
    .row23(32'hfbc67fc), .row24(32'hfbfc7f8), .row25(32'h1f3f8780), .row26(32'h1f3f0780),
    .row27(32'h3e3b87fc), .row28(32'hfc3b97fe), .row29(32'hf839e7fe), .row30(32'he038c3fc), .row31({32{1'b0}}));

  assign the_1_st_line_of_the_picture = {32{1'b0}};
  assign the_1_st_line_of_the_picture_2 = {32{1'b0}};
  assign the_2_nd_line_of_the_picture = 32'h3e07e1f0;
  assign the_2_nd_line_of_the_picture_2 = 32'h1f03e1f0;
  assign the_3_rd_line_of_the_picture = 32'h7f8ff1f0;
  assign the_3_rd_line_of_the_picture_2 = 32'h3f87f9f8;
  assign the_4_th_line_of_the_picture = 32'h71dff3f8;
  assign the_4_th_line_of_the_picture_2 = 32'h7fc71d98;
  assign the_5_th_line_of_the_picture = 32'h60dfe3b8;
  assign the_5_th_line_of_the_picture_2 = 32'hffe60d8c;
  assign the_6_th_line_of_the_picture = 32'h60dc071c;
  assign the_6_th_line_of_the_picture_2 = 32'hf1e60d8c;
  assign the_7_th_line_of_the_picture = 32'h60dc070d;
  assign the_7_th_line_of_the_picture_2 = 32'he0f60d86;
  assign the_8_th_line_of_the_picture = 32'h719fee01;
  assign the_8_th_line_of_the_picture_2 = 32'hc0771986;
  assign the_9_th_line_of_the_picture = 32'h7f1fce01;
  assign the_9_th_line_of_the_picture_2 = 32'hc077f186;
  assign the_10_th_line_of_the_picture = 32'h7e1c070d;
  assign the_10_th_line_of_the_picture_2 = 32'he0f7e186;
  assign the_11_th_line_of_the_picture = 32'h7c1c071c;
  assign the_11_th_line_of_the_picture_2 = 32'hf1e7c18c;
  assign the_12_th_line_of_the_picture = 32'h6e1fe3b8;
  assign the_12_th_line_of_the_picture_2 = 32'hffe6e18c;
  assign the_13_th_line_of_the_picture = 32'h6e5ff3f8;
  assign the_13_th_line_of_the_picture_2 = 32'h7fc6e598;
  assign the_14_th_line_of_the_picture = 32'h679ff1f0;
  assign the_14_th_line_of_the_picture_2 = 32'h3f8679f8;
  assign the_15_th_line_of_the_picture = 32'h630fe1f0;
  assign the_15_th_line_of_the_picture_2 = 32'h1f0631f0;
  assign the_16_th_line_of_the_picture = {32{1'b0}};
  assign the_16_th_line_of_the_picture_2 = {32{1'b0}};
  assign the_17_th_line_of_the_picture = {32{1'b0}};
  assign the_17_th_line_of_the_picture_2 = {32{1'b0}};
  assign the_18_th_line_of_the_picture = 32'hf81f007;
  assign the_18_th_line_of_the_picture_2 = 32'he01f81fc;
  assign the_19_th_line_of_the_picture = 32'h1fc1f01f;
  assign the_19_th_line_of_the_picture_2 = 32'hf83fe3fe;
  assign the_20_th_line_of_the_picture = 32'h3fe3f83f;
  assign the_20_th_line_of_the_picture_2 = 32'hfc3c77fe;
  assign the_21_st_line_of_the_picture = 32'h38e3b87c;
  assign the_21_st_line_of_the_picture_2 = 32'h3e3837fc;
  assign the_22_nd_line_of_the_picture = 32'h3c671cf8;
  assign the_22_nd_line_of_the_picture_2 = 32'h1f383780;
  assign the_23_rd_line_of_the_picture = 32'h1e270cf8;
  assign the_23_rd_line_of_the_picture_2 = 32'h1f383780;
  assign the_24_th_line_of_the_picture = 32'hf0e01f0;
  assign the_24_th_line_of_the_picture_2 = 32'hfbc67fc;
  assign the_25_th_line_of_the_picture = 32'h78e01f0;
  assign the_25_th_line_of_the_picture_2 = 32'hfbfc7f8;
  assign the_26_th_line_of_the_picture = 32'h43c70cf8;
  assign the_26_th_line_of_the_picture_2 = 32'h1f3f8780;
  assign the_27_th_line_of_the_picture = 32'h61e71cf8;
  assign the_27_th_line_of_the_picture_2 = 32'h1f3f0780;
  assign the_28_th_line_of_the_picture = 32'h70e3b87c;
  assign the_28_th_line_of_the_picture_2 = 32'h3e3b87fc;
  assign the_29_th_line_of_the_picture = 32'h79e3f83f;
  assign the_29_th_line_of_the_picture_2 = 32'hfc3b97fe;
  assign the_30_th_line_of_the_picture = 32'h3fe1f01f;
  assign the_30_th_line_of_the_picture_2 = 32'hf839e7fe;
  assign the_31_st_line_of_the_picture = 32'h1fc1f007;
  assign the_31_st_line_of_the_picture_2 = 32'he038c3fc;
  assign the_32_nd_line_of_the_picture = {32{1'b0}};
  assign the_32_nd_line_of_the_picture_2 = {32{1'b0}};
endmodule

module \текущие_очки  (
  output [31:0] the_1_st_line_of_the_picture,
  output [31:0] the_2_nd_line_of_the_picture,
  output [31:0] the_3_rd_line_of_the_picture,
  output [31:0] the_4_th_line_of_the_picture,
  output [31:0] the_5_th_line_of_the_picture,
  output [31:0] the_6_th_line_of_the_picture,
  output [31:0] the_7_th_line_of_the_picture,
  output [31:0] the_8_th_line_of_the_picture,
  output [31:0] the_9_th_line_of_the_picture,
  output [31:0] the_10_th_line_of_the_picture,
  output [31:0] the_11_th_line_of_the_picture,
  output [31:0] the_12_th_line_of_the_picture,
  output [31:0] the_13_th_line_of_the_picture,
  output [31:0] the_14_th_line_of_the_picture,
  output [31:0] the_15_th_line_of_the_picture,
  output [31:0] the_16_th_line_of_the_picture,
  output [31:0] the_17_th_line_of_the_picture,
  output [31:0] the_18_th_line_of_the_picture,
  output [31:0] the_19_th_line_of_the_picture,
  output [31:0] the_20_th_line_of_the_picture,
  output [31:0] the_21_st_line_of_the_picture,
  output [31:0] the_22_nd_line_of_the_picture,
  output [31:0] the_23_rd_line_of_the_picture,
  output [31:0] the_24_th_line_of_the_picture,
  output [31:0] the_25_th_line_of_the_picture,
  output [31:0] the_26_th_line_of_the_picture,
  output [31:0] the_27_th_line_of_the_picture,
  output [31:0] the_28_th_line_of_the_picture,
  output [31:0] the_29_th_line_of_the_picture,
  output [31:0] the_30_th_line_of_the_picture,
  output [31:0] the_31_st_line_of_the_picture,
  output [31:0] the_1_st_line_of_the_picture_2,
  output [31:0] the_2_nd_line_of_the_picture_2,
  output [31:0] the_3_rd_line_of_the_picture_2,
  output [31:0] the_4_th_line_of_the_picture_2,
  output [31:0] the_5_th_line_of_the_picture_2,
  output [31:0] the_6_th_line_of_the_picture_2,
  output [31:0] the_7_th_line_of_the_picture_2,
  output [31:0] the_8_th_line_of_the_picture_2,
  output [31:0] the_9_th_line_of_the_picture_2,
  output [31:0] the_10_th_line_of_the_picture_2,
  output [31:0] the_11_th_line_of_the_picture_2,
  output [31:0] the_12_th_line_of_the_picture_2,
  output [31:0] the_13_th_line_of_the_picture_2,
  output [31:0] the_14_th_line_of_the_picture_2,
  output [31:0] the_15_th_line_of_the_picture_2,
  output [31:0] the_16_th_line_of_the_picture_2,
  output [31:0] the_17_th_line_of_the_picture_2,
  output [31:0] the_18_th_line_of_the_picture_2,
  output [31:0] the_19_th_line_of_the_picture_2,
  output [31:0] the_20_th_line_of_the_picture_2,
  output [31:0] the_21_st_line_of_the_picture_2,
  output [31:0] the_22_nd_line_of_the_picture_2,
  output [31:0] the_23_rd_line_of_the_picture_2,
  output [31:0] the_24_th_line_of_the_picture_2,
  output [31:0] the_25_th_line_of_the_picture_2,
  output [31:0] the_26_th_line_of_the_picture_2,
  output [31:0] the_27_th_line_of_the_picture_2,
  output [31:0] the_28_th_line_of_the_picture_2,
  output [31:0] the_29_th_line_of_the_picture_2,
  output [31:0] the_30_th_line_of_the_picture_2,
  output [31:0] the_31_st_line_of_the_picture_2
);

  DotMatrix #(.inputtype("row"), .matrixcols(32), .matrixrows(32)) dotmatrix_1 (
    .row0({32{1'b0}}), .row1(32'he663e0f), .row2(32'he777f9f), .row3(32'h1f3371dc), .row4(32'h1b3360d8),
    .row5(32'h31b360d8), .row6(32'h30b360d8), .row7(32'h6033719c), .row8(32'h60337f1f), .row9(32'h30b37e1f),
    .row10(32'h31b37c1f), .row11(32'h1b336e1b), .row12(32'h1f3f6e5b), .row13(32'he3f6799),
    .row14(32'he1e6318), .row15({32{1'b0}}), .row16({32{1'b0}}), .row17(32'hf81f007), .row18(32'h1fc1f01f),
    .row19(32'h3fe3f83f), .row20(32'h38e3b87c), .row21(32'h3c671cf8), .row22(32'h1e270cf8),
    .row23(32'hf0e01f0), .row24(32'h78e01f0), .row25(32'h43c70cf8), .row26(32'h61e71cf8),
    .row27(32'h70e3b87c), .row28(32'h79e3f83f), .row29(32'h3fe1f01f), .row30(32'h1fc1f007), .row31({32{1'b0}}));
  DotMatrix #(.inputtype("row"), .matrixcols(32), .matrixrows(32)) dotmatrix_2 (
    .row0({32{1'b0}}), .row1(32'h81f33d00), .row2(32'he3fb9dc0), .row3(32'h77fb8dfc), .row4(32'h37f3ccfe),
    .row5(32'h3703cc3e), .row6(32'h3703ec30), .row7(32'h67f36c30), .row8(32'hc7e37c30), .row9(32'h87033c30),
    .row10(32'h7033c30), .row11(32'h87f31c30), .row12(32'h17fb1c30), .row13(32'he7fb8c30),
    .row14(32'hc3f3cc30), .row15({32{1'b0}}), .row16({32{1'b0}}), .row17(32'he01f81fc), .row18(32'hf83fe3fe),
    .row19(32'hfc3c77fe), .row20(32'h3e3837fc), .row21(32'h1f383780), .row22(32'h1f383780),
    .row23(32'hfbc67fc), .row24(32'hfbfc7f8), .row25(32'h1f3f8780), .row26(32'h1f3f0780),
    .row27(32'h3e3b87fc), .row28(32'hfc3b97fe), .row29(32'hf839e7fe), .row30(32'he038c3fc), .row31({32{1'b0}}));

  assign the_1_st_line_of_the_picture = {32{1'b0}};
  assign the_1_st_line_of_the_picture_2 = {32{1'b0}};
  assign the_2_nd_line_of_the_picture = 32'he663e0f;
  assign the_2_nd_line_of_the_picture_2 = 32'h81f33d00;
  assign the_3_rd_line_of_the_picture = 32'he777f9f;
  assign the_3_rd_line_of_the_picture_2 = 32'he3fb9dc0;
  assign the_4_th_line_of_the_picture = 32'h1f3371dc;
  assign the_4_th_line_of_the_picture_2 = 32'h77fb8dfc;
  assign the_5_th_line_of_the_picture = 32'h1b3360d8;
  assign the_5_th_line_of_the_picture_2 = 32'h37f3ccfe;
  assign the_6_th_line_of_the_picture = 32'h31b360d8;
  assign the_6_th_line_of_the_picture_2 = 32'h3703cc3e;
  assign the_7_th_line_of_the_picture = 32'h30b360d8;
  assign the_7_th_line_of_the_picture_2 = 32'h3703ec30;
  assign the_8_th_line_of_the_picture = 32'h6033719c;
  assign the_8_th_line_of_the_picture_2 = 32'h67f36c30;
  assign the_9_th_line_of_the_picture = 32'h60337f1f;
  assign the_9_th_line_of_the_picture_2 = 32'hc7e37c30;
  assign the_10_th_line_of_the_picture = 32'h30b37e1f;
  assign the_10_th_line_of_the_picture_2 = 32'h87033c30;
  assign the_11_th_line_of_the_picture = 32'h31b37c1f;
  assign the_11_th_line_of_the_picture_2 = 32'h7033c30;
  assign the_12_th_line_of_the_picture = 32'h1b336e1b;
  assign the_12_th_line_of_the_picture_2 = 32'h87f31c30;
  assign the_13_th_line_of_the_picture = 32'h1f3f6e5b;
  assign the_13_th_line_of_the_picture_2 = 32'h17fb1c30;
  assign the_14_th_line_of_the_picture = 32'he3f6799;
  assign the_14_th_line_of_the_picture_2 = 32'he7fb8c30;
  assign the_15_th_line_of_the_picture = 32'he1e6318;
  assign the_15_th_line_of_the_picture_2 = 32'hc3f3cc30;
  assign the_16_th_line_of_the_picture = {32{1'b0}};
  assign the_16_th_line_of_the_picture_2 = {32{1'b0}};
  assign the_17_th_line_of_the_picture = {32{1'b0}};
  assign the_17_th_line_of_the_picture_2 = {32{1'b0}};
  assign the_18_th_line_of_the_picture = 32'hf81f007;
  assign the_18_th_line_of_the_picture_2 = 32'he01f81fc;
  assign the_19_th_line_of_the_picture = 32'h1fc1f01f;
  assign the_19_th_line_of_the_picture_2 = 32'hf83fe3fe;
  assign the_20_th_line_of_the_picture = 32'h3fe3f83f;
  assign the_20_th_line_of_the_picture_2 = 32'hfc3c77fe;
  assign the_21_st_line_of_the_picture = 32'h38e3b87c;
  assign the_21_st_line_of_the_picture_2 = 32'h3e3837fc;
  assign the_22_nd_line_of_the_picture = 32'h3c671cf8;
  assign the_22_nd_line_of_the_picture_2 = 32'h1f383780;
  assign the_23_rd_line_of_the_picture = 32'h1e270cf8;
  assign the_23_rd_line_of_the_picture_2 = 32'h1f383780;
  assign the_24_th_line_of_the_picture = 32'hf0e01f0;
  assign the_24_th_line_of_the_picture_2 = 32'hfbc67fc;
  assign the_25_th_line_of_the_picture = 32'h78e01f0;
  assign the_25_th_line_of_the_picture_2 = 32'hfbfc7f8;
  assign the_26_th_line_of_the_picture = 32'h43c70cf8;
  assign the_26_th_line_of_the_picture_2 = 32'h1f3f8780;
  assign the_27_th_line_of_the_picture = 32'h61e71cf8;
  assign the_27_th_line_of_the_picture_2 = 32'h1f3f0780;
  assign the_28_th_line_of_the_picture = 32'h70e3b87c;
  assign the_28_th_line_of_the_picture_2 = 32'h3e3b87fc;
  assign the_29_th_line_of_the_picture = 32'h79e3f83f;
  assign the_29_th_line_of_the_picture_2 = 32'hfc3b97fe;
  assign the_30_th_line_of_the_picture = 32'h3fe1f01f;
  assign the_30_th_line_of_the_picture_2 = 32'hf839e7fe;
  assign the_31_st_line_of_the_picture = 32'h1fc1f007;
  assign the_31_st_line_of_the_picture_2 = 32'he038c3fc;
endmodule

module \очки  (
  input  clock,
  input  game_over,
  input  rest,
  output [13:0] out_4
);

  wire and_1_out, comparator_1_eq;
  wire [4:0] counter_1_q;

  and and_1 (and_1_out, clock, ~game_over);  // AND_Gate
  Counter #(.width(5), .max('h9)) counter_1 (
    .Q(counter_1_q), .clk(and_1_out), .clr(rest));  // open: load, D, count, carry
  Comparator #(.width(5)) comparator_1 (.a(counter_1_q), .b(5'b01001), .eq(comparator_1_eq));  // open: gt, lt
  Counter #(.width(14), .max('h3fff)) counter_2 (
    .Q(out_4), .clk(comparator_1_eq), .clr(rest));  // open: load, D, count, carry
endmodule
