// Logisim project проект.circ as structural Verilog: 5 circuits, main circuit dino
module main (
  input  Game_Over
);

  wire and_1_out, and_2_out, clock_1_out, clock_2_out, comparator_1_eq, counter_2_carry, counter_3_carry,
       counter_4_carry, fall_1_st_j, jump_out, jump_up_1_fall;
  wire [3:0] count1, count2, count3, count4;
  wire [4:0] counter_1_q;
  wire [31:0] D1, D2, D3, D4, D5, D6, D7, D8, D9, f1, f2, f3, f4, f5, f6, f7, f8, fall_1_d1, fall_1_d2,
       fall_1_d3, fall_1_d4, fall_1_d5, fall_1_d6, fall_1_d7, fall_1_d8, fall_1_d9, fall_1_f1, fall_1_f2,
       fall_1_f3, fall_1_f4, fall_1_f5, fall_1_f6, fall_1_f7, fall_1_f8, jump_up_1_d1, jump_up_1_d2,
       jump_up_1_d3, jump_up_1_d4, jump_up_1_d5, jump_up_1_d6, jump_up_1_d7, jump_up_1_d8, jump_up_1_d9,
       jump_up_1_f1, jump_up_1_f2, jump_up_1_f3, jump_up_1_f4, jump_up_1_f5, jump_up_1_f6, jump_up_1_f7,
       jump_up_1_f8, v1, v2, v3, v4, v5, v6, v7, v8, v9, v10, v11, v12, v13, v14, v15, v16, v17, v18, v19,
       v20, v21, v22, v23, v24, v25, v26, v27, v28, v29, v30, v31, v32;

  Clock clock_1 (.out(clock_1_out));
  Hex_Digit_Display hex_digit_display_1 (.value(count1));  // open: dp
  Hex_Digit_Display hex_digit_display_2 (.value(count2));  // open: dp
  Counter #(.width(5), .max('h1f)) counter_1 (.Q(counter_1_q), .clk(clock_1_out));  // open: load, D, count, carry, clr
  dino dino_1 (
    .stop(Game_Over), .out_19(v1), .out_20(v2), .out_21(v3), .out_22(v4), .out_23(v5), .out_24(v6),
    .out_25(v7), .out_26(v8), .out_27(v9), .out_28(v10), .out_29(v11), .out_30(v12), .out_31(v13),
    .out_32(v14), .out_33(v15), .out_34(v16), .out_35(v17), .out_36(v18), .out_37(v19), .out_38(v20),
    .out_39(v21), .out_40(v22), .out_41(v23), .out_42(v24), .out_43(v25), .out_44(v26), .out_45(v27),
    .out_46(v28), .out_47(v29), .out_48(v30), .out_49(v31), .out_50(v32), .in_2(D1), .in_3(D2), .in_4(D3),
    .in_5(D4), .in_6(D5), .in_7(D6), .in_8(D7), .in_9(D8), .in_10(D9), .in_11(f1), .in_12(f2), .in_13(f3),
    .in_14(f4), .in_15(f5), .in_16(f6), .in_17(f7), .in_18(f8));
  Hex_Digit_Display hex_digit_display_3 (.value(count3));  // open: dp
  Comparator #(.width(5)) comparator_1 (.a(counter_1_q), .b({5{1'b1}}), .eq(comparator_1_eq));  // open: gt, lt
  Hex_Digit_Display hex_digit_display_4 (.value(count4));  // open: dp
  DotMatrix #(.inputtype("row"), .matrixcols(32), .matrixrows(32)) dotmatrix_1 (
    .row0(v32), .row1(v31), .row2(v30), .row3(v29), .row4(v28), .row5(v27), .row6(v26), .row7(v25),
    .row8(v24), .row9(v23), .row10(v22), .row11(v21), .row12(v20), .row13(v19), .row14(v18), .row15(v17),
    .row16(v16), .row17(v15), .row18(v14), .row19(v13), .row20(v12), .row21(v11), .row22(v10), .row23(v9),
    .row24(v8), .row25(v7), .row26(v6), .row27(v5), .row28(v4), .row29(v3), .row30(v2), .row31(v1));
  Counter #(.width(4), .max('h9)) counter_2 (
    .Q(count4), .carry(counter_2_carry), .clk(comparator_1_eq));  // open: load, D, count, clr
  Counter #(.width(4), .max('h9)) counter_3 (
    .count(counter_2_carry), .Q(count3), .carry(counter_3_carry), .clk(comparator_1_eq));  // open: load, D, clr
  Counter #(.width(4), .max('h9)) counter_4 (
    .count(and_1_out), .Q(count2), .carry(counter_4_carry), .clk(comparator_1_eq));  // open: load, D, clr
  and and_1 (and_1_out, counter_3_carry, counter_2_carry);
  Counter #(.width(4), .max('h9)) counter_5 (
    .count(and_2_out), .Q(count1), .clk(comparator_1_eq));  // open: load, D, carry, clr
  and and_2 (and_2_out, counter_4_carry, and_1_out);
  Button jump (.out(jump_out));
  Clock clock_2 (.out(clock_2_out));
  jump_up jump_up_1 (
    .clock(clock_2_out), .jump(jump_out), .clean(fall_1_st_j), .d1(jump_up_1_d1), .d2(jump_up_1_d2),
    .d3(jump_up_1_d3), .d4(jump_up_1_d4), .d5(jump_up_1_d5), .d6(jump_up_1_d6), .d7(jump_up_1_d7),
    .d8(jump_up_1_d8), .d9(jump_up_1_d9), .f1(jump_up_1_f1), .f2(jump_up_1_f2), .f3(jump_up_1_f3),
    .f4(jump_up_1_f4), .f5(jump_up_1_f5), .f6(jump_up_1_f6), .f7(jump_up_1_f7), .f8(jump_up_1_f8),
    .fall(jump_up_1_fall));
  Multiplexer #(.width(32)) multiplexer_1 (
    .in0(jump_up_1_f8), .in1(fall_1_d1), .out(f8), .sel(jump_up_1_fall));  // open: en
  Multiplexer #(.width(32)) multiplexer_2 (
    .in0(jump_up_1_f7), .in1(fall_1_d2), .out(f7), .sel(jump_up_1_fall));  // open: en
  fall fall_1 (
    .clock(clock_2_out), .fall(jump_up_1_fall), .clean(fall_1_st_j), .f8_in(jump_up_1_f8),
    .f7_in(jump_up_1_f7), .f6_in(jump_up_1_f6), .f5_in(jump_up_1_f5), .f4_in(jump_up_1_f4),
    .f3_in(jump_up_1_f3), .f2_in(jump_up_1_f2), .f1_in(jump_up_1_f1), .f0_in(jump_up_1_d9), .d1(fall_1_d1),
    .d2(fall_1_d2), .d3(fall_1_d3), .d4(fall_1_d4), .d5(fall_1_d5), .d6(fall_1_d6), .d7(fall_1_d7),
    .d8(fall_1_d8), .d9(fall_1_d9), .f1(fall_1_f1), .f2(fall_1_f2), .f3(fall_1_f3), .f4(fall_1_f4),
    .f5(fall_1_f5), .f6(fall_1_f6), .f7(fall_1_f7), .f8(fall_1_f8), .st_j(fall_1_st_j));
  Multiplexer #(.width(32)) multiplexer_3 (
    .in0(jump_up_1_f6), .in1(fall_1_d3), .out(f6), .sel(jump_up_1_fall));  // open: en
  Multiplexer #(.width(32)) multiplexer_4 (
    .in0(jump_up_1_f5), .in1(fall_1_d4), .out(f5), .sel(jump_up_1_fall));  // open: en
  Multiplexer #(.width(32)) multiplexer_5 (
    .in0(jump_up_1_f4), .in1(fall_1_d5), .out(f4), .sel(jump_up_1_fall));  // open: en
  Multiplexer #(.width(32)) multiplexer_6 (
    .in0(jump_up_1_f3), .in1(fall_1_d6), .out(f3), .sel(jump_up_1_fall));  // open: en
  Multiplexer #(.width(32)) multiplexer_7 (
    .in0(jump_up_1_f2), .in1(fall_1_d7), .out(f2), .sel(jump_up_1_fall));  // open: en
  Multiplexer #(.width(32)) multiplexer_8 (
    .in0(jump_up_1_f1), .in1(fall_1_d8), .out(f1), .sel(jump_up_1_fall));  // open: en
  Multiplexer #(.width(32)) multiplexer_9 (
    .in0(jump_up_1_d9), .in1(fall_1_d9), .out(D9), .sel(jump_up_1_fall));  // open: en
  Multiplexer #(.width(32)) multiplexer_10 (
    .in0(jump_up_1_d8), .in1(fall_1_f1), .out(D8), .sel(jump_up_1_fall));  // open: en
  Multiplexer #(.width(32)) multiplexer_11 (
    .in0(jump_up_1_d7), .in1(fall_1_f2), .out(D7), .sel(jump_up_1_fall));  // open: en
  Multiplexer #(.width(32)) multiplexer_12 (
    .in0(jump_up_1_d5), .in1(fall_1_f4), .out(D5), .sel(jump_up_1_fall));  // open: en
  Multiplexer #(.width(32)) multiplexer_13 (
    .in0(jump_up_1_d6), .in1(fall_1_f3), .out(D6), .sel(jump_up_1_fall));  // open: en
  Multiplexer #(.width(32)) multiplexer_14 (
    .in0(jump_up_1_d4), .in1(fall_1_f5), .out(D4), .sel(jump_up_1_fall));  // open: en
  Multiplexer #(.width(32)) multiplexer_15 (
    .in0(jump_up_1_d3), .in1(fall_1_f6), .out(D3), .sel(jump_up_1_fall));  // open: en
  Multiplexer #(.width(32)) multiplexer_16 (
    .in0(jump_up_1_d2), .in1(fall_1_f7), .out(D2), .sel(jump_up_1_fall));  // open: en
  Multiplexer #(.width(32)) multiplexer_17 (
    .in0(jump_up_1_d1), .in1(fall_1_f8), .out(D1), .sel(jump_up_1_fall));  // open: en
endmodule

// Display
module dino (
  input  stop,
  input  [31:0] in_2,
  input  [31:0] in_3,
  input  [31:0] in_4,
  input  [31:0] in_5,
  input  [31:0] in_6,
  input  [31:0] in_7,
  input  [31:0] in_8,
  input  [31:0] in_9,
  input  [31:0] in_10,
  input  [31:0] in_11,
  input  [31:0] in_12,
  input  [31:0] in_13,
  input  [31:0] in_14,
  input  [31:0] in_15,
  input  [31:0] in_16,
  input  [31:0] in_17,
  input  [31:0] in_18,
  output [31:0] out_19,
  output [31:0] out_20,
  output [31:0] out_21,
  output [31:0] out_22,
  output [31:0] out_23,
  output [31:0] out_24,
  output [31:0] out_25,
  output [31:0] out_26,
  output [31:0] out_27,
  output [31:0] out_28,
  output [31:0] out_29,
  output [31:0] out_30,
  output [31:0] out_31,
  output [31:0] out_32,
  output [31:0] out_33,
  output [31:0] out_34,
  output [31:0] out_35,
  output [31:0] out_36,
  output [31:0] out_37,
  output [31:0] out_38,
  output [31:0] out_39,
  output [31:0] out_40,
  output [31:0] out_41,
  output [31:0] out_42,
  output [31:0] out_43,
  output [31:0] out_44,
  output [31:0] out_45,
  output [31:0] out_46,
  output [31:0] out_47,
  output [31:0] out_48,
  output [31:0] out_49,
  output [31:0] out_50
);

  Multiplexer #(.width(32)) multiplexer_1 (.in0(in_3), .in1({32{1'b0}}), .out(out_20), .sel(stop));  // open: en
  Multiplexer #(.width(32)) multiplexer_2 (.in0(in_2), .in1({32{1'b0}}), .out(out_19), .sel(stop));  // open: en
  Multiplexer #(.width(32)) multiplexer_3 (.in0(in_4), .in1({32{1'b0}}), .out(out_21), .sel(stop));  // open: en
  Multiplexer #(.width(32)) multiplexer_4 (.in0(in_5), .in1({32{1'b0}}), .out(out_22), .sel(stop));  // open: en
  Multiplexer #(.width(32)) multiplexer_5 (.in0(in_7), .in1({32{1'b0}}), .out(out_24), .sel(stop));  // open: en
  Multiplexer #(.width(32)) multiplexer_6 (.in0(in_6), .in1({32{1'b0}}), .out(out_23), .sel(stop));  // open: en
  Multiplexer #(.width(32)) multiplexer_7 (.in0(in_8), .in1({32{1'b0}}), .out(out_25), .sel(stop));  // open: en
  Multiplexer #(.width(32)) multiplexer_8 (.in0(in_9), .in1({32{1'b0}}), .out(out_26), .sel(stop));  // open: en
  Multiplexer #(.width(32)) multiplexer_9 (.in0(in_11), .in1({32{1'b0}}), .out(out_28), .sel(stop));  // open: en
  Multiplexer #(.width(32)) multiplexer_10 (.in0(in_10), .in1({32{1'b0}}), .out(out_27), .sel(stop));  // open: en
  Multiplexer #(.width(32)) multiplexer_11 (.in0(in_13), .in1({32{1'b0}}), .out(out_30), .sel(stop));  // open: en
  Multiplexer #(.width(32)) multiplexer_12 (.in0(in_12), .in1({32{1'b0}}), .out(out_29), .sel(stop));  // open: en
  Multiplexer #(.width(32)) multiplexer_13 (.in0(in_14), .in1({32{1'b0}}), .out(out_31), .sel(stop));  // open: en
  Multiplexer #(.width(32)) multiplexer_14 (.in0(in_15), .in1({32{1'b0}}), .out(out_32), .sel(stop));  // open: en
  Multiplexer #(.width(32)) multiplexer_15 (.in0(in_16), .in1({32{1'b0}}), .out(out_33), .sel(stop));  // open: en
  Multiplexer #(.width(32)) multiplexer_16 (.in0(in_17), .in1({32{1'b0}}), .out(out_34), .sel(stop));  // open: en
  Multiplexer #(.width(32)) multiplexer_17 (.in0({32{1'b0}}), .in1({32{1'b0}}), .out(out_36), .sel(stop));  // open: en
  Multiplexer #(.width(32)) multiplexer_18 (.in0(in_18), .in1({32{1'b0}}), .out(out_35), .sel(stop));  // open: en
  Multiplexer #(.width(32)) multiplexer_19 (.in0({32{1'b0}}), .in1({32{1'b0}}), .out(out_37), .sel(stop));  // open: en
  Multiplexer #(.width(32)) multiplexer_20 (.in0({32{1'b0}}), .in1({32{1'b0}}), .out(out_38), .sel(stop));  // open: en
  Multiplexer #(.width(32)) multiplexer_21 (.in0({32{1'b0}}), .in1({32{1'b0}}), .out(out_39), .sel(stop));  // open: en
  Multiplexer #(.width(32)) multiplexer_22 (.in0({32{1'b0}}), .in1({32{1'b0}}), .out(out_40), .sel(stop));  // open: en
  Multiplexer #(.width(32)) multiplexer_23 (.in0({32{1'b0}}), .in1({32{1'b0}}), .out(out_41), .sel(stop));  // open: en
  Multiplexer #(.width(32)) multiplexer_24 (.in0({32{1'b0}}), .in1({32{1'b0}}), .out(out_42), .sel(stop));  // open: en
  Multiplexer #(.width(32)) multiplexer_25 (.in0({32{1'b0}}), .in1({32{1'b0}}), .out(out_44), .sel(stop));  // open: en
  Multiplexer #(.width(32)) multiplexer_26 (.in0({32{1'b0}}), .in1({32{1'b0}}), .out(out_43), .sel(stop));  // open: en
  Multiplexer #(.width(32)) multiplexer_27 (.in0({32{1'b0}}), .in1({32{1'b0}}), .out(out_46), .sel(stop));  // open: en
  Multiplexer #(.width(32)) multiplexer_28 (.in0({32{1'b0}}), .in1({32{1'b0}}), .out(out_45), .sel(stop));  // open: en
  Multiplexer #(.width(32)) multiplexer_29 (.in0({32{1'b0}}), .in1({32{1'b0}}), .out(out_48), .sel(stop));  // open: en
  Multiplexer #(.width(32)) multiplexer_30 (.in0({32{1'b0}}), .in1({32{1'b0}}), .out(out_47), .sel(stop));  // open: en
  Multiplexer #(.width(32)) multiplexer_31 (.in0({32{1'b0}}), .in1({32{1'b0}}), .out(out_50), .sel(stop));  // open: en
  Multiplexer #(.width(32)) multiplexer_32 (.in0({32{1'b0}}), .in1({32{1'b0}}), .out(out_49), .sel(stop));  // open: en

  // Other names for the same wires on the sheet: D1[31:0] = in_2; D2[31:0] = in_3; D3[31:0] = in_4; D4[31:0] = in_5;
  //   D5[31:0] = in_6; D6[31:0] = in_7; D7[31:0] = in_8; D8[31:0] = in_9; D9[31:0] = in_10; f1[31:0] = in_11;
  //   f2[31:0] = in_12; f3[31:0] = in_13; f4[31:0] = in_14; f5[31:0] = in_15; f6[31:0] = in_16; f7[31:0] = in_17;
  //   f8[31:0] = in_18
endmodule

module dinovis (
);

  DotMatrix #(.inputtype("row"), .matrixcols(32), .matrixrows(20)) dotmatrix_1 (
    .row11(32'h3c00000), .row12(32'h3000000), .row13(32'h3c00000), .row14(32'h47000000),
    .row15(32'h2fc00000), .row16(32'h1f400000), .row17(32'hf000000), .row18(32'h9000000), .row19(32'hd800000));  // open: row0, row1, row2, row3, row4, row5, row6, row7, row8, row9, row10
endmodule

module jump_up (
  input  clock,
  input  jump,
  input  clean,
  output [31:0] d1,
  output [31:0] d2,
  output [31:0] d3,
  output [31:0] d4,
  output [31:0] d5,
  output [31:0] d6,
  output [31:0] d7,
  output [31:0] d8,
  output [31:0] d9,
  output [31:0] f1,
  output [31:0] f2,
  output [31:0] f3,
  output [31:0] f4,
  output [31:0] f5,
  output [31:0] f6,
  output [31:0] f7,
  output [31:0] f8,
  output fall
);

  wire and_1_out, and_2_out, and_3_out, clock_1_out, comparator_1_eq, comparator_1_gt, comparator_2_eq,
       comparator_3_eq, multiplexer_1_out, not_1_out, not_2_out;
  wire [7:0] counter_2_q;
  wire [31:0] counter_1_q, multiplexer_2_out, multiplexer_3_out, multiplexer_4_out, multiplexer_5_out,
       multiplexer_6_out, multiplexer_7_out, multiplexer_8_out, multiplexer_9_out, multiplexer_10_out;

  Clock clock_1 (.out(clock_1_out));
  and and_1 (and_1_out, jump, and_2_out);
  not not_1 (not_1_out, jump);
  Multiplexer multiplexer_1 (
    .in0(comparator_2_eq), .in1(comparator_3_eq), .out(multiplexer_1_out), .sel(fall));  // open: en
  and and_2 (and_2_out, comparator_2_eq, multiplexer_1_out);
  Counter #(.width(32), .max('hffffffff), .trigger("falling")) counter_1 (
    .Q(counter_1_q), .clk(and_1_out), .clr(and_3_out));  // open: load, D, count, carry
  and and_3 (and_3_out, clean, not_1_out);
  Counter #(.trigger("falling")) counter_2 (
    .Q(counter_2_q), .clk(clock_1_out), .clr(comparator_2_eq));  // open: load, D, count, carry
  Comparator #(.width(32)) comparator_1 (
    .a(counter_1_q), .b({32{1'b0}}), .gt(comparator_1_gt), .eq(comparator_1_eq));  // open: lt
  Comparator comparator_2 (.a(counter_2_q), .b(8'h20), .eq(comparator_2_eq));  // open: gt, lt
  Register #(.width(32)) register_1 (.D(multiplexer_2_out), .en(and_2_out), .Q(d1), .clk(and_2_out));  // open: clr
  Multiplexer #(.width(32)) multiplexer_2 (
    .in0({32{1'b0}}), .in1(32'hd800000), .out(multiplexer_2_out), .sel(comparator_1_eq));  // open: en
  Multiplexer #(.width(32)) multiplexer_3 (
    .in0(d1), .in1(32'h9000000), .out(multiplexer_3_out), .sel(comparator_1_eq));  // open: en
  not not_2 (not_2_out, comparator_1_gt);
  Register #(.width(32)) register_2 (.D(multiplexer_3_out), .en(and_2_out), .Q(d2), .clk(and_2_out));  // open: clr
  Multiplexer #(.width(32)) multiplexer_4 (
    .in0(d2), .in1(32'hf000000), .out(multiplexer_4_out), .sel(comparator_1_eq));  // open: en
  Register #(.width(32)) register_3 (.D(multiplexer_4_out), .en(and_2_out), .Q(d3), .clk(and_2_out));  // open: clr
  Register #(.width(32)) register_4 (.D(multiplexer_5_out), .en(and_2_out), .Q(d4), .clk(and_2_out));  // open: clr
  Multiplexer #(.width(32)) multiplexer_5 (
    .in0(d3), .in1(32'h1f400000), .out(multiplexer_5_out), .sel(comparator_1_eq));  // open: en
  Register #(.width(32)) register_5 (.D(multiplexer_7_out), .en(and_2_out), .Q(d6), .clk(and_2_out));  // open: clr
  Register #(.width(32)) register_6 (.D(multiplexer_6_out), .en(and_2_out), .Q(d5), .clk(and_2_out));  // open: clr
  Multiplexer #(.width(32)) multiplexer_6 (
    .in0(d4), .in1(32'h2fc00000), .out(multiplexer_6_out), .sel(comparator_1_eq));  // open: en
  Multiplexer #(.width(32)) multiplexer_7 (
    .in0(d5), .in1(32'h47000000), .out(multiplexer_7_out), .sel(comparator_1_eq));  // open: en
  Register #(.width(32)) register_7 (.D(multiplexer_8_out), .en(and_2_out), .Q(d7), .clk(and_2_out));  // open: clr
  Multiplexer #(.width(32)) multiplexer_8 (
    .in0(d6), .in1(32'h3c00000), .out(multiplexer_8_out), .sel(comparator_1_eq));  // open: en
  Register #(.width(32)) register_8 (.D(multiplexer_9_out), .en(and_2_out), .Q(d8), .clk(and_2_out));  // open: clr
  Register #(.width(32)) register_9 (.D(multiplexer_10_out), .en(and_2_out), .Q(d9), .clk(and_2_out));  // open: clr
  Multiplexer #(.width(32)) multiplexer_9 (
    .in0(d7), .in1(32'h3000000), .out(multiplexer_9_out), .sel(comparator_1_eq));  // open: en
  Register #(.width(32)) register_10 (.D(d9), .en(and_2_out), .Q(f1), .clk(and_2_out), .clr(not_2_out));
  Multiplexer #(.width(32)) multiplexer_10 (
    .in0(d8), .in1(32'h3c00000), .out(multiplexer_10_out), .sel(comparator_1_eq));  // open: en
  Register #(.width(32)) register_11 (.D(f2), .en(and_2_out), .Q(f3), .clk(and_2_out), .clr(not_2_out));
  Register #(.width(32)) register_12 (.D(f1), .en(and_2_out), .Q(f2), .clk(and_2_out), .clr(not_2_out));
  Register #(.width(32)) register_13 (.D(f4), .en(and_2_out), .Q(f5), .clk(and_2_out), .clr(not_2_out));
  Register #(.width(32)) register_14 (.D(f3), .en(and_2_out), .Q(f4), .clk(and_2_out), .clr(not_2_out));
  Register #(.width(32)) register_15 (.D(f5), .en(and_2_out), .Q(f6), .clk(and_2_out), .clr(not_2_out));
  Comparator #(.width(32)) comparator_3 (.a(f8), .b({32{1'b0}}), .eq(comparator_3_eq));  // open: gt, lt
  not not_3 (fall, comparator_3_eq);
  Register #(.width(32)) register_16 (.D(f7), .en(and_2_out), .Q(f8), .clk(and_2_out), .clr(not_2_out));
  Register #(.width(32)) register_17 (.D(f6), .en(and_2_out), .Q(f7), .clk(and_2_out), .clr(not_2_out));
  Register #(.width(32)) register_18 (.D(f8), .en(and_2_out), .clk(and_2_out), .clr(not_2_out));  // open: Q
endmodule

module fall (
  input  clock,
  input  fall,
  input  clean,
  input  [31:0] f8_in,
  input  [31:0] f7_in,
  input  [31:0] f6_in,
  input  [31:0] f5_in,
  input  [31:0] f4_in,
  input  [31:0] f3_in,
  input  [31:0] f2_in,
  input  [31:0] f1_in,
  input  [31:0] f0_in,
  output [31:0] d1,
  output [31:0] d2,
  output [31:0] d3,
  output [31:0] d4,
  output [31:0] d5,
  output [31:0] d6,
  output [31:0] d7,
  output [31:0] d8,
  output [31:0] d9,
  output [31:0] f1,
  output [31:0] f2,
  output [31:0] f3,
  output [31:0] f4,
  output [31:0] f5,
  output [31:0] f6,
  output [31:0] f7,
  output [31:0] f8,
  output st_j
);

  wire and_1_out, and_2_out, and_3_out, clock_1_out, comparator_1_eq, comparator_1_gt, comparator_2_eq,
       comparator_3_eq, multiplexer_1_out, not_1_out, not_2_out;
  wire [7:0] counter_2_q;
  wire [31:0] counter_1_q, multiplexer_2_out, multiplexer_3_out, multiplexer_4_out, multiplexer_5_out,
       multiplexer_6_out, multiplexer_7_out, multiplexer_8_out, multiplexer_9_out, multiplexer_10_out;

  Clock clock_1 (.out(clock_1_out));
  and and_1 (and_1_out, fall, and_2_out);
  not not_1 (not_1_out, fall);
  Multiplexer multiplexer_1 (
    .in0(comparator_2_eq), .in1(comparator_3_eq), .out(multiplexer_1_out), .sel(st_j));  // open: en
  and and_2 (and_2_out, comparator_2_eq, multiplexer_1_out);
  Counter #(.width(32), .max('hffffffff), .trigger("falling")) counter_1 (
    .Q(counter_1_q), .clk(and_1_out), .clr(and_3_out));  // open: load, D, count, carry
  and and_3 (and_3_out, not_1_out, clean);
  Counter #(.trigger("falling")) counter_2 (
    .Q(counter_2_q), .clk(clock_1_out), .clr(comparator_2_eq));  // open: load, D, count, carry
  Comparator #(.width(32)) comparator_1 (
    .a(counter_1_q), .b({32{1'b0}}), .gt(comparator_1_gt), .eq(comparator_1_eq));  // open: lt
  Comparator comparator_2 (.a(counter_2_q), .b(8'h20), .eq(comparator_2_eq));  // open: gt, lt
  Register #(.width(32)) register_1 (.D(multiplexer_2_out), .en(and_2_out), .Q(d1), .clk(and_2_out));  // open: clr
  Multiplexer #(.width(32)) multiplexer_2 (
    .in0({32{1'b0}}), .in1(f8_in), .out(multiplexer_2_out), .sel(comparator_1_eq));  // open: en
  Multiplexer #(.width(32)) multiplexer_3 (
    .in0(d1), .in1(f7_in), .out(multiplexer_3_out), .sel(comparator_1_eq));  // open: en
  not not_2 (not_2_out, comparator_1_gt);
  Register #(.width(32)) register_2 (.D(multiplexer_3_out), .en(and_2_out), .Q(d2), .clk(and_2_out));  // open: clr
  Multiplexer #(.width(32)) multiplexer_4 (
    .in0(d2), .in1(f6_in), .out(multiplexer_4_out), .sel(comparator_1_eq));  // open: en
  Register #(.width(32)) register_3 (.D(multiplexer_4_out), .en(and_2_out), .Q(d3), .clk(and_2_out));  // open: clr
  Register #(.width(32)) register_4 (.D(multiplexer_5_out), .en(and_2_out), .Q(d4), .clk(and_2_out));  // open: clr
  Multiplexer #(.width(32)) multiplexer_5 (
    .in0(d3), .in1(f5_in), .out(multiplexer_5_out), .sel(comparator_1_eq));  // open: en
  Register #(.width(32)) register_5 (.D(multiplexer_6_out), .en(and_2_out), .Q(d5), .clk(and_2_out));  // open: clr
  Register #(.width(32)) register_6 (.D(multiplexer_7_out), .en(and_2_out), .Q(d6), .clk(and_2_out));  // open: clr
  Multiplexer #(.width(32)) multiplexer_6 (
    .in0(d4), .in1(f4_in), .out(multiplexer_6_out), .sel(comparator_1_eq));  // open: en
  Multiplexer #(.width(32)) multiplexer_7 (
    .in0(d5), .in1(f3_in), .out(multiplexer_7_out), .sel(comparator_1_eq));  // open: en
  Register #(.width(32)) register_7 (.D(multiplexer_8_out), .en(and_2_out), .Q(d7), .clk(and_2_out));  // open: clr
  Multiplexer #(.width(32)) multiplexer_8 (
    .in0(d6), .in1(f2_in), .out(multiplexer_8_out), .sel(comparator_1_eq));  // open: en
  Register #(.width(32)) register_8 (.D(multiplexer_9_out), .en(and_2_out), .Q(d8), .clk(and_2_out));  // open: clr
  Register #(.width(32)) register_9 (.D(multiplexer_10_out), .en(and_2_out), .Q(d9), .clk(and_2_out));  // open: clr
  Multiplexer #(.width(32)) multiplexer_9 (
    .in0(d7), .in1(f1_in), .out(multiplexer_9_out), .sel(comparator_1_eq));  // open: en
  Register #(.width(32)) register_10 (.D(d9), .en(and_2_out), .Q(f1), .clk(and_2_out), .clr(not_2_out));
  Multiplexer #(.width(32)) multiplexer_10 (
    .in0(d8), .in1(f0_in), .out(multiplexer_10_out), .sel(comparator_1_eq));  // open: en
  Register #(.width(32)) register_11 (.D(f1), .en(and_2_out), .Q(f2), .clk(and_2_out), .clr(not_2_out));
  Register #(.width(32)) register_12 (.D(f2), .en(and_2_out), .Q(f3), .clk(and_2_out), .clr(not_2_out));
  Register #(.width(32)) register_13 (.D(f3), .en(and_2_out), .Q(f4), .clk(and_2_out), .clr(not_2_out));
  Register #(.width(32)) register_14 (.D(f4), .en(and_2_out), .Q(f5), .clk(and_2_out), .clr(not_2_out));
  Register #(.width(32)) register_15 (.D(f5), .en(and_2_out), .Q(f6), .clk(and_2_out), .clr(not_2_out));
  not not_3 (st_j, comparator_3_eq);
  Comparator #(.width(32)) comparator_3 (.a(f8), .b({32{1'b0}}), .eq(comparator_3_eq));  // open: gt, lt
  Register #(.width(32)) register_16 (.D(f7), .en(and_2_out), .Q(f8), .clk(and_2_out), .clr(not_2_out));
  Register #(.width(32)) register_17 (.D(f6), .en(and_2_out), .Q(f7), .clk(and_2_out), .clr(not_2_out));
  Register #(.width(32)) register_18 (.D(f8), .en(and_2_out), .clk(and_2_out), .clr(not_2_out));  // open: Q
endmodule
